// Logisim project 5bit_IO.circ as structural Verilog: 1 circuit, main circuit main
module main (
  input  in_1,
  input  External_Input,
  input  in_3,
  input  in_4,
  input  in_5,
  input  in_6,
  input  in_7,
  input  in_8,
  input  in_9,
  input  in_10,
  output out_11,
  output out_12,
  output out_13,
  output out_14,
  output out_15,
  output out_16
);

  wire and_1_out, nand_1_out, nand_2_out, nor_1_out, nor_2_out, nor_3_out, nor_4_out, nor_5_out, nor_6_out,
       nor_7_out, nor_8_out, nor_9_out, nor_10_out, nor_11_out, nor_12_out, nor_13_out, nor_14_out,
       nor_15_out, nor_16_out, nor_17_out, nor_18_out, nor_19_out, nor_20_out, nor_21_out, nor_22_out,
       nor_23_out, nor_24_out, nor_25_out, nor_26_out, nor_27_out, nor_28_out, nor_29_out, nor_30_out,
       nor_31_out, nor_32_out, nor_33_out, nor_34_out, nor_35_out, nor_36_out, nor_37_out, nor_38_out,
       nor_40_out, nor_42_out, nor_44_out, nor_46_out, nor_48_out, not_1_out, not_2_out, not_3_out,
       not_4_out, not_5_out, not_6_out, not_7_out, not_8_out, not_9_out, not_10_out, not_11_out, not_12_out,
       not_13_out;

  not not_1 (not_1_out, in_6);
  not not_2 (not_2_out, in_7);
  not not_3 (not_3_out, in_8);
  not not_4 (not_4_out, in_10);
  not not_5 (not_5_out, in_9);
  nor nor_1 (nor_1_out, in_8, not_2_out, not_1_out);
  nor nor_2 (nor_2_out, not_3_out, not_2_out, not_1_out);
  nor nor_3 (nor_3_out, not_4_out, not_5_out);
  not not_6 (not_6_out, in_1);
  not not_7 (not_7_out, External_Input);
  nand nand_1 (nand_1_out, not_5_out, nor_1_out);
  nand nand_2 (nand_2_out, nor_1_out, nor_3_out);
  not not_8 (not_8_out, in_5);
  not not_9 (not_9_out, in_4);
  not not_10 (not_10_out, in_3);
  nor nor_4 (nor_4_out, not_8_out, nand_1_out);
  nor nor_5 (nor_5_out, not_9_out, nand_1_out);
  nor nor_6 (nor_6_out, not_10_out, nand_1_out);
  nor nor_7 (nor_7_out, not_7_out, nand_1_out);
  nor nor_8 (nor_8_out, not_6_out, nand_1_out);
  not not_11 (not_11_out, nand_2_out);
  nor nor_9 (nor_9_out, nor_4_out, nand_2_out);
  nor nor_10 (nor_10_out, nor_9_out, nand_2_out);
  nor nor_11 (nor_11_out, nor_5_out, nand_2_out);
  nor nor_12 (nor_12_out, nor_11_out, nand_2_out);
  nor nor_13 (nor_13_out, nor_6_out, nand_2_out);
  nor nor_14 (nor_14_out, nor_13_out, nand_2_out);
  nor nor_15 (nor_15_out, nor_7_out, nand_2_out);
  nor nor_16 (nor_16_out, nor_15_out, nand_2_out);
  nor nor_17 (nor_17_out, nor_8_out, nand_2_out);
  nor nor_18 (nor_18_out, nor_17_out, nand_2_out);
  nor nor_19 (nor_19_out, nor_9_out, nor_20_out);
  nor nor_20 (nor_20_out, nor_19_out, nor_10_out);
  nor nor_21 (nor_21_out, nor_11_out, nor_22_out);
  nor nor_22 (nor_22_out, nor_21_out, nor_12_out);
  nor nor_23 (nor_23_out, nor_13_out, nor_24_out);
  nor nor_24 (nor_24_out, nor_23_out, nor_14_out);
  nor nor_25 (nor_25_out, nor_15_out, nor_26_out);
  nor nor_26 (nor_26_out, nor_25_out, nor_16_out);
  nor nor_27 (nor_27_out, nor_17_out, nor_28_out);
  nor nor_28 (nor_28_out, nor_27_out, nor_18_out);
  nor nor_29 (nor_29_out, nor_19_out, not_11_out);
  nor nor_30 (nor_30_out, nor_29_out, not_11_out);
  nor nor_31 (nor_31_out, nor_21_out, not_11_out);
  nor nor_32 (nor_32_out, nor_31_out, not_11_out);
  nor nor_33 (nor_33_out, nor_23_out, not_11_out);
  nor nor_34 (nor_34_out, nor_33_out, not_11_out);
  nor nor_35 (nor_35_out, nor_25_out, not_11_out);
  nor nor_36 (nor_36_out, nor_35_out, not_11_out);
  nor nor_37 (nor_37_out, nor_27_out, not_11_out);
  nor nor_38 (nor_38_out, nor_37_out, not_11_out);
  and and_1 (and_1_out, nor_3_out, nor_2_out);
  nor nor_39 (out_11, nor_29_out, nor_40_out);
  nor nor_40 (nor_40_out, out_11, nor_30_out);
  nor nor_41 (out_12, nor_31_out, nor_42_out);
  nor nor_42 (nor_42_out, out_12, nor_32_out);
  nor nor_43 (out_13, nor_33_out, nor_44_out);
  nor nor_44 (nor_44_out, out_13, nor_34_out);
  nor nor_45 (out_14, nor_35_out, nor_46_out);
  nor nor_46 (nor_46_out, out_14, nor_36_out);
  nor nor_47 (out_15, nor_37_out, nor_48_out);
  nor nor_48 (nor_48_out, out_15, nor_38_out);
  buf buffer_1 (out_16, not_12_out);
  not not_12 (not_12_out, not_13_out);
  not not_13 (not_13_out, and_1_out);

  // Notes on the sheet:
  //   External Control
  //   48 NOR, 3 NAND, 7 INV / 29 6J6 Dual Triodes
  //   Addressing / OpCode Inverters not counted
endmodule
