// Logisim project Tape_Clock_v1.circ as structural Verilog: 1 circuit, main circuit main
module main (
  input  RESET,
  input  DATA,
  input  INITIAL,
  input  WRT,
  input  PTO_7,
  input  PTO_6,
  input  PTO_5,
  input  PTO_4,
  input  PTO_3,
  input  PTO_2,
  input  PTO_1,
  input  PTO_0,
  output TAPE,
  output nRD,
  output MCLK,
  output nWT,
  output WRT_L,
  output DATA_2
);

  wire and_1_out, and_2_out, and_3_out, and_4_out, and_5_out, and_6_out, and_7_out, and_8_out, and_9_out,
       and_10_out, and_11_out, and_12_out, and_13_out, and_14_out, and_15_out, and_16_out, and_17_out,
       and_18_out, and_19_out, and_20_out, buffer_1_out, buffer_2_out, buffer_3_out, buffer_4_out,
       buffer_5_out, buffer_6_out, buffer_7_out, buffer_8_out, buffer_9_out, buffer_10_out, buffer_11_out,
       buffer_12_out, buffer_13_out, buffer_14_out, buffer_15_out, buffer_16_out, clock_1_out, nor_1_out,
       nor_2_out, nor_3_out, nor_5_out, nor_6_out, nor_8_out, nor_9_out, nor_10_out, nor_12_out, nor_13_out,
       nor_16_out, nor_17_out, nor_18_out, nor_19_out, nor_20_out, not_1_out, not_2_out, not_3_out,
       not_4_out, not_5_out, not_6_out, not_7_out, not_8_out, not_9_out, not_10_out, or_1_out, or_2_out,
       or_3_out, or_4_out, or_5_out, or_6_out, or_7_out, or_8_out, or_9_out, or_10_out;

  Clock clock_1 (.out(clock_1_out));
  not not_1 (not_1_out, clock_1_out);
  and and_1 (and_1_out, nor_19_out, clock_1_out);
  or or_1 (or_1_out, RESET, and_2_out);
  and and_2 (and_2_out, nor_20_out, clock_1_out);
  buf buffer_1 (buffer_1_out, not_2_out);
  buf buffer_2 (buffer_2_out, PTO_7);
  not not_2 (not_2_out, PTO_7);
  nor nor_1 (nor_1_out, and_1_out, nor_2_out);
  nor nor_2 (nor_2_out, nor_1_out, or_1_out);
  buf buffer_3 (buffer_3_out, not_3_out);
  buf buffer_4 (buffer_4_out, PTO_6);
  not not_3 (not_3_out, PTO_6);
  or or_2 (or_2_out, RESET, and_3_out);
  and and_3 (and_3_out, nor_1_out, not_1_out);
  and and_4 (and_4_out, nor_2_out, not_1_out);
  buf buffer_5 (buffer_5_out, not_4_out);
  buf buffer_6 (buffer_6_out, not_5_out);
  buf buffer_7 (buffer_7_out, PTO_4);
  buf buffer_8 (buffer_8_out, PTO_5);
  not not_4 (not_4_out, PTO_4);
  not not_5 (not_5_out, PTO_5);
  nor nor_3 (nor_3_out, or_2_out, TAPE);
  nor nor_4 (TAPE, nor_3_out, and_4_out);
  buf buffer_9 (buffer_9_out, not_6_out);
  buf buffer_10 (buffer_10_out, PTO_2);
  buf buffer_11 (buffer_11_out, PTO_3);
  not not_6 (not_6_out, PTO_3);
  or or_3 (or_3_out, RESET, and_5_out);
  and and_5 (and_5_out, nor_3_out, clock_1_out);
  and and_6 (and_6_out, TAPE, clock_1_out);
  buf buffer_12 (buffer_12_out, not_7_out);
  buf buffer_13 (buffer_13_out, not_8_out);
  buf buffer_14 (buffer_14_out, PTO_1);
  not not_7 (not_7_out, PTO_1);
  not not_8 (not_8_out, PTO_2);
  nor nor_5 (nor_5_out, or_3_out, nor_6_out);
  nor nor_6 (nor_6_out, nor_5_out, and_6_out);
  buf buffer_15 (buffer_15_out, not_9_out);
  buf buffer_16 (buffer_16_out, PTO_0);
  not not_9 (not_9_out, PTO_0);
  and and_7 (and_7_out, nor_5_out, not_1_out);
  and and_8 (and_8_out, nor_6_out, not_1_out);
  or or_4 (or_4_out, RESET, and_8_out);
  nor nor_7 (nRD, and_7_out, nor_8_out);
  nor nor_8 (nor_8_out, nRD, or_4_out);
  or or_5 (or_5_out, RESET, and_9_out);
  and and_9 (and_9_out, nRD, clock_1_out);
  and and_10 (and_10_out, nor_8_out, clock_1_out);
  nor nor_9 (nor_9_out, or_5_out, nor_10_out);
  nor nor_10 (nor_10_out, nor_9_out, and_10_out);
  or or_6 (or_6_out, RESET, and_11_out);
  and and_11 (and_11_out, nor_19_out, TAPE);
  and and_12 (and_12_out, MCLK, WRT);
  and and_13 (and_13_out, nor_9_out, not_1_out);
  and and_14 (and_14_out, nor_10_out, not_1_out);
  or or_7 (or_7_out, RESET, and_14_out);
  nor nor_11 (WRT_L, or_6_out, nor_12_out);
  nor nor_12 (nor_12_out, WRT_L, and_12_out);
  nor nor_13 (nor_13_out, and_13_out, MCLK);
  nor nor_14 (MCLK, nor_13_out, or_7_out);
  nor nor_15 (DATA_2, TAPE, nor_16_out);
  nor nor_16 (nor_16_out, DATA_2, INITIAL);
  or or_8 (or_8_out, RESET, and_15_out);
  and and_15 (and_15_out, nor_13_out, clock_1_out);
  and and_16 (and_16_out, MCLK, clock_1_out);
  nor nor_17 (nor_17_out, or_8_out, nor_18_out);
  nor nor_18 (nor_18_out, nor_17_out, and_16_out);
  and and_17 (and_17_out, DATA_2, not_10_out);
  not not_10 (not_10_out, WRT_L);
  and and_18 (and_18_out, WRT_L, DATA);
  and and_19 (and_19_out, nor_17_out, not_1_out);
  and and_20 (and_20_out, nor_18_out, not_1_out);
  or or_9 (or_9_out, RESET, and_20_out);
  nand nand_1 (nWT, nor_20_out, or_10_out);
  or or_10 (or_10_out, and_17_out, and_18_out);
  nor nor_19 (nor_19_out, and_19_out, nor_20_out);
  nor nor_20 (nor_20_out, nor_19_out, or_9_out);
endmodule
