// Logisim project CoreMemory.circ as structural Verilog: 1 circuit, main circuit main
module main (
  input  A1,
  input  A0,
  input  SENSE,
  input  in_4,
  output RD,
  output WT
);

  wire and_1_out, and_2_out, and_3_out, and_4_out, and_5_out, and_6_out, and_7_out, and_8_out, and_9_out,
       clock_1_out, d_ff_1_qn, d_ff_2_q, d_ff_2_qn, d_ff_3_q, d_ff_3_qn, nor_1_out, nor_2_out, nor_3_out,
       nor_4_out, nor_5_out, nor_6_out, nor_7_out, nor_8_out, nor_9_out, nor_10_out, nor_11_out, nor_12_out,
       not_1_out, not_2_out, not_3_out, not_4_out, not_5_out, not_6_out;

  Clock clock_1 (.out(clock_1_out));
  not not_1 (not_1_out, A0);
  not not_2 (not_2_out, A1);
  and and_1 (and_1_out, in_4, d_ff_3_qn, d_ff_2_qn, d_ff_1_qn);
  nor nor_1 (nor_1_out, A0, A1);
  nor nor_2 (nor_2_out, not_1_out, A1);
  nor nor_3 (nor_3_out, A0, not_2_out);
  nor nor_4 (nor_4_out, not_1_out, not_2_out);
  D_Flip_Flop d_ff_1 (.clk(clock_1_out), .D(and_1_out), .Q(RD), .Qn(d_ff_1_qn));  // open: preset, en, reset
  and and_2 (and_2_out, WT, nor_1_out);
  and and_3 (and_3_out, nor_1_out, RD);
  and and_4 (and_4_out, WT, nor_2_out);
  and and_5 (and_5_out, nor_2_out, RD);
  and and_6 (and_6_out, WT, nor_3_out);
  and and_7 (and_7_out, nor_3_out, RD);
  and and_8 (and_8_out, WT, nor_4_out);
  and and_9 (and_9_out, nor_4_out, RD);
  and and_10 (WT, SENSE, d_ff_3_q);
  D_Flip_Flop d_ff_2 (.clk(clock_1_out), .D(RD), .Q(d_ff_2_q), .Qn(d_ff_2_qn));  // open: preset, en, reset
  D_Flip_Flop d_ff_3 (.clk(clock_1_out), .D(d_ff_2_q), .Q(d_ff_3_q), .Qn(d_ff_3_qn));  // open: preset, en, reset
  not not_3 (not_3_out, nor_5_out);
  nor nor_5 (nor_5_out, and_3_out, and_5_out);
  not not_4 (not_4_out, nor_6_out);
  nor nor_6 (nor_6_out, and_7_out, and_9_out);
  nor nor_7 (nor_7_out, and_3_out, and_7_out);
  nor nor_8 (nor_8_out, and_5_out, and_9_out);
  not not_5 (not_5_out, nor_7_out);
  not not_6 (not_6_out, nor_8_out);
  not not_7 (not_3_out, nor_11_out);
  not not_8 (not_4_out, nor_12_out);
  not not_9 (not_5_out, nor_10_out);
  not not_10 (not_6_out, nor_9_out);
  nor nor_9 (nor_9_out, and_8_out, and_4_out);
  nor nor_10 (nor_10_out, and_6_out, and_2_out);
  nor nor_11 (nor_11_out, and_2_out, and_4_out);
  nor nor_12 (nor_12_out, and_6_out, and_8_out);
endmodule
