// Logisim project CoreMemory3.circ as structural Verilog: 1 circuit, main circuit main
module main (
  input  A3,
  input  A2,
  input  A1,
  input  A0,
  output RD,
  output WT,
  output RD_2,
  output WT_2
);

  wire controlled_buffer_1_out, controlled_buffer_2_out, controlled_buffer_3_out, controlled_buffer_4_out,
       controlled_buffer_5_out, controlled_buffer_6_out, controlled_buffer_7_out, controlled_buffer_8_out,
       controlled_buffer_9_out, controlled_buffer_10_out, controlled_buffer_11_out, controlled_buffer_12_out,
       controlled_buffer_13_out, controlled_buffer_14_out, controlled_buffer_15_out,
       controlled_buffer_16_out, nor_1_out, nor_2_out, nor_3_out, nor_4_out, nor_5_out, nor_6_out, nor_7_out,
       nor_8_out, nor_9_out, nor_10_out, nor_11_out, nor_12_out, nor_13_out, nor_14_out, nor_15_out,
       nor_16_out, nor_17_out, nor_18_out, nor_19_out, nor_20_out, nor_21_out, nor_22_out, nor_23_out,
       nor_24_out, nor_25_out, nor_26_out, nor_27_out, nor_28_out, nor_29_out, nor_30_out, nor_31_out,
       nor_32_out, not_1_out, not_2_out, not_3_out, not_4_out, not_5_out, not_6_out, not_7_out, not_8_out,
       or_1_out, or_2_out, or_3_out, or_4_out, or_5_out, or_6_out, or_7_out, or_8_out, or_9_out, or_10_out,
       or_11_out, or_12_out, or_13_out, or_14_out, or_15_out, or_16_out, or_17_out, or_18_out, or_19_out,
       or_20_out, or_21_out, or_22_out, or_23_out, or_24_out, or_25_out, or_26_out, or_27_out, or_28_out,
       or_29_out, or_30_out, or_31_out, or_32_out;

  not not_1 (not_1_out, A3);
  not not_2 (not_2_out, A0);
  not not_3 (not_3_out, A2);
  not not_4 (not_4_out, A1);
  or or_1 (or_1_out, A0, A1, A2, A3);
  or or_2 (or_2_out, not_2_out, A1, A2, A3);
  or or_3 (or_3_out, A0, not_4_out, A2, A3);
  or or_4 (or_4_out, not_2_out, not_4_out, A2, A3);
  or or_5 (or_5_out, A0, A1, not_3_out, A3);
  or or_6 (or_6_out, not_2_out, A1, not_3_out, A3);
  or or_7 (or_7_out, A0, not_4_out, not_3_out, A3);
  or or_8 (or_8_out, not_2_out, not_4_out, not_3_out, A3);
  nor nor_1 (nor_1_out, WT, or_1_out);
  nor nor_2 (nor_2_out, or_1_out, RD);
  nor nor_3 (nor_3_out, WT, or_2_out);
  nor nor_4 (nor_4_out, or_2_out, RD);
  nor nor_5 (nor_5_out, WT, or_3_out);
  nor nor_6 (nor_6_out, or_3_out, RD);
  nor nor_7 (nor_7_out, WT, or_4_out);
  nor nor_8 (nor_8_out, or_4_out, RD);
  nor nor_9 (nor_9_out, WT, or_5_out);
  nor nor_10 (nor_10_out, or_5_out, RD);
  nor nor_11 (nor_11_out, WT, or_6_out);
  nor nor_12 (nor_12_out, or_6_out, RD);
  nor nor_13 (nor_13_out, WT, or_7_out);
  nor nor_14 (nor_14_out, or_7_out, RD);
  nor nor_15 (nor_15_out, WT, or_8_out);
  nor nor_16 (nor_16_out, or_8_out, RD);
  or or_9 (or_9_out, nor_2_out, nor_4_out, nor_6_out, nor_8_out);
  assign controlled_buffer_1_out = or_9_out ? 1'b1 : 1'bz;  // Controlled_Buffer controlled_buffer_1
  or or_10 (or_10_out, nor_10_out, nor_12_out, nor_14_out, nor_16_out);
  assign controlled_buffer_2_out = or_10_out ? 1'b1 : 1'bz;  // Controlled_Buffer controlled_buffer_2
  or or_11 (or_11_out, nor_24_out, nor_22_out, nor_20_out, nor_18_out);
  assign controlled_buffer_3_out = or_11_out ? 1'b1 : 1'bz;  // Controlled_Buffer controlled_buffer_3
  or or_12 (or_12_out, nor_32_out, nor_30_out, nor_28_out, nor_26_out);
  assign controlled_buffer_4_out = or_12_out ? 1'b1 : 1'bz;  // Controlled_Buffer controlled_buffer_4
  or or_13 (or_13_out, nor_2_out, nor_10_out, nor_18_out, nor_26_out);
  assign controlled_buffer_5_out = or_13_out ? 1'b1 : 1'bz;  // Controlled_Buffer controlled_buffer_5
  assign controlled_buffer_6_out = or_14_out ? 1'b1 : 1'bz;  // Controlled_Buffer controlled_buffer_6
  or or_14 (or_14_out, nor_25_out, nor_17_out, nor_9_out, nor_1_out);
  or or_15 (or_15_out, nor_6_out, nor_14_out, nor_22_out, nor_30_out);
  or or_16 (or_16_out, nor_4_out, nor_12_out, nor_20_out, nor_28_out);
  assign controlled_buffer_7_out = or_16_out ? 1'b1 : 1'bz;  // Controlled_Buffer controlled_buffer_7
  assign controlled_buffer_8_out = or_17_out ? 1'b1 : 1'bz;  // Controlled_Buffer controlled_buffer_8
  or or_17 (or_17_out, nor_27_out, nor_19_out, nor_11_out, nor_3_out);
  or or_18 (or_18_out, nor_29_out, nor_21_out, nor_13_out, nor_5_out);
  or or_19 (or_19_out, nor_8_out, nor_16_out, nor_24_out, nor_32_out);
  assign controlled_buffer_9_out = or_15_out ? 1'b1 : 1'bz;  // Controlled_Buffer controlled_buffer_9
  assign controlled_buffer_10_out = or_19_out ? 1'b1 : 1'bz;  // Controlled_Buffer controlled_buffer_10
  assign controlled_buffer_11_out = or_18_out ? 1'b1 : 1'bz;  // Controlled_Buffer controlled_buffer_11
  assign controlled_buffer_12_out = or_20_out ? 1'b1 : 1'bz;  // Controlled_Buffer controlled_buffer_12
  or or_20 (or_20_out, nor_31_out, nor_23_out, nor_15_out, nor_7_out);
  or or_21 (or_21_out, nor_1_out, nor_3_out, nor_5_out, nor_7_out);
  assign controlled_buffer_13_out = or_21_out ? 1'b1 : 1'bz;  // Controlled_Buffer controlled_buffer_13
  or or_22 (or_22_out, nor_9_out, nor_11_out, nor_13_out, nor_15_out);
  assign controlled_buffer_14_out = or_22_out ? 1'b1 : 1'bz;  // Controlled_Buffer controlled_buffer_14
  or or_23 (or_23_out, nor_17_out, nor_19_out, nor_21_out, nor_23_out);
  assign controlled_buffer_15_out = or_23_out ? 1'b1 : 1'bz;  // Controlled_Buffer controlled_buffer_15
  or or_24 (or_24_out, nor_25_out, nor_27_out, nor_29_out, nor_31_out);
  assign controlled_buffer_16_out = or_24_out ? 1'b1 : 1'bz;  // Controlled_Buffer controlled_buffer_16
  nor nor_17 (nor_17_out, WT, or_25_out);
  nor nor_18 (nor_18_out, or_25_out, RD);
  not nor_19 (nor_19_out, or_26_out);  // NOR_Gate
  not nor_20 (nor_20_out, or_26_out);  // NOR_Gate
  not nor_21 (nor_21_out, or_27_out);  // NOR_Gate
  not nor_22 (nor_22_out, or_27_out);  // NOR_Gate
  not nor_23 (nor_23_out, or_28_out);  // NOR_Gate
  not nor_24 (nor_24_out, or_28_out);  // NOR_Gate
  not nor_25 (nor_25_out, or_29_out);  // NOR_Gate
  not nor_26 (nor_26_out, or_29_out);  // NOR_Gate
  not nor_27 (nor_27_out, or_30_out);  // NOR_Gate
  not nor_28 (nor_28_out, or_30_out);  // NOR_Gate
  not nor_29 (nor_29_out, or_31_out);  // NOR_Gate
  not nor_30 (nor_30_out, or_31_out);  // NOR_Gate
  not nor_31 (nor_31_out, or_32_out);  // NOR_Gate
  not nor_32 (nor_32_out, or_32_out);  // NOR_Gate
  not not_5 (not_5_out, A3);
  or or_25 (or_25_out, A0, A1, A2, not_5_out);
  or or_26 (or_26_out, not_7_out, A1, A2, not_5_out);
  or or_27 (or_27_out, A0, not_8_out, A2, not_5_out);
  or or_28 (or_28_out, not_7_out, not_8_out, A2, not_5_out);
  or or_29 (or_29_out, A0, A1, not_6_out, not_5_out);
  or or_30 (or_30_out, not_7_out, A1, not_6_out, not_5_out);
  or or_31 (or_31_out, A0, not_8_out, not_6_out, not_5_out);
  or or_32 (or_32_out, not_7_out, not_8_out, not_6_out, not_5_out);
  not not_6 (not_6_out, A2);
  not not_7 (not_7_out, A0);
  not not_8 (not_8_out, A1);

  assign RD_2 = RD;
  assign WT_2 = WT;
  // also tied to GND on the sheet: {controlled_buffer_1_out, controlled_buffer_2_out, controlled_buffer_3_out, controlled_buffer_4_out, controlled_buffer_5_out, controlled_buffer_6_out, controlled_buffer_7_out, controlled_buffer_8_out, controlled_buffer_9_out, controlled_buffer_11_out, controlled_buffer_10_out, controlled_buffer_12_out, controlled_buffer_13_out, controlled_buffer_14_out, controlled_buffer_15_out, controlled_buffer_16_out}
endmodule
