// Logisim project UE0_v2.circ as structural Verilog: 1 circuit, main circuit main
module main (
  input  CLK,
  input  A2,
  input  A1,
  input  A0,
  input  I2,
  input  I1,
  input  I0,
  input  DATA,
  input  E0,
  input  E1,
  input  E2,
  output RR,
  output WRT,
  output out_14,
  output out_15,
  output out_16,
  output out_17,
  output DBUS
);

  wire buffer_1_out, buffer_7_out, buffer_8_out, nand_1_out, nand_2_out, nand_3_out, nand_4_out, nand_5_out,
       nand_6_out, nand_7_out, nand_8_out, nor_1_out, nor_2_out, nor_3_out, nor_4_out, nor_5_out, nor_6_out,
       nor_7_out, nor_8_out, nor_9_out, nor_10_out, nor_11_out, nor_12_out, nor_13_out, nor_14_out,
       nor_15_out, nor_16_out, nor_17_out, nor_18_out, nor_19_out, nor_20_out, nor_21_out, nor_22_out,
       nor_23_out, nor_24_out, nor_25_out, nor_26_out, nor_27_out, nor_28_out, nor_29_out, nor_30_out,
       nor_31_out, nor_32_out, nor_33_out, nor_34_out, nor_35_out, nor_36_out, nor_37_out, nor_38_out,
       nor_39_out, nor_40_out, nor_41_out, nor_42_out, not_1_out, not_2_out, not_3_out, not_4_out, not_5_out,
       not_6_out, not_7_out, not_8_out, not_9_out, not_10_out, not_11_out, not_13_out, or_2_out, or_3_out,
       or_4_out, or_5_out, or_6_out, or_7_out;

  not not_1 (not_1_out, A0);
  not not_2 (not_2_out, A1);
  buf buffer_1 (buffer_1_out, not_4_out);
  or or_1 (DBUS, DATA, or_7_out, buffer_1_out);
  not not_3 (not_3_out, DBUS);
  nand nand_1 (nand_1_out, not_8_out, RR);
  not not_4 (not_4_out, nand_1_out);
  not not_5 (not_5_out, I0);
  nand nand_2 (nand_2_out, not_5_out, I1, not_7_out);
  not not_6 (not_6_out, nand_2_out);
  not not_7 (not_7_out, I2);
  nand nand_3 (nand_3_out, I0, I1, I2);
  not not_8 (not_8_out, nand_3_out);
  nor nor_1 (nor_1_out, I0, RR, DBUS);
  nor nor_2 (nor_2_out, I1, nor_23_out, DBUS);
  nor nor_3 (nor_3_out, I2, RR, not_3_out);
  or or_2 (or_2_out, not_10_out, A0, A1);
  or or_3 (or_3_out, not_10_out, not_1_out, A1);
  nor nor_4 (nor_4_out, nor_1_out, nor_2_out, nor_3_out);
  nor nor_5 (nor_5_out, DBUS, or_2_out);
  nor nor_6 (nor_6_out, nor_5_out, or_2_out);
  nor nor_7 (nor_7_out, DBUS, or_3_out);
  nor nor_8 (nor_8_out, nor_7_out, or_3_out);
  nand nand_4 (nand_4_out, nand_3_out, CLK);
  not not_9 (not_9_out, nand_4_out);
  nor nor_9 (nor_9_out, nor_5_out, nor_10_out);
  nor nor_10 (nor_10_out, nor_9_out, nor_6_out);
  nor nor_11 (nor_11_out, nor_7_out, nor_12_out);
  nor nor_12 (nor_12_out, nor_11_out, nor_8_out);
  nor nor_13 (nor_13_out, A1, A0, E0);
  nor nor_14 (nor_14_out, nor_4_out, not_9_out);
  nor nor_15 (nor_15_out, nor_14_out, not_9_out);
  not not_10 (not_10_out, WRT);
  nor nor_16 (nor_16_out, WRT, nor_10_out, A0, A1);
  nor nor_17 (nor_17_out, WRT, nor_12_out, not_1_out, A1);
  nor nor_18 (nor_18_out, A1, not_1_out, E1);
  nor nor_19 (nor_19_out, nor_14_out, nor_20_out);
  nor nor_20 (nor_20_out, nor_19_out, nor_15_out);
  or or_4 (or_4_out, not_10_out, A0, not_2_out);
  or or_5 (or_5_out, not_10_out, not_1_out, not_2_out);
  nor nor_21 (nor_21_out, nor_22_out, nor_23_out);
  nor nor_22 (nor_22_out, nor_19_out, nand_4_out);
  nor nor_23 (nor_23_out, nor_21_out, nor_24_out);
  nor nor_24 (nor_24_out, nor_22_out, nand_4_out);
  nor nor_25 (nor_25_out, DBUS, or_4_out);
  nor nor_26 (nor_26_out, nor_25_out, or_4_out);
  nor nor_27 (nor_27_out, DBUS, or_5_out);
  nor nor_28 (nor_28_out, nor_27_out, or_5_out);
  nor nor_29 (nor_29_out, not_2_out, A0, E2);
  nand nand_5 (nand_5_out, CLK, not_6_out);
  buf buffer_2 (RR, nor_21_out);
  nand nand_6 (nand_6_out, not_8_out, CLK);
  nor nor_30 (nor_30_out, nor_25_out, nor_31_out);
  nor nor_31 (nor_31_out, nor_30_out, nor_26_out);
  nor nor_32 (nor_32_out, nor_27_out, nor_33_out);
  nor nor_33 (nor_33_out, nor_32_out, nor_28_out);
  nor nor_34 (nor_34_out, not_2_out, not_1_out, nor_23_out);
  nor nor_35 (nor_35_out, DBUS, nand_5_out);
  nor nor_36 (nor_36_out, nor_35_out, nand_5_out);
  nand nand_7 (nand_7_out, nor_39_out, not_11_out);
  not not_11 (not_11_out, nand_6_out);
  nor nor_37 (nor_37_out, WRT, nor_31_out, A0, not_2_out);
  nor nor_38 (nor_38_out, WRT, nor_33_out, not_1_out, not_2_out);
  or or_6 (or_6_out, nor_34_out, nor_29_out, nor_18_out, nor_13_out);
  nor nor_39 (nor_39_out, nor_35_out, nor_40_out);
  nor nor_40 (nor_40_out, nor_39_out, nor_36_out);
  not not_12 (WRT, nand_7_out);
  nor nor_41 (nor_41_out, A2, nor_42_out);
  nor nor_42 (nor_42_out, nor_37_out, nor_16_out, nor_38_out, nor_17_out);
  buf buffer_3 (out_14, nor_30_out);
  buf buffer_4 (out_15, nor_9_out);
  buf buffer_5 (out_16, nor_32_out);
  buf buffer_6 (out_17, nor_11_out);
  not not_13 (not_13_out, nand_8_out);
  nand nand_8 (nand_8_out, A2, or_6_out);
  or or_7 (or_7_out, buffer_8_out, buffer_7_out);
  buf buffer_7 (buffer_7_out, not_13_out);
  buf buffer_8 (buffer_8_out, nor_41_out);

  // Notes on the sheet:
  //   MEMORY
  //   000: RAM0
  //   001: RAM1
  //   010: RAM2
  //   011: RAM3
  //   100: EXT0
  //   101: EXT1
  //   110: EXT2
  //   111: RR
  //   000: AND
  //   001: XNOR
  //   010: OEN
  //   OPERATION
  //   100: LD
  //   110: OR
  //   011: ORCD
  //   111: STO
  //   101: ORCR
endmodule
