// Logisim project UE4_ALL.circ as structural Verilog: 1 circuit, main circuit main
module main (
  input  A2,
  input  A1,
  input  A0,
  input  I1,
  input  I0,
  input  _1_RST,
  input  nRD,
  input  nWT,
  input  D3,
  input  D2,
  input  D1,
  input  D0,
  output nRD_2,
  output nWT_2,
  output OU0,
  output WRT,
  output OU1,
  output OU2,
  output OU3,
  output FLG1F
);

  wire _14_CLK_out, and_1_out, and_2_out, and_3_out, and_4_out, and_5_out, and_6_out, and_7_out, and_8_out,
       and_9_out, and_10_out, and_11_out, and_12_out, and_13_out, and_14_out, and_15_out, and_16_out,
       and_17_out, and_18_out, and_19_out, and_20_out, and_21_out, and_22_out, and_23_out, and_24_out,
       and_25_out, and_26_out, and_27_out, and_28_out, and_29_out, and_30_out, and_31_out, and_32_out,
       and_33_out, and_34_out, and_35_out, and_36_out, controlled_buffer_1_out, controlled_buffer_2_out,
       controlled_buffer_3_out, controlled_buffer_4_out, controlled_buffer_5_out, controlled_buffer_6_out,
       controlled_buffer_7_out, controlled_buffer_8_out, controlled_buffer_9_out, controlled_buffer_10_out,
       controlled_buffer_11_out, controlled_buffer_12_out, controlled_buffer_13_out,
       controlled_buffer_14_out, nand_1_out, nand_2_out, nor_1_out, nor_2_out, nor_3_out, nor_4_out,
       nor_5_out, nor_6_out, nor_7_out, nor_8_out, nor_9_out, nor_10_out, nor_11_out, nor_12_out, nor_14_out,
       nor_16_out, nor_18_out, nor_20_out, nor_21_out, nor_23_out, nor_24_out, nor_25_out, nor_26_out,
       nor_27_out, nor_28_out, nor_29_out, nor_30_out, nor_31_out, nor_32_out, nor_33_out, nor_34_out,
       nor_35_out, nor_36_out, nor_37_out, nor_38_out, nor_39_out, nor_40_out, nor_41_out, nor_42_out,
       nor_43_out, nor_44_out, nor_45_out, nor_46_out, nor_47_out, nor_48_out, nor_49_out, nor_50_out,
       nor_51_out, nor_52_out, nor_53_out, nor_55_out, nor_56_out, nor_57_out, nor_58_out, not_1_out,
       not_2_out, not_3_out, not_4_out, not_5_out, not_6_out, not_7_out, not_8_out, not_9_out, not_10_out,
       not_11_out, not_12_out, not_13_out, not_14_out, not_15_out, not_16_out, not_17_out, not_18_out,
       not_19_out, not_20_out, not_21_out, not_22_out, not_23_out, or_1_out, or_2_out, or_3_out, or_4_out,
       or_5_out, or_6_out, or_7_out, or_8_out, or_9_out, or_10_out, or_11_out, or_12_out, or_13_out,
       or_14_out, or_15_out, or_16_out, or_17_out, or_18_out, or_19_out, or_20_out, or_21_out, or_22_out,
       or_23_out, or_24_out, or_25_out, or_26_out;

  or or_1 (or_1_out, A0, A1, A2);
  or or_2 (or_2_out, not_14_out, A1, A2);
  or or_3 (or_3_out, A0, not_11_out, A2);
  or or_4 (or_4_out, not_14_out, not_11_out, A2);
  or or_5 (or_5_out, A0, A1, not_12_out);
  or or_6 (or_6_out, not_14_out, A1, not_12_out);
  nor nor_1 (nor_1_out, nWT, or_1_out);
  nor nor_2 (nor_2_out, or_1_out, nRD);
  nor nor_3 (nor_3_out, nWT, or_2_out);
  nor nor_4 (nor_4_out, or_2_out, nRD);
  nor nor_5 (nor_5_out, nWT, or_3_out);
  nor nor_6 (nor_6_out, or_3_out, nRD);
  nor nor_7 (nor_7_out, nWT, or_4_out);
  nor nor_8 (nor_8_out, or_4_out, nRD);
  nor nor_9 (nor_9_out, nWT, or_5_out);
  nor nor_10 (nor_10_out, or_5_out, nRD);
  nor nor_11 (nor_11_out, nWT, or_6_out);
  nor nor_12 (nor_12_out, or_6_out, nRD);
  nand nand_1 (nand_1_out, nWT, nRD);
  assign controlled_buffer_1_out = nor_2_out ? 1'b1 : 1'bz;  // Controlled_Buffer controlled_buffer_1
  assign controlled_buffer_2_out = nor_4_out ? 1'b1 : 1'bz;  // Controlled_Buffer controlled_buffer_2
  assign controlled_buffer_3_out = nor_6_out ? 1'b1 : 1'bz;  // Controlled_Buffer controlled_buffer_3
  assign controlled_buffer_4_out = nor_8_out ? 1'b1 : 1'bz;  // Controlled_Buffer controlled_buffer_4
  assign controlled_buffer_5_out = nor_10_out ? 1'b1 : 1'bz;  // Controlled_Buffer controlled_buffer_5
  assign controlled_buffer_6_out = nor_12_out ? 1'b1 : 1'bz;  // Controlled_Buffer controlled_buffer_6
  assign controlled_buffer_7_out = nand_1_out ? 1'b1 : 1'bz;  // Controlled_Buffer controlled_buffer_7
  assign controlled_buffer_8_out = nand_1_out ? 1'b1 : 1'bz;  // Controlled_Buffer controlled_buffer_8
  assign controlled_buffer_9_out = nor_1_out ? 1'b1 : 1'bz;  // Controlled_Buffer controlled_buffer_9
  assign controlled_buffer_10_out = nor_3_out ? 1'b1 : 1'bz;  // Controlled_Buffer controlled_buffer_10
  assign controlled_buffer_11_out = nor_5_out ? 1'b1 : 1'bz;  // Controlled_Buffer controlled_buffer_11
  assign controlled_buffer_12_out = nor_7_out ? 1'b1 : 1'bz;  // Controlled_Buffer controlled_buffer_12
  assign controlled_buffer_13_out = nor_9_out ? 1'b1 : 1'bz;  // Controlled_Buffer controlled_buffer_13
  assign controlled_buffer_14_out = nor_11_out ? 1'b1 : 1'bz;  // Controlled_Buffer controlled_buffer_14
  nor nor_13 (OU0, or_7_out, nor_14_out);
  nor nor_14 (nor_14_out, OU0, and_2_out);
  nor nor_15 (OU1, or_8_out, nor_16_out);
  nor nor_16 (nor_16_out, OU1, and_4_out);
  nor nor_17 (OU2, or_9_out, nor_18_out);
  nor nor_18 (nor_18_out, OU2, and_6_out);
  nor nor_19 (OU3, or_10_out, nor_20_out);
  nor nor_20 (nor_20_out, OU3, and_8_out);
  or or_7 (or_7_out, _1_RST, and_1_out);
  or or_8 (or_8_out, _1_RST, and_3_out);
  or or_9 (or_9_out, _1_RST, and_5_out);
  or or_10 (or_10_out, _1_RST, and_7_out);
  and and_1 (and_1_out, OU0, not_1_out, nor_21_out);
  not not_1 (not_1_out, or_23_out);
  and and_2 (and_2_out, nor_21_out, or_23_out, nor_14_out);
  not not_2 (not_2_out, or_24_out);
  and and_3 (and_3_out, OU1, not_2_out, nor_21_out);
  and and_4 (and_4_out, nor_21_out, or_24_out, nor_16_out);
  and and_5 (and_5_out, OU2, not_3_out, nor_21_out);
  not not_3 (not_3_out, or_25_out);
  and and_6 (and_6_out, nor_21_out, or_25_out, nor_18_out);
  and and_7 (and_7_out, OU3, not_4_out, nor_21_out);
  not not_4 (not_4_out, or_26_out);
  and and_8 (and_8_out, nor_21_out, or_26_out, nor_20_out);
  not not_5 (not_5_out, D3);
  nor nor_21 (nor_21_out, not_8_out, or_11_out, or_12_out);
  nor nor_22 (FLG1F, not_12_out, not_11_out, not_14_out, not_13_out, not_15_out);
  not not_6 (not_6_out, D2);
  not not_7 (not_7_out, D1);
  nor nor_23 (nor_23_out, not_5_out, or_13_out);
  nor nor_24 (nor_24_out, not_6_out, or_13_out);
  not not_8 (not_8_out, WRT);
  or or_11 (or_11_out, not_15_out, not_13_out);
  or or_12 (or_12_out, A0, not_11_out, not_12_out);
  not not_9 (not_9_out, or_11_out);
  or or_13 (or_13_out, not_9_out, or_12_out);
  not not_10 (not_10_out, D0);
  nor nor_25 (nor_25_out, not_10_out, or_13_out);
  nor nor_26 (nor_26_out, not_7_out, or_13_out);
  not not_11 (not_11_out, A1);
  not not_12 (not_12_out, A2);
  not not_13 (not_13_out, I1);
  not not_14 (not_14_out, A0);
  not not_15 (not_15_out, I0);
  nor nor_27 (nor_27_out, I0, not_13_out);
  not not_16 (not_16_out, and_9_out);
  and and_9 (and_9_out, I0, I1);
  and and_10 (and_10_out, A0, A1, A2);
  nor nor_28 (nor_28_out, I0, I1);
  nor nor_29 (nor_29_out, not_15_out, I1);
  nor nor_30 (nor_30_out, and_9_out, and_10_out);
  and and_11 (and_11_out, or_23_out, nor_28_out);
  and and_12 (and_12_out, or_24_out, nor_28_out);
  and and_13 (and_13_out, or_25_out, nor_28_out);
  and and_14 (and_14_out, or_26_out, nor_28_out);
  and and_15 (and_15_out, or_23_out, nor_29_out, nor_46_out);
  and and_16 (and_16_out, or_24_out, nor_29_out, nor_48_out);
  and and_17 (and_17_out, or_25_out, nor_29_out, nor_50_out);
  and and_18 (and_18_out, or_26_out, nor_29_out, nor_52_out);
  nor nor_31 (nor_31_out, and_11_out, and_15_out);
  not not_17 (not_17_out, nor_31_out);
  nor nor_32 (nor_32_out, and_12_out, and_16_out);
  nor nor_33 (nor_33_out, and_13_out, and_17_out);
  nor nor_34 (nor_34_out, and_14_out, and_18_out);
  not not_18 (not_18_out, nor_32_out);
  not not_19 (not_19_out, nor_33_out);
  not not_20 (not_20_out, nor_34_out);
  Clock _14_CLK (.out(_14_CLK_out));
  not not_21 (not_21_out, _14_CLK_out);
  nor nor_35 (nor_35_out, not_21_out, and_9_out, nor_27_out);
  and and_19 (and_19_out, nor_36_out, nor_31_out, nor_35_out);
  and and_20 (and_20_out, nor_35_out, not_17_out, nor_37_out);
  and and_21 (and_21_out, nor_38_out, nor_32_out, nor_35_out);
  and and_22 (and_22_out, nor_35_out, not_18_out, nor_39_out);
  and and_23 (and_23_out, nor_40_out, nor_33_out, nor_35_out);
  and and_24 (and_24_out, nor_35_out, not_19_out, nor_41_out);
  and and_25 (and_25_out, nor_42_out, nor_34_out, nor_35_out);
  and and_26 (and_26_out, nor_35_out, not_20_out, nor_43_out);
  or or_14 (or_14_out, _1_RST, and_20_out);
  or or_15 (or_15_out, _1_RST, and_22_out);
  or or_16 (or_16_out, _1_RST, and_24_out);
  or or_17 (or_17_out, _1_RST, and_26_out);
  nand nand_2 (nand_2_out, nor_27_out, _14_CLK_out);
  not not_22 (not_22_out, nand_2_out);
  not not_23 (not_23_out, or_23_out);
  and and_27 (and_27_out, nor_44_out, not_23_out, not_22_out);
  and and_28 (and_28_out, not_22_out, or_23_out, nor_45_out);
  nor nor_36 (nor_36_out, and_19_out, nor_37_out);
  nor nor_37 (nor_37_out, nor_36_out, or_14_out);
  nor nor_38 (nor_38_out, and_21_out, nor_39_out);
  nor nor_39 (nor_39_out, nor_38_out, or_15_out);
  nor nor_40 (nor_40_out, and_23_out, nor_41_out);
  nor nor_41 (nor_41_out, nor_40_out, or_16_out);
  nor nor_42 (nor_42_out, and_25_out, nor_43_out);
  nor nor_43 (nor_43_out, nor_42_out, or_17_out);
  or or_18 (or_18_out, _1_RST, and_27_out);
  nor nor_44 (nor_44_out, or_18_out, nor_45_out);
  nor nor_45 (nor_45_out, nor_44_out, and_28_out);
  or or_19 (or_19_out, _1_RST, and_29_out);
  and and_29 (and_29_out, nor_46_out, nor_36_out, not_21_out);
  and and_30 (and_30_out, not_21_out, nor_37_out, nor_47_out);
  or or_20 (or_20_out, _1_RST, and_31_out);
  and and_31 (and_31_out, nor_48_out, nor_38_out, not_21_out);
  and and_32 (and_32_out, not_21_out, nor_39_out, nor_49_out);
  or or_21 (or_21_out, _1_RST, and_33_out);
  and and_33 (and_33_out, nor_50_out, nor_40_out, not_21_out);
  and and_34 (and_34_out, not_21_out, nor_41_out, nor_51_out);
  or or_22 (or_22_out, _1_RST, and_35_out);
  and and_35 (and_35_out, nor_52_out, nor_42_out, not_21_out);
  and and_36 (and_36_out, not_21_out, nor_43_out, nor_53_out);
  nor nor_46 (nor_46_out, or_19_out, nor_47_out);
  nor nor_47 (nor_47_out, nor_46_out, and_30_out);
  nor nor_48 (nor_48_out, or_20_out, nor_49_out);
  nor nor_49 (nor_49_out, nor_48_out, and_32_out);
  nor nor_50 (nor_50_out, or_21_out, nor_51_out);
  nor nor_51 (nor_51_out, nor_50_out, and_34_out);
  nor nor_52 (nor_52_out, or_22_out, nor_53_out);
  nor nor_53 (nor_53_out, nor_52_out, and_36_out);
  or or_23 (or_23_out, nor_25_out, nor_55_out);
  or or_24 (or_24_out, nor_26_out, nor_56_out);
  or or_25 (or_25_out, nor_24_out, nor_57_out);
  or or_26 (or_26_out, nor_23_out, nor_58_out);
  nor nor_54 (WRT, not_21_out, not_16_out, nor_45_out);
  nor nor_55 (nor_55_out, nor_30_out, nor_46_out);
  nor nor_56 (nor_56_out, nor_30_out, nor_48_out);
  nor nor_57 (nor_57_out, nor_30_out, nor_50_out);
  nor nor_58 (nor_58_out, nor_30_out, nor_52_out);

  assign nRD_2 = nRD;
  assign nWT_2 = nWT;
  // also tied to GND on the sheet: {controlled_buffer_1_out, controlled_buffer_2_out, controlled_buffer_3_out, controlled_buffer_4_out, controlled_buffer_5_out, controlled_buffer_6_out, controlled_buffer_7_out, controlled_buffer_8_out, controlled_buffer_9_out, controlled_buffer_10_out, controlled_buffer_11_out, controlled_buffer_12_out, controlled_buffer_13_out, controlled_buffer_14_out}

  // Notes on the sheet:
  //   46 NOR GATES
  //   23 NOT GATES
  //   1 NAND GATES
  //   70 INVERTERS NEEDED
  //   OUTPUT REGISTER
  //   EXTERNAL INPUT
  //   OEN
  //   STO
  //   111
  //   LD
  //   NAND
  //   00: LD, 01: NAND
  //   10: OEN, 11: STO
  //   LOGIC UNIT
  //   RESULTS REGISTER
  //   OEN REGISTER
endmodule
