// Logisim project UE4_FSM.circ as structural Verilog: 1 circuit, main circuit main
module main (
  input  in_1,
  input  in_2,
  input  in_3,
  input  in_4,
  input  in_5,
  input  in_6,
  input  in_7,
  input  in_8,
  input  in_9,
  output TAPE,
  output CLK,
  output READ,
  output WRT
);

  wire and_1_out, and_2_out, and_3_out, and_4_out, and_5_out, and_6_out, and_7_out, and_8_out, clock_1_out,
       nor_1_out, nor_2_out, nor_3_out, nor_4_out, nor_5_out, nor_6_out, nor_7_out, nor_8_out, not_1_out,
       not_2_out, not_3_out, not_4_out, or_1_out, or_2_out, or_3_out, or_4_out, or_5_out, or_6_out, undriven,
       undriven_2, undriven_3, undriven_4, undriven_5, undriven_6, undriven_7, undriven_8;

  Clock clock_1 (.out(clock_1_out));
  or or_1 (or_1_out, in_1, WRT);
  D_Flip_Flop d_ff_1 (.clk(clock_1_out), .D(or_1_out), .Q(TAPE));  // open: Qn, preset, en, reset
  D_Flip_Flop d_ff_2 (.clk(clock_1_out), .D(TAPE), .Q(READ));  // open: Qn, preset, en, reset
  D_Flip_Flop d_ff_3 (.clk(clock_1_out), .D(READ), .Q(CLK));  // open: Qn, preset, en, reset
  D_Flip_Flop d_ff_4 (.clk(clock_1_out), .D(CLK), .Q(WRT));  // open: Qn, preset, en, reset
  or or_2 (or_2_out, READ, CLK);
  not not_1 (not_1_out, undriven);
  and and_1 (and_1_out, nor_1_out, not_1_out, or_2_out);
  and and_2 (and_2_out, or_2_out, undriven, nor_2_out);
  and and_3 (and_3_out, nor_3_out, not_2_out, or_2_out);
  not not_2 (not_2_out, undriven_2);
  and and_4 (and_4_out, or_2_out, undriven_2, nor_4_out);
  and and_5 (and_5_out, nor_5_out, not_3_out, or_2_out);
  not not_3 (not_3_out, undriven_3);
  and and_6 (and_6_out, or_2_out, undriven_3, nor_6_out);
  and and_7 (and_7_out, nor_7_out, not_4_out, or_2_out);
  not not_4 (not_4_out, undriven_4);
  and and_8 (and_8_out, or_2_out, undriven_4, nor_8_out);
  or or_3 (or_3_out, undriven_5, and_1_out);
  or or_4 (or_4_out, undriven_6, and_3_out);
  or or_5 (or_5_out, undriven_7, and_5_out);
  or or_6 (or_6_out, undriven_8, and_7_out);
  nor nor_1 (nor_1_out, or_3_out, nor_2_out);
  nor nor_2 (nor_2_out, nor_1_out, and_2_out);
  nor nor_3 (nor_3_out, or_4_out, nor_4_out);
  nor nor_4 (nor_4_out, nor_3_out, and_4_out);
  nor nor_5 (nor_5_out, or_5_out, nor_6_out);
  nor nor_6 (nor_6_out, nor_5_out, and_6_out);
  nor nor_7 (nor_7_out, or_6_out, nor_8_out);
  nor nor_8 (nor_8_out, nor_7_out, and_8_out);
endmodule
