// Logisim project Proc.circ as structural Verilog: 1 circuit, main circuit main
module main (
  input  A2,
  input  A1,
  input  A0,
  input  STO,
  input  DAT,
  output RR,
  output DAT_2,
  output WRT
);

  wire Clock_out, nor_1_out, nor_2_out, nor_3_out, nor_4_out, nor_5_out, nor_6_out, nor_7_out, nor_8_out,
       nor_9_out, nor_10_out, nor_11_out, nor_12_out, nor_13_out, nor_15_out, not_1_out, not_2_out,
       not_3_out, or_1_out, or_2_out;

  Clock Clock (.out(Clock_out));
  not not_1 (not_1_out, A0);
  not not_2 (not_2_out, DAT);
  not not_3 (not_3_out, Clock_out);
  or or_1 (or_1_out, not_1_out, STO);
  nor nor_1 (nor_1_out, A1, STO);
  or or_2 (or_2_out, A2, STO);
  nor nor_2 (nor_2_out, or_1_out, STO);
  nor nor_3 (nor_3_out, or_1_out, nor_15_out, not_2_out);
  nor nor_4 (nor_4_out, nor_1_out, RR, not_2_out);
  nor nor_5 (nor_5_out, or_2_out, nor_15_out, DAT);
  nor nor_6 (nor_6_out, nor_2_out, RR, DAT);
  nor nor_7 (nor_7_out, nor_3_out, nor_4_out, nor_5_out, nor_6_out);
  nor nor_8 (nor_8_out, nor_7_out, not_3_out);
  nor nor_9 (nor_9_out, nor_8_out, not_3_out);
  and and_1 (WRT, Clock_out, STO);
  nor nor_10 (nor_10_out, nor_8_out, nor_11_out);
  nor nor_11 (nor_11_out, nor_10_out, nor_9_out);
  nor nor_12 (nor_12_out, nor_10_out, Clock_out);
  nor nor_13 (nor_13_out, nor_12_out, Clock_out);
  nor nor_14 (RR, nor_12_out, nor_15_out);
  nor nor_15 (nor_15_out, RR, nor_13_out);
  and and_2 (DAT_2, RR, WRT);

  // Notes on the sheet:
  //   000 = LD; 001 = Invert RR; 010 = AND; 011 = NOR; 100 = OR; 101 = NAND; 110 = NOP; 111 = LDC
endmodule
