// Logisim project Ram.circ as structural Verilog: 1 circuit, main circuit main
module main (
  input  Write,
  input  Data,
  input  in_3,
  input  in_4,
  input  in_5,
  input  in_6,
  output out_7
);

  wire buffer_1_out, buffer_5_out, buffer_9_out, nor_1_out, nor_2_out, nor_3_out, nor_4_out, nor_5_out,
       nor_6_out, nor_7_out, nor_8_out, nor_9_out, nor_10_out, nor_11_out, nor_12_out, nor_13_out,
       nor_14_out, nor_15_out, nor_16_out, nor_17_out, nor_18_out, nor_19_out, nor_20_out, nor_21_out,
       nor_22_out, nor_23_out, nor_24_out, nor_25_out, nor_26_out, nor_27_out, nor_28_out, nor_29_out,
       nor_30_out, nor_31_out, nor_32_out, nor_33_out, nor_34_out, nor_35_out, nor_36_out, nor_37_out,
       nor_38_out, nor_39_out, nor_40_out, nor_41_out, nor_42_out, nor_43_out, nor_44_out, nor_45_out,
       nor_46_out, nor_47_out, nor_48_out, nor_49_out, nor_50_out, nor_51_out, nor_52_out, nor_53_out,
       nor_54_out, nor_55_out, nor_56_out, nor_57_out, nor_58_out, nor_59_out, nor_60_out, nor_61_out,
       nor_62_out, nor_63_out, nor_64_out, nor_65_out, nor_66_out, nor_67_out, nor_68_out, nor_69_out,
       nor_70_out, nor_71_out, nor_72_out, nor_73_out, nor_74_out, nor_75_out, nor_76_out, nor_77_out,
       nor_78_out, nor_79_out, nor_80_out, not_1_out, not_2_out, not_3_out, not_4_out, not_5_out, or_1_out,
       or_2_out, or_3_out, or_4_out, or_5_out, or_6_out, or_7_out, or_8_out, or_9_out, or_10_out, or_11_out,
       or_12_out, or_13_out, or_14_out, or_15_out, or_16_out, or_17_out, or_18_out, or_19_out, or_20_out,
       or_21_out, or_22_out, or_23_out, or_24_out, or_25_out, or_26_out, or_27_out, or_28_out, or_29_out;

  not not_1 (not_1_out, in_4);
  not not_2 (not_2_out, in_3);
  not not_3 (not_3_out, in_6);
  not not_4 (not_4_out, in_5);
  or or_1 (or_1_out, in_6, in_5);
  or or_2 (or_2_out, not_3_out, in_5);
  or or_3 (or_3_out, in_6, not_4_out);
  or or_4 (or_4_out, not_3_out, not_4_out);
  or or_5 (or_5_out, in_4, in_3);
  or or_6 (or_6_out, not_1_out, in_3);
  or or_7 (or_7_out, in_4, not_2_out);
  or or_8 (or_8_out, not_1_out, not_2_out);
  or or_9 (or_9_out, buffer_5_out, or_5_out, or_1_out);
  or or_10 (or_10_out, buffer_5_out, or_5_out, or_2_out);
  or or_11 (or_11_out, buffer_5_out, or_5_out, or_3_out);
  or or_12 (or_12_out, buffer_5_out, or_5_out, or_4_out);
  or or_13 (or_13_out, out_7, Data);
  nor nor_1 (nor_1_out, buffer_1_out, or_9_out);
  nor nor_2 (nor_2_out, nor_1_out, or_9_out);
  nor nor_3 (nor_3_out, buffer_1_out, or_10_out);
  nor nor_4 (nor_4_out, nor_3_out, or_10_out);
  nor nor_5 (nor_5_out, buffer_1_out, or_11_out);
  nor nor_6 (nor_6_out, nor_5_out, or_11_out);
  nor nor_7 (nor_7_out, buffer_1_out, or_12_out);
  nor nor_8 (nor_8_out, nor_7_out, or_12_out);
  buf buffer_1 (buffer_1_out, or_13_out);
  buf buffer_2 (buffer_1_out, or_13_out);
  buf buffer_3 (buffer_1_out, or_13_out);
  buf buffer_4 (buffer_1_out, or_13_out);
  nor nor_9 (nor_9_out, nor_1_out, nor_10_out);
  nor nor_10 (nor_10_out, nor_9_out, nor_2_out);
  nor nor_11 (nor_11_out, nor_3_out, nor_12_out);
  nor nor_12 (nor_12_out, nor_11_out, nor_4_out);
  nor nor_13 (nor_13_out, nor_5_out, nor_14_out);
  nor nor_14 (nor_14_out, nor_13_out, nor_6_out);
  nor nor_15 (nor_15_out, nor_7_out, nor_16_out);
  nor nor_16 (nor_16_out, nor_15_out, nor_8_out);
  nor nor_17 (nor_17_out, buffer_9_out, nor_10_out, or_5_out, or_1_out);
  nor nor_18 (nor_18_out, buffer_9_out, nor_12_out, or_5_out, or_2_out);
  nor nor_19 (nor_19_out, buffer_9_out, nor_14_out, or_5_out, or_3_out);
  nor nor_20 (nor_20_out, buffer_9_out, nor_16_out, or_5_out, or_4_out);
  not not_5 (not_5_out, Write);
  buf buffer_5 (buffer_5_out, not_5_out);
  buf buffer_6 (buffer_5_out, not_5_out);
  buf buffer_7 (buffer_5_out, not_5_out);
  buf buffer_8 (buffer_5_out, not_5_out);
  or or_14 (or_14_out, buffer_5_out, or_6_out, or_1_out);
  or or_15 (or_15_out, buffer_5_out, or_6_out, or_2_out);
  or or_16 (or_16_out, buffer_5_out, or_6_out, or_3_out);
  or or_17 (or_17_out, buffer_5_out, or_6_out, or_4_out);
  nor nor_21 (nor_21_out, buffer_1_out, or_14_out);
  nor nor_22 (nor_22_out, nor_21_out, or_14_out);
  nor nor_23 (nor_23_out, buffer_1_out, or_15_out);
  nor nor_24 (nor_24_out, nor_23_out, or_15_out);
  nor nor_25 (nor_25_out, buffer_1_out, or_16_out);
  nor nor_26 (nor_26_out, nor_25_out, or_16_out);
  nor nor_27 (nor_27_out, buffer_1_out, or_17_out);
  nor nor_28 (nor_28_out, nor_27_out, or_17_out);
  buf buffer_9 (buffer_9_out, Write);
  buf buffer_10 (buffer_9_out, Write);
  buf buffer_11 (buffer_9_out, Write);
  buf buffer_12 (buffer_9_out, Write);
  nor nor_29 (nor_29_out, nor_21_out, nor_30_out);
  nor nor_30 (nor_30_out, nor_29_out, nor_22_out);
  nor nor_31 (nor_31_out, nor_23_out, nor_32_out);
  nor nor_32 (nor_32_out, nor_31_out, nor_24_out);
  nor nor_33 (nor_33_out, nor_25_out, nor_34_out);
  nor nor_34 (nor_34_out, nor_33_out, nor_26_out);
  nor nor_35 (nor_35_out, nor_27_out, nor_36_out);
  nor nor_36 (nor_36_out, nor_35_out, nor_28_out);
  nor nor_37 (nor_37_out, buffer_9_out, nor_30_out, or_6_out, or_1_out);
  nor nor_38 (nor_38_out, buffer_9_out, nor_32_out, or_6_out, or_2_out);
  nor nor_39 (nor_39_out, buffer_9_out, nor_34_out, or_6_out, or_3_out);
  nor nor_40 (nor_40_out, buffer_9_out, nor_36_out, or_6_out, or_4_out);
  or or_18 (or_18_out, buffer_5_out, or_7_out, or_1_out);
  or or_19 (or_19_out, buffer_5_out, or_7_out, or_2_out);
  or or_20 (or_20_out, buffer_5_out, or_7_out, or_3_out);
  or or_21 (or_21_out, buffer_5_out, or_7_out, or_4_out);
  nor nor_41 (nor_41_out, buffer_1_out, or_18_out);
  nor nor_42 (nor_42_out, nor_41_out, or_18_out);
  nor nor_43 (nor_43_out, buffer_1_out, or_19_out);
  nor nor_44 (nor_44_out, nor_43_out, or_19_out);
  nor nor_45 (nor_45_out, buffer_1_out, or_20_out);
  nor nor_46 (nor_46_out, nor_45_out, or_20_out);
  nor nor_47 (nor_47_out, buffer_1_out, or_21_out);
  nor nor_48 (nor_48_out, nor_47_out, or_21_out);
  nor nor_49 (nor_49_out, nor_41_out, nor_50_out);
  nor nor_50 (nor_50_out, nor_49_out, nor_42_out);
  nor nor_51 (nor_51_out, nor_43_out, nor_52_out);
  nor nor_52 (nor_52_out, nor_51_out, nor_44_out);
  nor nor_53 (nor_53_out, nor_45_out, nor_54_out);
  nor nor_54 (nor_54_out, nor_53_out, nor_46_out);
  nor nor_55 (nor_55_out, nor_47_out, nor_56_out);
  nor nor_56 (nor_56_out, nor_55_out, nor_48_out);
  nor nor_57 (nor_57_out, buffer_9_out, nor_50_out, or_7_out, or_1_out);
  nor nor_58 (nor_58_out, buffer_9_out, nor_52_out, or_7_out, or_2_out);
  nor nor_59 (nor_59_out, buffer_9_out, nor_54_out, or_7_out, or_3_out);
  nor nor_60 (nor_60_out, buffer_9_out, nor_56_out, or_7_out, or_4_out);
  or or_22 (or_22_out, buffer_5_out, or_8_out, or_1_out);
  or or_23 (or_23_out, buffer_5_out, or_8_out, or_2_out);
  or or_24 (or_24_out, buffer_5_out, or_8_out, or_3_out);
  or or_25 (or_25_out, buffer_5_out, or_8_out, or_4_out);
  nor nor_61 (nor_61_out, buffer_1_out, or_22_out);
  nor nor_62 (nor_62_out, nor_61_out, or_22_out);
  nor nor_63 (nor_63_out, buffer_1_out, or_23_out);
  nor nor_64 (nor_64_out, nor_63_out, or_23_out);
  nor nor_65 (nor_65_out, buffer_1_out, or_24_out);
  nor nor_66 (nor_66_out, nor_65_out, or_24_out);
  nor nor_67 (nor_67_out, buffer_1_out, or_25_out);
  nor nor_68 (nor_68_out, nor_67_out, or_25_out);
  nor nor_69 (nor_69_out, nor_61_out, nor_70_out);
  nor nor_70 (nor_70_out, nor_69_out, nor_62_out);
  nor nor_71 (nor_71_out, nor_63_out, nor_72_out);
  nor nor_72 (nor_72_out, nor_71_out, nor_64_out);
  nor nor_73 (nor_73_out, nor_65_out, nor_74_out);
  nor nor_74 (nor_74_out, nor_73_out, nor_66_out);
  nor nor_75 (nor_75_out, nor_67_out, nor_76_out);
  nor nor_76 (nor_76_out, nor_75_out, nor_68_out);
  nor nor_77 (nor_77_out, buffer_9_out, nor_70_out, or_8_out, or_1_out);
  nor nor_78 (nor_78_out, buffer_9_out, nor_72_out, or_8_out, or_2_out);
  nor nor_79 (nor_79_out, buffer_9_out, nor_74_out, or_8_out, or_3_out);
  nor nor_80 (nor_80_out, buffer_9_out, nor_76_out, or_8_out, or_4_out);
  or or_26 (or_26_out, nor_77_out, nor_57_out, nor_37_out, nor_17_out);
  or or_27 (or_27_out, nor_78_out, nor_58_out, nor_38_out, nor_18_out);
  or or_28 (or_28_out, nor_79_out, nor_59_out, nor_39_out, nor_19_out);
  or or_29 (or_29_out, nor_80_out, nor_60_out, nor_40_out, nor_20_out);
  or or_30 (out_7, or_29_out, or_28_out, or_27_out, or_26_out);
endmodule
