// Logisim project DFlipFlop.circ as structural Verilog: 1 circuit, main circuit main
module main (
  input  DATA,
  input  DATA_2,
  input  WRITE,
  input  WRITE_2,
  input  Y_SEL,
  input  Y_SEL_2,
  input  X_SEL,
  input  X_SEL_2,
  output out_9,
  output out_10
);

  wire nor_1_out, nor_2_out, nor_3_out, nor_4_out, nor_6_out, nor_7_out, nor_8_out, nor_9_out, not_1_out,
       not_2_out, or_1_out, or_2_out;

  not not_1 (not_1_out, WRITE);
  or or_1 (or_1_out, not_1_out, Y_SEL, X_SEL);
  nor nor_1 (nor_1_out, DATA, or_1_out);
  nor nor_2 (nor_2_out, nor_1_out, or_1_out);
  nor nor_3 (nor_3_out, nor_1_out, nor_4_out);
  nor nor_4 (nor_4_out, nor_3_out, nor_2_out);
  nor nor_5 (out_10, WRITE, nor_4_out, Y_SEL, X_SEL);
  not not_2 (not_2_out, WRITE_2);
  or or_2 (or_2_out, not_2_out, Y_SEL_2, X_SEL_2);
  nor nor_6 (nor_6_out, DATA_2, or_2_out);
  nor nor_7 (nor_7_out, nor_6_out, or_2_out);
  nor nor_8 (nor_8_out, nor_6_out, nor_9_out);
  buf buffer_1 (out_9, nor_8_out);
  nor nor_9 (nor_9_out, nor_8_out, nor_7_out);

  // Notes on the sheet:
  //   SCRATCH REGISTER D FLIP FLOP
  //   OUTPUT REGISTER D FLIP FLOP
endmodule
