// Logisim project UE14500_Full_Gates_v8_buff.circ as structural Verilog: 1 circuit, main circuit main
module main (
  input  _4_I3,
  input  _5_I2,
  input  _6_I1,
  input  _7_I0,
  input  RST,
  input  DATA,
  output DATA_2,
  output DATA_3,
  output CLK_2,
  output CLK_2_2,
  output CLK_1,
  output out_12,
  output IEN,
  output OEN,
  output _2_WRITE,
  output out_16,
  output _15_RR,
  output CAR,
  output out_19,
  output RR,
  output out_21,
  output SKIP,
  output _10_FLG0,
  output _12_JMP,
  output _11_RTN,
  output _9_FLGF
);

  wire buffer_1_out, buffer_2_out, buffer_3_out, buffer_4_out, buffer_5_out, buffer_7_out, buffer_8_out,
       buffer_9_out, buffer_10_out, buffer_11_out, buffer_12_out, buffer_13_out, buffer_14_out,
       buffer_16_out, buffer_17_out, buffer_18_out, buffer_19_out, buffer_20_out, buffer_21_out,
       buffer_22_out, buffer_23_out, buffer_24_out, buffer_25_out, buffer_26_out, buffer_29_out,
       buffer_30_out, buffer_31_out, buffer_32_out, buffer_33_out, buffer_36_out, buffer_37_out,
       buffer_39_out, nand_1_out, nand_2_out, nand_3_out, nand_4_out, nand_5_out, nand_6_out, nand_7_out,
       nand_8_out, nand_9_out, nand_10_out, nand_11_out, nand_12_out, nand_13_out, nand_14_out, nand_15_out,
       nand_16_out, nor_1_out, nor_2_out, nor_3_out, nor_4_out, nor_5_out, nor_6_out, nor_7_out, nor_8_out,
       nor_9_out, nor_10_out, nor_11_out, nor_12_out, nor_13_out, nor_14_out, nor_15_out, nor_16_out,
       nor_18_out, nor_20_out, nor_22_out, nor_24_out, nor_25_out, nor_26_out, nor_27_out, nor_28_out,
       nor_29_out, nor_30_out, nor_31_out, nor_32_out, nor_33_out, nor_34_out, nor_35_out, nor_36_out,
       nor_37_out, nor_38_out, nor_39_out, nor_40_out, nor_41_out, nor_42_out, nor_43_out, nor_44_out,
       nor_45_out, nor_46_out, nor_47_out, nor_48_out, nor_49_out, nor_50_out, nor_52_out, nor_53_out,
       nor_54_out, nor_55_out, nor_56_out, nor_57_out, nor_58_out, nor_59_out, nor_60_out, nor_61_out,
       nor_62_out, nor_63_out, nor_64_out, nor_65_out, nor_66_out, nor_67_out, nor_68_out, nor_69_out,
       nor_70_out, nor_71_out, nor_72_out, nor_73_out, nor_74_out, nor_75_out, nor_76_out, nor_77_out,
       nor_78_out, nor_79_out, nor_80_out, nor_81_out, nor_83_out, nor_84_out, nor_85_out, nor_86_out,
       nor_87_out, nor_89_out, not_1_out, not_2_out, not_3_out, not_4_out, not_5_out, not_6_out, not_7_out,
       not_8_out, not_9_out, not_10_out, not_11_out, not_12_out, not_13_out, not_14_out, not_15_out,
       not_16_out, not_17_out, not_18_out, or_1_out, or_2_out, or_3_out, or_4_out, or_5_out, or_6_out,
       or_7_out, or_8_out, or_9_out, or_10_out, or_11_out, or_12_out, or_13_out, or_14_out, or_15_out,
       or_16_out, or_17_out, or_18_out, or_19_out, or_20_out, or_21_out, or_23_out, or_24_out, or_25_out,
       or_26_out, or_27_out;

  or or_1 (or_1_out, _7_I0, buffer_39_out);
  or or_2 (or_2_out, _6_I1, buffer_39_out);
  or or_3 (or_3_out, _5_I2, buffer_39_out);
  or or_4 (or_4_out, buffer_39_out, _4_I3);
  buf buffer_1 (buffer_1_out, or_1_out);
  buf buffer_2 (buffer_2_out, or_2_out);
  buf buffer_3 (buffer_3_out, or_3_out);
  buf buffer_4 (buffer_4_out, or_4_out);
  buf buffer_5 (buffer_5_out, not_1_out);
  not not_1 (not_1_out, CLK_1);
  buf buffer_6 (buffer_5_out, not_1_out);
  nor nor_1 (nor_1_out, nor_4_out, nor_2_out);
  nor nor_2 (nor_2_out, nor_1_out, buffer_5_out);
  nor nor_3 (nor_3_out, nor_2_out, buffer_5_out, nor_4_out);
  nor nor_4 (nor_4_out, nor_3_out, buffer_1_out);
  nor nor_5 (nor_5_out, nor_8_out, nor_6_out);
  nor nor_6 (nor_6_out, nor_5_out, buffer_5_out);
  nor nor_7 (nor_7_out, nor_6_out, buffer_5_out, nor_8_out);
  nor nor_8 (nor_8_out, nor_7_out, buffer_2_out);
  nor nor_9 (nor_9_out, nor_12_out, nor_10_out);
  nor nor_10 (nor_10_out, nor_9_out, buffer_5_out);
  nor nor_11 (nor_11_out, nor_10_out, buffer_5_out, nor_12_out);
  nor nor_12 (nor_12_out, nor_11_out, buffer_3_out);
  nor nor_13 (nor_13_out, nor_16_out, nor_14_out);
  nor nor_14 (nor_14_out, nor_13_out, buffer_5_out);
  nor nor_15 (nor_15_out, nor_14_out, buffer_5_out, nor_16_out);
  nor nor_16 (nor_16_out, nor_15_out, buffer_4_out);
  or or_5 (or_5_out, RST, nor_2_out);
  nor nor_17 (out_12, or_5_out, nor_18_out);
  nor nor_18 (nor_18_out, out_12, nor_3_out);
  or or_6 (or_6_out, RST, nor_6_out);
  nor nor_19 (out_16, or_6_out, nor_20_out);
  nor nor_20 (nor_20_out, out_16, nor_7_out);
  or or_7 (or_7_out, RST, nor_10_out);
  nor nor_21 (out_19, or_7_out, nor_22_out);
  nor nor_22 (nor_22_out, out_19, nor_11_out);
  or or_8 (or_8_out, RST, nor_14_out);
  nor nor_23 (out_21, or_8_out, nor_24_out);
  nor nor_24 (nor_24_out, out_21, nor_15_out);
  buf buffer_7 (buffer_7_out, out_12);
  buf buffer_8 (buffer_8_out, nor_18_out);
  buf buffer_9 (buffer_9_out, out_16);
  buf buffer_10 (buffer_10_out, nor_20_out);
  buf buffer_11 (buffer_11_out, out_19);
  buf buffer_12 (buffer_12_out, nor_22_out);
  buf buffer_13 (buffer_13_out, out_21);
  buf buffer_14 (buffer_14_out, nor_24_out);
  buf buffer_15 (_10_FLG0, nor_25_out);
  nor nor_25 (nor_25_out, buffer_7_out, buffer_9_out, buffer_11_out, buffer_13_out);
  nor nor_26 (nor_26_out, buffer_8_out, buffer_9_out, buffer_11_out, buffer_13_out);
  buf buffer_16 (buffer_16_out, nor_26_out);
  nor nor_27 (nor_27_out, buffer_7_out, buffer_10_out, buffer_11_out, buffer_13_out);
  buf buffer_17 (buffer_17_out, nor_27_out);
  buf buffer_18 (buffer_18_out, nor_28_out);
  nor nor_28 (nor_28_out, buffer_8_out, buffer_10_out, buffer_11_out, buffer_13_out);
  buf buffer_19 (buffer_19_out, nor_29_out);
  nor nor_29 (nor_29_out, buffer_7_out, buffer_9_out, buffer_12_out, buffer_13_out);
  buf buffer_20 (buffer_20_out, nor_30_out);
  nor nor_30 (nor_30_out, buffer_8_out, buffer_9_out, buffer_12_out, buffer_13_out);
  buf buffer_21 (buffer_21_out, nor_31_out);
  nor nor_31 (nor_31_out, buffer_7_out, buffer_10_out, buffer_12_out, buffer_13_out);
  nor nor_32 (nor_32_out, buffer_8_out, buffer_10_out, buffer_12_out, buffer_13_out);
  buf buffer_22 (buffer_22_out, nor_32_out);
  buf buffer_23 (buffer_23_out, nor_33_out);
  nor nor_33 (nor_33_out, buffer_7_out, buffer_9_out, buffer_11_out, buffer_14_out);
  nor nor_34 (nor_34_out, buffer_8_out, buffer_9_out, buffer_11_out, buffer_14_out);
  buf buffer_24 (buffer_24_out, nor_34_out);
  buf buffer_25 (buffer_25_out, nor_35_out);
  nor nor_35 (nor_35_out, buffer_7_out, buffer_10_out, buffer_11_out, buffer_14_out);
  nor nor_36 (nor_36_out, buffer_8_out, buffer_10_out, buffer_11_out, buffer_14_out);
  buf buffer_26 (buffer_26_out, nor_36_out);
  nor nor_37 (nor_37_out, buffer_7_out, buffer_9_out, buffer_12_out, buffer_14_out);
  buf buffer_27 (_12_JMP, nor_37_out);
  buf buffer_28 (_11_RTN, nor_38_out);
  nor nor_38 (nor_38_out, buffer_8_out, buffer_9_out, buffer_12_out, buffer_14_out);
  nor nor_39 (nor_39_out, buffer_7_out, buffer_10_out, buffer_12_out, buffer_14_out);
  buf buffer_29 (buffer_29_out, nor_39_out);
  buf buffer_30 (buffer_30_out, nor_40_out);
  nor nor_40 (nor_40_out, buffer_8_out, buffer_10_out, buffer_12_out, buffer_14_out);
  nand nand_1 (nand_1_out, buffer_25_out, CLK_2);
  nor nor_41 (nor_41_out, nor_44_out, nor_42_out);
  nor nor_42 (nor_42_out, nor_41_out, nand_1_out);
  nor nor_43 (nor_43_out, nor_42_out, nand_1_out, nor_44_out);
  nor nor_44 (nor_44_out, nor_43_out, DATA_2);
  nor nor_45 (nor_45_out, buffer_32_out, buffer_18_out);
  not not_2 (not_2_out, buffer_32_out);
  or or_9 (or_9_out, RST, nor_42_out);
  nor nor_46 (nor_46_out, buffer_32_out, nor_45_out);
  or or_10 (or_10_out, nor_46_out, nor_47_out);
  nor nor_47 (nor_47_out, nor_45_out, buffer_18_out);
  nand nand_2 (nand_2_out, buffer_32_out, buffer_16_out);
  nor nor_48 (nor_48_out, buffer_20_out, buffer_32_out, RR);
  nor nor_49 (nor_49_out, buffer_20_out, buffer_32_out, RR);
  nor nor_50 (nor_50_out, buffer_21_out, not_2_out, buffer_36_out);
  or or_11 (or_11_out, buffer_20_out, buffer_21_out, buffer_22_out);
  nand nand_3 (nand_3_out, DATA_2, IEN);
  nor nor_51 (IEN, or_9_out, nor_52_out);
  nor nor_52 (nor_52_out, IEN, nor_43_out);
  buf buffer_31 (buffer_31_out, or_10_out);
  not not_3 (not_3_out, nand_2_out);
  nor nor_53 (nor_53_out, nor_48_out, nor_49_out, nor_50_out);
  not not_4 (not_4_out, nand_3_out);
  buf buffer_32 (buffer_32_out, not_4_out);
  nor nor_54 (nor_54_out, RR, buffer_31_out);
  nand nand_4 (nand_4_out, RR, buffer_31_out);
  nor nor_55 (nor_55_out, not_6_out, nor_54_out);
  nor nor_56 (nor_56_out, nor_55_out, CAR);
  nand nand_5 (nand_5_out, nor_59_out, or_12_out);
  or or_12 (or_12_out, buffer_18_out, buffer_17_out);
  or or_13 (or_13_out, not_3_out, buffer_19_out);
  not not_5 (not_5_out, nand_6_out);
  nand nand_6 (nand_6_out, nor_53_out, or_11_out);
  or or_14 (or_14_out, buffer_20_out, buffer_21_out, buffer_22_out);
  or or_15 (or_15_out, buffer_16_out, buffer_18_out, buffer_17_out);
  nand nand_7 (nand_7_out, CLK_2, or_16_out);
  or or_16 (or_16_out, buffer_17_out, buffer_18_out, buffer_19_out);
  not not_6 (not_6_out, nand_4_out);
  nand nand_8 (nand_8_out, nor_55_out, CAR);
  not not_7 (not_7_out, nand_5_out);
  nor nor_57 (nor_57_out, or_17_out, nor_58_out);
  nor nor_58 (nor_58_out, or_17_out, RR);
  or or_17 (or_17_out, or_14_out, or_15_out);
  Clock u_CLK_1 (.out(CLK_1));
  buf buffer_33 (buffer_33_out, nand_7_out);
  not not_8 (not_8_out, buffer_33_out);
  or or_18 (or_18_out, not_6_out, not_9_out);
  not not_9 (not_9_out, nand_8_out);
  nor nor_59 (nor_59_out, not_9_out, nor_56_out);
  or or_19 (or_19_out, not_7_out, or_13_out, not_5_out, nor_57_out);
  not not_10 (not_10_out, CLK_2);
  Clock u_CLK_2 (.out(CLK_2));
  nor nor_60 (nor_60_out, nor_67_out, buffer_33_out);
  nor nor_61 (nor_61_out, nor_60_out, buffer_33_out);
  nor nor_62 (nor_62_out, buffer_19_out, or_18_out);
  nor nor_63 (nor_63_out, or_19_out, not_10_out);
  nor nor_64 (nor_64_out, nor_63_out, not_10_out);
  nor nor_65 (nor_65_out, nor_60_out, nor_66_out);
  nor nor_66 (nor_66_out, nor_65_out, nor_61_out);
  nor nor_67 (nor_67_out, buffer_19_out, nor_62_out);
  nor nor_68 (nor_68_out, nor_63_out, nor_69_out);
  nor nor_69 (nor_69_out, nor_68_out, nor_64_out);
  or or_20 (or_20_out, _11_RTN, buffer_36_out);
  or or_21 (or_21_out, buffer_29_out, _11_RTN);
  nor nor_70 (nor_70_out, nor_65_out, not_8_out);
  nor nor_71 (nor_71_out, nor_70_out, not_8_out);
  nor nor_72 (nor_72_out, nor_68_out, CLK_2);
  nor nor_73 (nor_73_out, nor_72_out, CLK_2);
  not not_11 (not_11_out, nand_9_out);
  nand nand_9 (nand_9_out, or_20_out, or_21_out, nor_83_out);
  not not_12 (not_12_out, nand_10_out);
  nand nand_10 (nand_10_out, RR, buffer_23_out);
  nor nor_74 (nor_74_out, nor_70_out, nor_75_out);
  nor nor_75 (nor_75_out, nor_74_out, nor_71_out);
  buf buffer_34 (CAR, nor_74_out);
  buf buffer_35 (RR, nor_76_out);
  nor nor_76 (nor_76_out, nor_72_out, nor_77_out);
  buf buffer_36 (buffer_36_out, nor_77_out);
  nor nor_77 (nor_77_out, nor_76_out, nor_73_out);
  nor nor_78 (nor_78_out, nor_81_out, nor_79_out);
  not not_13 (not_13_out, CLK_2);
  nor nor_79 (nor_79_out, nor_78_out, not_13_out);
  nor nor_80 (nor_80_out, nor_79_out, not_13_out, nor_81_out);
  nor nor_81 (nor_81_out, nor_80_out, not_11_out);
  or or_22 (DATA_2, DATA, buffer_37_out);
  buf buffer_37 (buffer_37_out, or_23_out);
  or or_23 (or_23_out, not_12_out, not_14_out);
  not not_14 (not_14_out, nand_11_out);
  nand nand_11 (nand_11_out, buffer_36_out, buffer_24_out);
  buf buffer_38 (_15_RR, RR);
  or or_24 (or_24_out, RST, nor_79_out);
  nand nand_12 (nand_12_out, buffer_26_out, CLK_2);
  nor nor_82 (SKIP, or_24_out, nor_83_out);
  nor nor_83 (nor_83_out, SKIP, nor_80_out);
  buf buffer_39 (buffer_39_out, SKIP);
  nor nor_84 (nor_84_out, nor_87_out, nor_85_out);
  nor nor_85 (nor_85_out, nor_84_out, nand_12_out);
  nor nor_86 (nor_86_out, nor_85_out, nand_12_out, nor_87_out);
  nor nor_87 (nor_87_out, nor_86_out, DATA_2);
  not not_15 (not_15_out, nand_13_out);
  nand nand_13 (nand_13_out, buffer_39_out, buffer_30_out);
  or or_25 (or_25_out, RST, nor_85_out);
  nor nor_88 (OEN, or_25_out, nor_89_out);
  nor nor_89 (nor_89_out, OEN, nor_86_out);
  not not_16 (not_16_out, nand_14_out);
  or or_26 (or_26_out, not_16_out, not_15_out);
  nand nand_14 (nand_14_out, or_26_out, buffer_30_out);
  nand nand_15 (nand_15_out, nand_14_out, buffer_30_out);
  or or_27 (or_27_out, buffer_24_out, buffer_23_out);
  not not_17 (not_17_out, nand_15_out);
  not not_18 (not_18_out, nand_16_out);
  nand nand_16 (nand_16_out, CLK_1, OEN, or_27_out);
  buf buffer_40 (_2_WRITE, not_18_out);
  buf buffer_41 (_9_FLGF, not_17_out);

  assign CLK_2_2 = CLK_2;
  assign DATA_3 = DATA_2;

  // Notes on the sheet:
  //   0000: NOP
  //   0001: LD
  //   0010: ADD
  //   0011: SUB
  //   0100: ONE
  //   0101: NAND
  //   0110: OR
  //   0111: XOR
  //   1000: STO
  //   1001: STOC
  //   1010: IEN
  //   1011: OEN
  //   1100: JMP
  //   1101: RTN
  //   1110: SKZ
  //   1111: NOP
endmodule
