// Logisim project UERAM_4Cells.circ as structural Verilog: 1 circuit, main circuit main
module main (
  input  DATA,
  input  WRT,
  input  X0,
  input  Y0,
  output out_5
);

  wire nor_1_out, nor_2_out, nor_3_out, nor_4_out, nor_5_out, nor_6_out, nor_7_out, nor_8_out, nor_9_out,
       nor_10_out, nor_11_out, nor_12_out, nor_13_out, nor_14_out, nor_15_out, nor_16_out, nor_17_out,
       nor_18_out, nor_19_out, nor_20_out, not_1_out, not_2_out, not_3_out, or_1_out, or_2_out, or_3_out,
       or_4_out;

  not not_1 (not_1_out, WRT);
  not not_2 (not_2_out, X0);
  nor nor_1 (nor_1_out, DATA, or_1_out);
  nor nor_2 (nor_2_out, nor_1_out, or_1_out);
  or or_1 (or_1_out, not_1_out, X0, Y0);
  nor nor_3 (nor_3_out, DATA, or_2_out);
  nor nor_4 (nor_4_out, nor_3_out, or_2_out);
  or or_2 (or_2_out, not_1_out, not_2_out, Y0);
  nor nor_5 (nor_5_out, nor_1_out, nor_6_out);
  nor nor_6 (nor_6_out, nor_5_out, nor_2_out);
  nor nor_7 (nor_7_out, nor_3_out, nor_8_out);
  nor nor_8 (nor_8_out, nor_7_out, nor_4_out);
  nor nor_9 (nor_9_out, WRT, nor_6_out, X0, Y0);
  nor nor_10 (nor_10_out, WRT, nor_8_out, not_2_out, Y0);
  not not_3 (not_3_out, Y0);
  or or_3 (or_3_out, not_1_out, X0, not_3_out);
  or or_4 (or_4_out, not_1_out, not_2_out, not_3_out);
  nor nor_11 (nor_11_out, DATA, or_3_out);
  nor nor_12 (nor_12_out, nor_11_out, or_3_out);
  nor nor_13 (nor_13_out, DATA, or_4_out);
  nor nor_14 (nor_14_out, nor_13_out, or_4_out);
  nor nor_15 (nor_15_out, nor_11_out, nor_16_out);
  nor nor_16 (nor_16_out, nor_15_out, nor_12_out);
  nor nor_17 (nor_17_out, nor_13_out, nor_18_out);
  nor nor_18 (nor_18_out, nor_17_out, nor_14_out);
  nor nor_19 (nor_19_out, WRT, nor_16_out, X0, not_3_out);
  nor nor_20 (nor_20_out, WRT, nor_18_out, not_2_out, not_3_out);
  or or_5 (out_5, nor_19_out, nor_9_out, nor_20_out, nor_10_out);
endmodule
