// Logisim project UE14500_ALU_Alternate.circ as structural Verilog: 1 circuit, main circuit main
module main (
  input  CLK,
  input  RST_BAR,
  input  DATA,
  input  ALU_EN,
  input  CLEAR_CARRY,
  input  SUB,
  input  ARITH_EN,
  input  LD,
  input  BITOP0,
  input  BITOP1,
  input  LOGIC_EN,
  output CARRY,
  output RR,
  output RR_BAR
);

  wire and_1_out, and_2_out, and_3_out, nand_1_out, nand_2_out, nand_3_out, nand_4_out, nand_5_out,
       nand_6_out, nand_7_out, nand_8_out, nand_9_out, nand_10_out, nand_11_out, nand_12_out, nand_13_out,
       nand_14_out, nand_15_out, nand_16_out, nand_17_out, nand_18_out, nand_19_out, nand_20_out,
       nand_21_out, nand_22_out, nand_23_out, nand_24_out, nand_25_out, nand_26_out, nand_27_out,
       nand_29_out, not_1_out, not_2_out, not_3_out, not_4_out, or_1_out, xor_1_out;

  or or_1 (or_1_out, CLEAR_CARRY, ARITH_EN);
  and and_1 (and_1_out, CLK, ALU_EN);
  nand nand_1 (nand_1_out, RR, CARRY);
  xor xor_1 (xor_1_out, DATA, SUB);
  nand nand_2 (nand_2_out, DATA, LD);
  nand nand_3 (nand_3_out, RR, nand_1_out);
  nand nand_4 (nand_4_out, nand_1_out, CARRY);
  not not_1 (not_1_out, DATA);
  nand nand_5 (nand_5_out, nand_3_out, nand_4_out);
  nand nand_6 (nand_6_out, nand_5_out, xor_1_out);
  nand nand_7 (nand_7_out, DATA, RR, BITOP0);
  nand nand_8 (nand_8_out, not_1_out, RR_BAR, BITOP1);
  nand nand_9 (nand_9_out, nand_5_out, nand_6_out);
  nand nand_10 (nand_10_out, nand_6_out, xor_1_out);
  nand nand_11 (nand_11_out, nand_9_out, nand_10_out);
  nand nand_12 (nand_12_out, nand_6_out, nand_1_out);
  nand nand_13 (nand_13_out, nand_7_out, nand_8_out, LOGIC_EN);
  not not_2 (not_2_out, CLEAR_CARRY);
  nand nand_14 (nand_14_out, nand_11_out, ARITH_EN);
  and and_2 (and_2_out, nand_12_out, not_2_out);
  nand nand_15 (nand_15_out, nand_14_out, nand_2_out, nand_13_out);
  and and_3 (and_3_out, or_1_out, and_1_out);
  nand nand_16 (nand_16_out, and_2_out, and_3_out);
  nand nand_17 (nand_17_out, nand_16_out, and_3_out);
  nand nand_18 (nand_18_out, nand_15_out, and_1_out);
  nand nand_19 (nand_19_out, nand_18_out, and_1_out);
  nand nand_20 (nand_20_out, nand_16_out, nand_21_out);
  nand nand_21 (nand_21_out, nand_20_out, nand_17_out, RST_BAR);
  not not_3 (not_3_out, and_3_out);
  nand nand_22 (nand_22_out, nand_18_out, nand_23_out);
  nand nand_23 (nand_23_out, nand_22_out, nand_19_out, RST_BAR);
  not not_4 (not_4_out, and_1_out);
  nand nand_24 (nand_24_out, nand_20_out, not_3_out);
  nand nand_25 (nand_25_out, nand_24_out, not_3_out);
  nand nand_26 (nand_26_out, nand_22_out, not_4_out);
  nand nand_27 (nand_27_out, nand_26_out, not_4_out);
  nand nand_28 (CARRY, nand_24_out, nand_29_out);
  nand nand_29 (nand_29_out, CARRY, nand_25_out, RST_BAR);
  nand nand_30 (RR, nand_26_out, RR_BAR);
  nand nand_31 (RR_BAR, RR, nand_27_out, RST_BAR);
endmodule
