// Logisim project 3-bitCounter.circ as structural Verilog: 1 circuit, main circuit main
module main (
  input  in_1,
  output out_2,
  output out_3,
  output out_4,
  output out_5,
  output out_6,
  output out_7,
  output out_8,
  output out_9,
  output out_10,
  output out_11,
  output out_12
);

  wire clock_1_out, nor_1_out, nor_2_out, nor_3_out, nor_4_out, nor_5_out, nor_6_out, nor_7_out, nor_8_out,
       nor_9_out, nor_10_out, nor_11_out, nor_12_out, nor_13_out, nor_14_out, nor_15_out, nor_16_out,
       nor_17_out, nor_18_out, nor_20_out, nor_22_out, nor_24_out, not_1_out, or_1_out, or_2_out, or_3_out,
       or_4_out, or_5_out, or_6_out;

  Clock clock_1 (.out(clock_1_out));
  not not_1 (not_1_out, clock_1_out);
  nor nor_1 (nor_1_out, nor_20_out, not_1_out);
  nor nor_2 (nor_2_out, nor_1_out, not_1_out);
  nor nor_3 (nor_3_out, nor_22_out, nor_20_out);
  nor nor_4 (nor_4_out, nor_3_out, nor_20_out);
  nor nor_5 (nor_5_out, nor_24_out, nor_22_out);
  nor nor_6 (nor_6_out, nor_5_out, nor_22_out);
  nor nor_7 (nor_7_out, or_1_out, nor_8_out);
  or or_1 (or_1_out, in_1, nor_1_out);
  nor nor_8 (nor_8_out, nor_7_out, nor_2_out);
  nor nor_9 (nor_9_out, or_2_out, nor_10_out);
  or or_2 (or_2_out, in_1, nor_3_out);
  nor nor_10 (nor_10_out, nor_9_out, nor_4_out);
  nor nor_11 (nor_11_out, or_3_out, nor_12_out);
  or or_3 (or_3_out, in_1, nor_5_out);
  nor nor_12 (nor_12_out, nor_11_out, nor_6_out);
  nor nor_13 (nor_13_out, nor_7_out, clock_1_out);
  nor nor_14 (nor_14_out, nor_13_out, clock_1_out);
  nor nor_15 (nor_15_out, nor_9_out, out_2);
  nor nor_16 (nor_16_out, nor_15_out, out_2);
  nor nor_17 (nor_17_out, nor_11_out, out_5);
  nor nor_18 (nor_18_out, nor_17_out, out_5);
  or or_4 (or_4_out, in_1, nor_13_out);
  or or_5 (or_5_out, in_1, nor_15_out);
  or or_6 (or_6_out, in_1, nor_17_out);
  nor nor_19 (out_2, or_4_out, nor_20_out);
  nor nor_20 (nor_20_out, out_2, nor_14_out);
  nor nor_21 (out_5, or_5_out, nor_22_out);
  nor nor_22 (nor_22_out, out_5, nor_16_out);
  nor nor_23 (out_9, or_6_out, nor_24_out);
  nor nor_24 (nor_24_out, out_9, nor_18_out);
  nor nor_25 (out_3, out_2, out_5, out_9);
  nor nor_26 (out_4, nor_20_out, out_5, out_9);
  nor nor_27 (out_6, out_9, nor_22_out, out_2);
  nor nor_28 (out_7, nor_20_out, nor_22_out, out_9);
  nor nor_29 (out_8, out_2, out_5, nor_24_out);
  nor nor_30 (out_10, nor_20_out, out_5, nor_24_out);
  nor nor_31 (out_11, out_2, nor_22_out, nor_24_out);
  nor nor_32 (out_12, nor_20_out, nor_22_out, nor_24_out);
endmodule
