// Logisim project RAM.circ as structural Verilog: 1 circuit, main circuit main
module main (
  input  A2,
  input  A1,
  input  A0,
  input  DAT,
  input  WRT,
  input  IRR,
  input  E3,
  input  E2,
  input  E1,
  output DBUS,
  output DBUS_2,
  output DBUS_3
);

  wire nor_1_out, nor_2_out, nor_3_out, nor_4_out, nor_5_out, nor_6_out, nor_7_out, nor_8_out, nor_9_out,
       nor_10_out, nor_11_out, nor_12_out, nor_13_out, nor_14_out, nor_15_out, nor_16_out, nor_17_out,
       nor_18_out, nor_19_out, nor_20_out, nor_21_out, nor_22_out, nor_23_out, nor_24_out, nor_25_out,
       not_1_out, not_2_out, not_3_out, or_1_out, or_2_out, or_3_out, or_4_out, or_5_out;

  not not_1 (not_1_out, A0);
  not not_2 (not_2_out, A1);
  or or_1 (or_1_out, not_3_out, A0, A1);
  or or_2 (or_2_out, not_3_out, not_1_out, A1);
  nor nor_1 (nor_1_out, nor_2_out, nor_3_out);
  nor nor_2 (nor_2_out, DAT, or_1_out);
  nor nor_3 (nor_3_out, nor_1_out, nor_4_out);
  nor nor_4 (nor_4_out, nor_2_out, or_1_out);
  nor nor_5 (nor_5_out, nor_6_out, nor_8_out);
  nor nor_6 (nor_6_out, DAT, or_2_out);
  nor nor_7 (nor_7_out, nor_6_out, or_2_out);
  nor nor_8 (nor_8_out, nor_5_out, nor_7_out);
  nor nor_9 (nor_9_out, A1, A0, E3);
  not not_3 (not_3_out, WRT);
  nor nor_10 (nor_10_out, WRT, nor_3_out, A0, A1);
  nor nor_11 (nor_11_out, WRT, nor_8_out, not_1_out, A1);
  nor nor_12 (nor_12_out, A1, not_1_out, E2);
  nor nor_13 (nor_13_out, DAT, or_3_out);
  nor nor_14 (nor_14_out, nor_13_out, or_3_out);
  or or_3 (or_3_out, not_3_out, A0, not_2_out);
  nor nor_15 (nor_15_out, DAT, or_4_out);
  nor nor_16 (nor_16_out, nor_15_out, or_4_out);
  or or_4 (or_4_out, not_3_out, not_1_out, not_2_out);
  nor nor_17 (nor_17_out, not_2_out, A0, E1);
  nor nor_18 (nor_18_out, nor_13_out, nor_19_out);
  nor nor_19 (nor_19_out, nor_18_out, nor_14_out);
  nor nor_20 (nor_20_out, nor_15_out, nor_21_out);
  nor nor_21 (nor_21_out, nor_20_out, nor_16_out);
  nor nor_22 (nor_22_out, WRT, nor_19_out, A0, not_2_out);
  nor nor_23 (nor_23_out, WRT, nor_21_out, not_1_out, not_2_out);
  nor nor_24 (nor_24_out, not_2_out, not_1_out, IRR);
  or or_5 (or_5_out, nor_24_out, nor_17_out, nor_12_out, nor_9_out);
  nor nor_25 (nor_25_out, nor_22_out, nor_10_out, nor_23_out, nor_11_out);
  and and_1 (DBUS_2, A2, or_5_out);
  nor nor_26 (DBUS, A2, nor_25_out);

  assign DBUS_3 = DAT;
endmodule
