// Logisim project DiodeRom.circ as structural Verilog: 1 circuit, main circuit main
module main (
  input  in_1,
  input  in_2,
  input  in_3,
  input  in_4,
  input  in_5,
  input  in_6,
  input  in_7,
  input  in_8,
  output A1,
  output A0,
  output I2,
  output I1,
  output I0,
  output DATA
);

  or or_1 (A1, in_1, in_1);
  or or_2 (A1, in_2, in_2);
  or or_3 (A1, in_3, in_3);
  // OR_Gate or_4 has open pins: in0=in_4, in1=in_4, out=open
  // OR_Gate or_5 has open pins: in0=in_5, in1=in_5, out=open
  // OR_Gate or_6 has open pins: in0=in_6, in1=in_6, out=open
  // OR_Gate or_7 has open pins: in0=in_7, in1=in_7, out=open
  // OR_Gate or_8 has open pins: in0=in_8, in1=in_8, out=open
  // OR_Gate or_9 has open pins: in0=in_1, in1=in_1, out=open
  // OR_Gate or_10 has open pins: in0=in_1, in1=in_1, out=open
  or or_11 (A0, in_2, in_2);
  or or_12 (I2, in_2, in_2);
  or or_13 (I2, in_3, in_3);
  or or_14 (A0, in_3, in_3);
  // OR_Gate or_15 has open pins: in0=in_4, in1=in_4, out=open
  // OR_Gate or_16 has open pins: in0=in_4, in1=in_4, out=open
  // OR_Gate or_17 has open pins: in0=in_5, in1=in_5, out=open
  // OR_Gate or_18 has open pins: in0=in_5, in1=in_5, out=open
  // OR_Gate or_19 has open pins: in0=in_6, in1=in_6, out=open
  // OR_Gate or_20 has open pins: in0=in_6, in1=in_6, out=open
  // OR_Gate or_21 has open pins: in0=in_7, in1=in_7, out=open
  // OR_Gate or_22 has open pins: in0=in_7, in1=in_7, out=open
  // OR_Gate or_23 has open pins: in0=in_8, in1=in_8, out=open
  // OR_Gate or_24 has open pins: in0=in_8, in1=in_8, out=open
  or or_25 (I1, in_1, in_1);
  or or_26 (I0, in_1, in_1);
  or or_27 (I1, in_2, in_2);
  or or_28 (I0, in_2, in_2);
  // OR_Gate or_29 has open pins: in0=in_3, in1=in_3, out=open
  // OR_Gate or_30 has open pins: in0=in_3, in1=in_3, out=open
  // OR_Gate or_31 has open pins: in0=in_4, in1=in_4, out=open
  // OR_Gate or_32 has open pins: in0=in_4, in1=in_4, out=open
  // OR_Gate or_33 has open pins: in0=in_5, in1=in_5, out=open
  // OR_Gate or_34 has open pins: in0=in_5, in1=in_5, out=open
  // OR_Gate or_35 has open pins: in0=in_6, in1=in_6, out=open
  // OR_Gate or_36 has open pins: in0=in_6, in1=in_6, out=open
  // OR_Gate or_37 has open pins: in0=in_7, in1=in_7, out=open
  // OR_Gate or_38 has open pins: in0=in_7, in1=in_7, out=open
  // OR_Gate or_39 has open pins: in0=in_8, in1=in_8, out=open
  // OR_Gate or_40 has open pins: in0=in_8, in1=in_8, out=open
  or or_41 (DATA, in_1, in_1);
  // OR_Gate or_42 has open pins: in0=in_2, in1=in_2, out=open
  // OR_Gate or_43 has open pins: in0=in_3, in1=in_3, out=open
  // OR_Gate or_44 has open pins: in0=in_4, in1=in_4, out=open
  // OR_Gate or_45 has open pins: in0=in_5, in1=in_5, out=open
  // OR_Gate or_46 has open pins: in0=in_6, in1=in_6, out=open
  // OR_Gate or_47 has open pins: in0=in_7, in1=in_7, out=open
  // OR_Gate or_48 has open pins: in0=in_8, in1=in_8, out=open
endmodule
