// Logisim project CPU_v3.circ as structural Verilog: 1 circuit, main circuit main
module main (
  input  I2,
  input  I1,
  input  I0,
  input  DATA,
  input  A4,
  input  A3,
  input  A2,
  input  A1,
  input  A0,
  output WRT,
  output RR
);

  wire and_1_out, and_2_out, and_3_out, and_4_out, and_5_out, and_6_out, and_7_out, and_8_out, clock_1_out,
       nand_1_out, nand_2_out, nand_3_out, nor_1_out, nor_2_out, nor_3_out, nor_4_out, nor_5_out, nor_6_out,
       nor_7_out, nor_8_out, nor_9_out, nor_10_out, nor_11_out, nor_13_out, nor_14_out, not_1_out, not_2_out,
       not_3_out, not_4_out, not_5_out, not_6_out, not_7_out, not_8_out, not_9_out, not_10_out, not_11_out,
       or_1_out, or_2_out, or_3_out;

  or or_1 (or_1_out, DATA, nor_14_out);
  not not_1 (not_1_out, or_1_out);
  not not_2 (not_2_out, I1);
  nor nor_1 (nor_1_out, I0, not_2_out, I2);
  nand nand_1 (nand_1_out, I0, I1, I2);
  not not_3 (not_3_out, nand_1_out);
  nor nor_2 (nor_2_out, I0, RR, or_1_out);
  nor nor_3 (nor_3_out, I1, nor_13_out, or_1_out);
  nor nor_4 (nor_4_out, I2, RR, not_1_out);
  or or_2 (or_2_out, nor_2_out, nor_3_out, nor_4_out);
  Clock clock_1 (.out(clock_1_out));
  not not_4 (not_4_out, clock_1_out);
  nand nand_2 (nand_2_out, clock_1_out, nor_1_out);
  nor nor_5 (nor_5_out, not_3_out, or_2_out);
  not not_5 (not_5_out, nor_5_out);
  not not_6 (not_6_out, A4);
  and and_1 (and_1_out, or_1_out, not_7_out);
  and and_2 (and_2_out, not_1_out, not_7_out);
  not not_7 (not_7_out, nand_2_out);
  and and_3 (and_3_out, nor_5_out, clock_1_out);
  and and_4 (and_4_out, not_5_out, clock_1_out);
  not not_8 (not_8_out, A1);
  not not_9 (not_9_out, A2);
  not not_10 (not_10_out, A3);
  nor nor_6 (nor_6_out, and_1_out, nor_7_out);
  nor nor_7 (nor_7_out, nor_6_out, and_2_out);
  and and_5 (and_5_out, nor_8_out, not_4_out);
  nor nor_8 (nor_8_out, and_3_out, nor_9_out);
  nor nor_9 (nor_9_out, nor_8_out, and_4_out);
  and and_6 (and_6_out, nor_9_out, not_4_out);
  not not_11 (not_11_out, A0);
  and and_7 (and_7_out, nor_6_out, nand_2_out);
  nor nor_10 (nor_10_out, and_7_out, nor_11_out);
  nor nor_11 (nor_11_out, nor_10_out, and_8_out);
  and and_8 (and_8_out, nor_7_out, nand_2_out);
  nor nor_12 (RR, and_5_out, nor_13_out);
  nor nor_13 (nor_13_out, RR, and_6_out);
  or or_3 (or_3_out, A0, A1, A2, not_10_out, not_6_out);
  not not_12 (WRT, nand_3_out);
  nand nand_3 (nand_3_out, nor_10_out, not_3_out, clock_1_out);
  nor nor_14 (nor_14_out, or_3_out, nor_13_out);

  // Notes on the sheet:
  //   OPERATION
  //   000: AND
  //   001: XNOR
  //   010: OEN
  //   011: ORCD
  //   100: LD
  //   101: ORCR
  //   110: OR
  //   111: STO
  //   OEN
  //   RR
  //   RR LOOPBACK: 1 1000
  //   /RR
endmodule
