// Logisim project CompleteSystem.circ as structural Verilog: 1 circuit, main circuit main
module main (
  input  DATA,
  input  in_2,
  output out_3,
  output out_4,
  output out_5,
  output out_6,
  output out_7,
  output out_8,
  output out_9,
  output out_10,
  output WRT,
  output RR
);

  wire and_1_out, and_2_out, and_3_out, clock_1_out, d_ff_1_q, d_ff_2_q, d_ff_3_q, d_ff_4_q, nor_2_out,
       nor_3_out, nor_4_out, nor_5_out, nor_6_out, not_1_out, not_2_out, not_3_out, not_4_out, not_5_out,
       not_6_out, OEN_q, or_1_out, RR_qn;
  wire [7:0] counter_1_q;

  Clock clock_1 (.out(clock_1_out));
  D_Flip_Flop d_ff_1 (.clk(clock_1_out), .D(d_ff_4_q), .Q(d_ff_1_q), .preset(in_2));  // open: Qn, en, reset
  D_Flip_Flop d_ff_2 (.clk(clock_1_out), .D(d_ff_1_q), .Q(d_ff_2_q), .reset(in_2));  // open: Qn, preset, en
  D_Flip_Flop d_ff_3 (.clk(clock_1_out), .D(d_ff_2_q), .Q(d_ff_3_q), .reset(in_2));  // open: Qn, preset, en
  D_Flip_Flop d_ff_4 (.clk(clock_1_out), .D(d_ff_3_q), .Q(d_ff_4_q), .reset(in_2));  // open: Qn, preset, en
  not not_1 (not_1_out, out_7);
  not not_2 (not_2_out, out_6);
  and and_1 (and_1_out, not_1_out, not_2_out, not_3_out, out_4, out_3);
  not not_3 (not_3_out, out_5);
  not not_4 (not_4_out, out_3);
  not not_5 (not_5_out, DATA);
  nor nor_1 (DATA, RR_qn, and_1_out);
  nor nor_2 (nor_2_out, out_10, not_6_out, out_8);
  not not_6 (not_6_out, out_9);
  and and_2 (and_2_out, out_10, out_9, out_8);
  nor nor_3 (nor_3_out, out_10, RR, DATA);
  nor nor_4 (nor_4_out, out_9, RR_qn, DATA);
  nor nor_5 (nor_5_out, out_8, RR, not_5_out);
  Counter counter_1 (.Q(counter_1_q), .clk(d_ff_1_q), .clr(in_2));  // open: load, D, count, carry
  or or_1 (or_1_out, nor_3_out, nor_4_out, nor_5_out);
  RAM #(.addrWidth(4), .dataWidth(1), .bus("separate")) ram_1 (
    .addr({out_4, out_5, out_6, out_7}), .din(DATA), .str(d_ff_4_q), .sel(not_4_out), .ld(d_ff_2_q));  // open: data, clk, clr
  ROM rom_1 (.addr(counter_1_q), .data({out_3, out_4, out_5, out_6, out_7, out_8, out_9, out_10}));  // open: sel
  and and_3 (and_3_out, nor_2_out, d_ff_3_q);
  D_Flip_Flop u_RR (.clk(d_ff_3_q), .D(nor_6_out), .Q(RR), .Qn(RR_qn));  // open: preset, en, reset
  nor nor_6 (nor_6_out, and_2_out, or_1_out);
  D_Flip_Flop OEN (.clk(and_3_out), .D(DATA), .Q(OEN_q));  // open: Qn, preset, en, reset
  and and_4 (WRT, OEN_q, and_2_out, d_ff_3_q);

  // Notes on the sheet:
  //   OPERATION
  //   000: AND
  //   001: XNOR
  //   010: OEN
  //   011: ORCD
  //   100: LD
  //   101: ORCR
  //   110: OR
  //   111: STO
endmodule
