// Logisim project External_IO_v2.circ as structural Verilog: 1 circuit, main circuit main
module main (
  input  A4,
  input  A3,
  input  A2,
  input  A1,
  input  A0,
  input  WRT_L,
  input  DATA,
  input  E7,
  input  E6,
  input  E5,
  input  E4,
  input  E3,
  input  E2,
  input  E1,
  input  E0,
  output DATA_2,
  output O0,
  output O1,
  output O2,
  output O3,
  output O4,
  output O5,
  output O6,
  output O7
);

  wire nand_1_out, nor_1_out, nor_2_out, nor_3_out, nor_4_out, nor_5_out, nor_6_out, nor_7_out, nor_8_out,
       not_1_out, not_2_out, not_3_out, not_4_out, not_5_out, not_6_out, not_7_out, not_8_out, not_9_out,
       not_10_out, not_11_out, not_12_out, not_13_out, not_14_out, not_15_out, or_1_out, or_2_out, or_3_out,
       or_4_out, or_5_out, or_6_out, or_7_out, or_8_out, or_9_out;

  or or_1 (or_1_out, nor_8_out, nor_7_out, nor_6_out, nor_5_out, nor_4_out, nor_3_out, nor_2_out, nor_1_out);
  not not_1 (not_1_out, E7);
  not not_2 (not_2_out, E5);
  not not_3 (not_3_out, E6);
  not not_4 (not_4_out, not_5_out);
  not not_5 (not_5_out, or_1_out);
  nor nor_1 (nor_1_out, or_2_out, not_8_out, WRT_L);
  nor nor_2 (nor_2_out, or_3_out, not_10_out, WRT_L);
  nor nor_3 (nor_3_out, or_4_out, not_9_out, WRT_L);
  nor nor_4 (nor_4_out, or_5_out, not_7_out, WRT_L);
  nor nor_5 (nor_5_out, or_6_out, not_6_out, WRT_L);
  nor nor_6 (nor_6_out, or_7_out, not_2_out, WRT_L);
  nor nor_7 (nor_7_out, or_8_out, not_3_out, WRT_L);
  nor nor_8 (nor_8_out, or_9_out, not_1_out, WRT_L);
  not not_6 (not_6_out, E4);
  not not_7 (not_7_out, E3);
  buf buffer_1 (DATA_2, not_4_out);
  not not_8 (not_8_out, E0);
  not not_9 (not_9_out, E2);
  not not_10 (not_10_out, E1);
  not not_11 (not_11_out, A4);
  not not_12 (not_12_out, A3);
  not not_13 (not_13_out, A2);
  not not_14 (not_14_out, A1);
  not not_15 (not_15_out, A0);
  or or_2 (or_2_out, A0, A1, A2, A3, not_11_out);
  or or_3 (or_3_out, not_15_out, A1, A2, A3, not_11_out);
  or or_4 (or_4_out, A0, not_14_out, A2, A3, not_11_out);
  or or_5 (or_5_out, not_15_out, not_14_out, A2, A3, not_11_out);
  or or_6 (or_6_out, A0, A1, not_13_out, A3, not_11_out);
  or or_7 (or_7_out, not_15_out, A1, not_13_out, A3, not_11_out);
  or or_8 (or_8_out, A0, not_14_out, not_13_out, A3, not_11_out);
  or or_9 (or_9_out, not_15_out, not_14_out, not_13_out, A3, not_11_out);
  nand nand_1 (nand_1_out, WRT_L, DATA);
  nor nor_9 (O0, or_2_out, nand_1_out);
  nor nor_10 (O1, or_3_out, nand_1_out);
  nor nor_11 (O2, or_4_out, nand_1_out);
  nor nor_12 (O3, or_5_out, nand_1_out);
  nor nor_13 (O4, or_6_out, nand_1_out);
  nor nor_14 (O5, or_7_out, nand_1_out);
  nor nor_15 (O6, or_8_out, nand_1_out);
  nor nor_16 (O7, or_9_out, nand_1_out);
endmodule
