// Logisim project StateMachine.circ as structural Verilog: 1 circuit, main circuit main
module main (
  input  in_1,
  input  STO,
  input  RR,
  input  INITIAL,
  output TAPE,
  output WRT1,
  output UPDT,
  output DATA_BUS,
  output READ,
  output CLCK,
  output WRT2,
  output WORKING_MEMORY
);

  wire and_1_out, clock_1_out, or_1_out, or_2_out, or_3_out, STORE_q;

  Clock clock_1 (.out(clock_1_out));
  or or_1 (or_1_out, in_1, WRT2);
  D_Flip_Flop d_ff_1 (.clk(clock_1_out), .D(or_1_out), .Q(TAPE));  // open: Qn, preset, en, reset
  D_Flip_Flop d_ff_2 (.clk(clock_1_out), .D(TAPE), .Q(READ));  // open: Qn, preset, en, reset
  D_Flip_Flop d_ff_3 (.clk(clock_1_out), .D(WRT1), .Q(CLCK));  // open: Qn, preset, en, reset
  D_Flip_Flop d_ff_4 (.clk(clock_1_out), .D(READ), .Q(WRT1));  // open: Qn, preset, en, reset
  and and_1 (and_1_out, STORE_q, UPDT);
  D_Flip_Flop d_ff_5 (.clk(clock_1_out), .D(CLCK), .Q(UPDT));  // open: Qn, preset, en, reset
  D_Flip_Flop #(.trigger("falling")) STORE (.clk(CLCK), .D(STO), .Q(STORE_q));  // open: Qn, preset, en, reset
  or or_2 (or_2_out, and_1_out, READ);
  or or_3 (or_3_out, INITIAL, DATA_BUS);
  D_Flip_Flop d_ff_6 (.clk(clock_1_out), .D(UPDT), .Q(WRT2));  // open: Qn, preset, en, reset
  and and_2 (DATA_BUS, STORE_q, RR);
  D_Flip_Flop #(.trigger("falling")) WORK (
    .clk(or_2_out), .D(or_3_out), .Q(WORKING_MEMORY));  // open: Qn, preset, en, reset
  and and_3 (DATA_BUS, CLCK, WORKING_MEMORY);
endmodule
