// Logisim project CoreMemory2.circ as structural Verilog: 1 circuit, main circuit main
module main (
  input  A1,
  input  A0,
  input  WRITEBACK,
  input  WRT,
  input  DATA,
  input  START,
  output RD,
  output WT
);

  wire and_1_out, and_2_out, and_3_out, clock_1_out, controlled_buffer_1_out, controlled_buffer_3_out,
       controlled_buffer_5_out, controlled_buffer_7_out, d_ff_1_q, d_ff_2_q, d_ff_2_qn, d_ff_3_q, d_ff_3_qn,
       nor_1_out, nor_2_out, nor_3_out, nor_4_out, nor_5_out, nor_6_out, nor_7_out, nor_8_out, not_1_out,
       not_2_out, not_3_out, or_1_out, or_2_out, or_3_out, or_4_out, or_5_out, or_6_out, or_7_out, or_8_out,
       or_9_out, or_10_out, or_11_out, or_12_out, or_13_out;

  Clock clock_1 (.out(clock_1_out));
  not not_1 (not_1_out, A0);
  not not_2 (not_2_out, A1);
  and and_1 (and_1_out, START, d_ff_3_qn, d_ff_2_qn, RD);
  or or_1 (or_1_out, A0, A1);
  or or_2 (or_2_out, not_1_out, A1);
  or or_3 (or_3_out, A0, not_2_out);
  or or_4 (or_4_out, not_1_out, not_2_out);
  D_Flip_Flop d_ff_1 (.clk(clock_1_out), .D(and_1_out), .Q(d_ff_1_q), .Qn(RD));  // open: preset, en, reset
  nor nor_1 (nor_1_out, WT, or_1_out);
  nor nor_2 (nor_2_out, or_1_out, RD);
  nor nor_3 (nor_3_out, WT, or_2_out);
  nor nor_4 (nor_4_out, or_2_out, RD);
  nor nor_5 (nor_5_out, WT, or_3_out);
  nor nor_6 (nor_6_out, or_3_out, RD);
  nor nor_7 (nor_7_out, WT, or_4_out);
  nor nor_8 (nor_8_out, or_4_out, RD);
  nand nand_1 (WT, d_ff_3_q, or_7_out);
  D_Flip_Flop d_ff_2 (.clk(clock_1_out), .D(d_ff_1_q), .Q(d_ff_2_q), .Qn(d_ff_2_qn));  // open: preset, en, reset
  D_Flip_Flop d_ff_3 (.clk(clock_1_out), .D(d_ff_2_q), .Q(d_ff_3_q), .Qn(d_ff_3_qn));  // open: preset, en, reset
  or or_5 (or_5_out, nor_2_out, nor_4_out);
  assign controlled_buffer_1_out = or_5_out ? 1'b1 : 1'bz;  // Controlled_Buffer controlled_buffer_1
  or or_6 (or_6_out, nor_6_out, nor_8_out);
  assign controlled_buffer_1_out = or_6_out ? 1'b1 : 1'bz;  // Controlled_Buffer controlled_buffer_2
  or or_7 (or_7_out, and_2_out, and_3_out);
  or or_8 (or_8_out, nor_4_out, nor_8_out);
  or or_9 (or_9_out, nor_2_out, nor_6_out);
  assign controlled_buffer_3_out = or_9_out ? 1'b1 : 1'bz;  // Controlled_Buffer controlled_buffer_3
  assign controlled_buffer_3_out = or_8_out ? 1'b1 : 1'bz;  // Controlled_Buffer controlled_buffer_4
  assign controlled_buffer_5_out = or_13_out ? 1'b1 : 1'bz;  // Controlled_Buffer controlled_buffer_5
  assign controlled_buffer_5_out = or_10_out ? 1'b1 : 1'bz;  // Controlled_Buffer controlled_buffer_6
  or or_10 (or_10_out, nor_5_out, nor_1_out);
  and and_2 (and_2_out, WRITEBACK, not_3_out);
  not not_3 (not_3_out, WRT);
  and and_3 (and_3_out, WRT, DATA);
  or or_11 (or_11_out, nor_1_out, nor_3_out);
  assign controlled_buffer_7_out = or_11_out ? 1'b1 : 1'bz;  // Controlled_Buffer controlled_buffer_7
  or or_12 (or_12_out, nor_5_out, nor_7_out);
  assign controlled_buffer_7_out = or_12_out ? 1'b1 : 1'bz;  // Controlled_Buffer controlled_buffer_8
  or or_13 (or_13_out, nor_7_out, nor_3_out);
  // also tied to GND on the sheet: {controlled_buffer_1_out, controlled_buffer_3_out, controlled_buffer_5_out, controlled_buffer_7_out}
endmodule
