// Logisim project TubeSBC.circ as structural Verilog: 1 circuit, main circuit main
module main (
  input  A2,
  input  A1,
  input  A0,
  input  DATA,
  input  CLK,
  output out_6,
  output out_7,
  output out_8,
  output out_9,
  output out_10
);

  wire nor_1_out, nor_2_out, nor_3_out, nor_4_out, nor_5_out, nor_6_out, nor_7_out, nor_8_out, nor_9_out,
       nor_10_out, nor_12_out, not_1_out, not_2_out;

  not not_1 (not_1_out, DATA);
  nor nor_1 (nor_1_out, A0, out_6, DATA);
  nor nor_2 (nor_2_out, A1, nor_12_out, DATA);
  nor nor_3 (nor_3_out, A2, out_6, not_1_out);
  not not_2 (not_2_out, CLK);
  nor nor_4 (nor_4_out, nor_1_out, nor_2_out, nor_3_out);
  nor nor_5 (nor_5_out, nor_4_out, CLK);
  nor nor_6 (nor_6_out, nor_5_out, CLK);
  nor nor_7 (nor_7_out, nor_5_out, nor_8_out);
  nor nor_8 (nor_8_out, nor_7_out, nor_6_out);
  nor nor_9 (nor_9_out, nor_7_out, not_2_out);
  nor nor_10 (nor_10_out, nor_9_out, not_2_out);
  nor nor_11 (out_6, nor_9_out, nor_12_out);
  nor nor_12 (nor_12_out, out_6, nor_10_out);

  assign out_7 = A2;
  assign out_8 = A1;
  assign out_9 = A0;
  assign out_10 = DATA;

  // Notes on the sheet:
  //   000: AND
  //   001: XNOR
  //   010: NOP
  //   011: ORCD
  //   100: LD
  //   101: ORCR
  //   110: OR
  //   111: ONE
endmodule
