// Logisim project TubeSBC_v3.circ as structural Verilog: 1 circuit, main circuit main
module main (
  input  A2,
  input  A1,
  input  A0,
  input  DATA,
  input  CLK,
  output RR,
  output WRT,
  output out_8,
  output out_9,
  output out_10,
  output DBUS
);

  wire nand_1_out, nand_2_out, nand_3_out, nand_4_out, nor_1_out, nor_2_out, nor_3_out, nor_4_out, nor_5_out,
       nor_6_out, nor_7_out, nor_8_out, nor_9_out, nor_10_out, nor_11_out, nor_12_out, not_1_out, not_2_out,
       not_3_out, not_4_out, not_5_out, not_6_out;

  nand nand_1 (nand_1_out, not_3_out, RR);
  not not_1 (not_1_out, nand_1_out);
  or or_1 (DBUS, DATA, not_1_out);
  not not_2 (not_2_out, DBUS);
  nand nand_2 (nand_2_out, A0, A1, A2);
  not not_3 (not_3_out, nand_2_out);
  nor nor_1 (nor_1_out, A0, RR, DBUS);
  nor nor_2 (nor_2_out, A1, nor_12_out, DBUS);
  nor nor_3 (nor_3_out, A2, RR, not_2_out);
  not not_4 (not_4_out, not_3_out);
  nor nor_4 (nor_4_out, nor_1_out, nor_2_out, nor_3_out);
  nand nand_3 (nand_3_out, not_4_out, CLK);
  not not_5 (not_5_out, nand_3_out);
  nor nor_5 (nor_5_out, nor_6_out, nor_7_out);
  nor nor_6 (nor_6_out, nor_4_out, not_5_out);
  nor nor_7 (nor_7_out, nor_5_out, nor_8_out);
  nor nor_8 (nor_8_out, nor_6_out, not_5_out);
  nor nor_9 (nor_9_out, nor_5_out, nand_3_out);
  nor nor_10 (nor_10_out, nor_9_out, nand_3_out);
  nor nor_11 (nor_11_out, nor_9_out, nor_12_out);
  nor nor_12 (nor_12_out, nor_11_out, nor_10_out);
  buf buffer_1 (RR, nor_11_out);
  nand nand_4 (nand_4_out, RR, not_3_out, CLK);
  buf buffer_2 (WRT, not_6_out);
  not not_6 (not_6_out, nand_4_out);

  assign out_8 = A2;
  assign out_9 = A1;
  assign out_10 = A0;

  // Notes on the sheet:
  //   000: AND
  //   001: XNOR
  //   010: NOP
  //   011: ORCD
  //   100: LD
  //   101: ORCR
  //   110: OR
  //   111: STO
endmodule
