// Logisim project 5bit_ALU_RR.circ as structural Verilog: 1 circuit, main circuit main
module main (
  input  in_1,
  input  in_2,
  input  in_3,
  input  in_4,
  input  in_5,
  input  in_6,
  input  in_7,
  input  in_8,
  output out_9,
  output out_10,
  output out_11,
  output out_12,
  output out_13
);

  wire and_1_out, and_2_out, and_3_out, and_4_out, and_5_out, nor_1_out, nor_2_out, nor_3_out, nor_4_out,
       nor_5_out, nor_6_out, nor_7_out, nor_8_out, nor_9_out, nor_10_out, nor_11_out, nor_12_out, nor_13_out,
       nor_14_out, nor_15_out, nor_16_out, nor_17_out, nor_18_out, nor_19_out, nor_20_out, nor_21_out,
       nor_22_out, nor_23_out, nor_24_out, nor_25_out, nor_26_out, nor_27_out, nor_28_out, nor_29_out,
       nor_30_out, nor_31_out, nor_32_out, nor_33_out, nor_34_out, nor_35_out, nor_36_out, nor_37_out,
       nor_38_out, nor_40_out, nor_42_out, nor_44_out, nor_46_out, nor_48_out, not_1_out, not_2_out,
       not_3_out, or_1_out, or_2_out, or_3_out, or_4_out, or_5_out, or_6_out;

  not not_1 (not_1_out, in_8);
  not not_2 (not_2_out, in_7);
  nor nor_1 (nor_1_out, in_8, in_7);
  nor nor_2 (nor_2_out, in_8, not_2_out);
  nor nor_3 (nor_3_out, not_1_out, not_2_out);
  and and_1 (and_1_out, in_6, nor_1_out);
  and and_2 (and_2_out, in_4, nor_1_out);
  and and_3 (and_3_out, in_3, nor_1_out);
  and and_4 (and_4_out, in_2, nor_1_out);
  and and_5 (and_5_out, in_1, nor_1_out);
  or or_1 (or_1_out, nor_1_out, nor_2_out, nor_3_out);
  nor nor_4 (nor_4_out, in_6, out_9, or_1_out);
  nor nor_5 (nor_5_out, in_4, out_10, or_1_out);
  nor nor_6 (nor_6_out, in_3, out_11, or_1_out);
  nor nor_7 (nor_7_out, in_2, out_12, or_1_out);
  nor nor_8 (nor_8_out, in_1, out_13, or_1_out);
  or or_2 (or_2_out, and_1_out, nor_4_out);
  or or_3 (or_3_out, and_2_out, nor_5_out);
  or or_4 (or_4_out, and_3_out, nor_6_out);
  or or_5 (or_5_out, and_4_out, nor_7_out);
  or or_6 (or_6_out, and_5_out, nor_8_out);
  not not_3 (not_3_out, in_5);
  nor nor_9 (nor_9_out, or_2_out, not_3_out);
  nor nor_10 (nor_10_out, nor_9_out, not_3_out);
  nor nor_11 (nor_11_out, or_3_out, not_3_out);
  nor nor_12 (nor_12_out, nor_11_out, not_3_out);
  nor nor_13 (nor_13_out, or_4_out, not_3_out);
  nor nor_14 (nor_14_out, nor_13_out, not_3_out);
  nor nor_15 (nor_15_out, or_5_out, not_3_out);
  nor nor_16 (nor_16_out, nor_15_out, not_3_out);
  nor nor_17 (nor_17_out, or_6_out, not_3_out);
  nor nor_18 (nor_18_out, nor_17_out, not_3_out);
  nor nor_19 (nor_19_out, nor_9_out, nor_20_out);
  nor nor_20 (nor_20_out, nor_19_out, nor_10_out);
  nor nor_21 (nor_21_out, nor_11_out, nor_22_out);
  nor nor_22 (nor_22_out, nor_21_out, nor_12_out);
  nor nor_23 (nor_23_out, nor_13_out, nor_24_out);
  nor nor_24 (nor_24_out, nor_23_out, nor_14_out);
  nor nor_25 (nor_25_out, nor_15_out, nor_26_out);
  nor nor_26 (nor_26_out, nor_25_out, nor_16_out);
  nor nor_27 (nor_27_out, nor_17_out, nor_28_out);
  nor nor_28 (nor_28_out, nor_27_out, nor_18_out);
  nor nor_29 (nor_29_out, nor_19_out, in_5);
  nor nor_30 (nor_30_out, nor_29_out, in_5);
  nor nor_31 (nor_31_out, nor_21_out, in_5);
  nor nor_32 (nor_32_out, nor_31_out, in_5);
  nor nor_33 (nor_33_out, nor_23_out, in_5);
  nor nor_34 (nor_34_out, nor_33_out, in_5);
  nor nor_35 (nor_35_out, nor_25_out, in_5);
  nor nor_36 (nor_36_out, nor_35_out, in_5);
  nor nor_37 (nor_37_out, nor_27_out, in_5);
  nor nor_38 (nor_38_out, nor_37_out, in_5);
  nor nor_39 (out_9, nor_29_out, nor_40_out);
  nor nor_40 (nor_40_out, out_9, nor_30_out);
  nor nor_41 (out_10, nor_31_out, nor_42_out);
  nor nor_42 (nor_42_out, out_10, nor_32_out);
  nor nor_43 (out_11, nor_33_out, nor_44_out);
  nor nor_44 (nor_44_out, out_11, nor_34_out);
  nor nor_45 (out_12, nor_35_out, nor_46_out);
  nor nor_46 (nor_46_out, out_12, nor_36_out);
  nor nor_47 (out_13, nor_37_out, nor_48_out);
  nor nor_48 (nor_48_out, out_13, nor_38_out);

  // Notes on the sheet:
  //   NOR
  //   LD
  //   OEN
  //   STO
  //   48 NOR / 24 6J6 Dual Triodes
  //   Addressing / OpCode Inverters not counted
endmodule
