// Logisim project ExternalInput_v1.circ as structural Verilog: 1 circuit, main circuit main
module main (
  input  A4,
  input  A3,
  input  A2,
  input  A1,
  input  A0,
  input  E7,
  input  E6,
  input  E5,
  input  E4,
  input  E3,
  input  E2,
  input  E1,
  input  E0,
  output DATA
);

  wire nor_1_out, nor_2_out, nor_3_out, nor_4_out, nor_5_out, nor_6_out, nor_7_out, nor_8_out, not_1_out,
       not_2_out, not_3_out, not_4_out, not_5_out, not_6_out, not_7_out, not_8_out, not_9_out, not_10_out,
       not_11_out, not_12_out, not_13_out, or_1_out;

  not not_1 (not_1_out, A2);
  not not_2 (not_2_out, A3);
  not not_3 (not_3_out, A4);
  not not_4 (not_4_out, A0);
  not not_5 (not_5_out, A1);
  not not_6 (not_6_out, E7);
  not not_7 (not_7_out, E4);
  not not_8 (not_8_out, E5);
  not not_9 (not_9_out, E6);
  not not_10 (not_10_out, E2);
  not not_11 (not_11_out, E3);
  not not_12 (not_12_out, E1);
  not not_13 (not_13_out, E0);
  nor nor_1 (nor_1_out, not_13_out, A0, A1, A2, A3, not_3_out);
  nor nor_2 (nor_2_out, not_12_out, not_4_out, A1, A2, A3, not_3_out);
  nor nor_3 (nor_3_out, not_10_out, A0, not_5_out, A2, A3, not_3_out);
  nor nor_4 (nor_4_out, not_11_out, not_4_out, not_5_out, A2, A3, not_3_out);
  nor nor_5 (nor_5_out, not_7_out, A0, A1, not_1_out, A3, not_3_out);
  nor nor_6 (nor_6_out, not_8_out, not_4_out, A1, not_1_out, A3, not_3_out);
  nor nor_7 (nor_7_out, not_9_out, A0, not_5_out, not_1_out, A3, not_3_out);
  nor nor_8 (nor_8_out, not_6_out, not_4_out, not_5_out, not_1_out, A3, not_3_out);
  or or_1 (or_1_out, nor_1_out, nor_2_out, nor_3_out, nor_4_out, nor_5_out, nor_6_out, nor_7_out, nor_8_out);
  buf buffer_1 (DATA, or_1_out);
endmodule
