// Logisim project Input.circ as structural Verilog: 1 circuit, main circuit main
module main (
  input  X_SEL,
  input  nRR,
  input  Y0,
  input  Y1,
  input  Y2,
  input  Y3,
  input  Y4,
  input  Y5,
  input  Y6,
  input  Y7,
  input  in_11,
  input  in_12,
  input  in_13,
  input  in_14,
  input  in_15,
  input  in_16,
  input  in_17,
  input  in_18,
  input  in_19,
  input  in_20,
  input  in_21,
  input  in_22,
  input  in_23,
  input  in_24,
  output DATA_BUS,
  output DATA_BUS_2
);

  wire nor_1_out, nor_2_out, nor_3_out, nor_4_out, nor_5_out, nor_6_out, nor_7_out, nor_8_out, nor_9_out,
       nor_10_out, nor_11_out, nor_12_out, nor_13_out, nor_14_out, nor_15_out, not_1_out, not_2_out,
       not_3_out, not_4_out, not_5_out, not_6_out, not_7_out, not_8_out, not_9_out, or_1_out, or_2_out,
       or_3_out, or_4_out;

  not not_1 (not_1_out, Y0);
  not not_2 (not_2_out, Y1);
  not not_3 (not_3_out, Y2);
  not not_4 (not_4_out, Y3);
  not not_5 (not_5_out, Y4);
  not not_6 (not_6_out, Y5);
  not not_7 (not_7_out, Y6);
  not not_8 (not_8_out, Y7);
  not not_9 (not_9_out, X_SEL);
  nor nor_1 (nor_1_out, not_9_out, nRR, not_1_out);
  nor nor_2 (nor_2_out, in_11, in_18);
  nor nor_3 (nor_3_out, not_9_out, nor_2_out, not_2_out);
  nor nor_4 (nor_4_out, in_12, in_19);
  nor nor_5 (nor_5_out, not_9_out, nor_4_out, not_3_out);
  nor nor_6 (nor_6_out, in_13, in_20);
  or or_1 (or_1_out, nor_1_out, nor_3_out, nor_5_out);
  nor nor_7 (nor_7_out, not_9_out, nor_6_out, not_4_out);
  nor nor_8 (nor_8_out, in_14, in_21);
  nor nor_9 (nor_9_out, not_9_out, nor_8_out, not_5_out);
  nor nor_10 (nor_10_out, in_15, in_22);
  or or_2 (or_2_out, or_1_out, nor_7_out, nor_9_out);
  nor nor_11 (nor_11_out, not_9_out, nor_10_out, not_6_out);
  nor nor_12 (nor_12_out, in_16, in_23);
  nor nor_13 (nor_13_out, not_9_out, nor_12_out, not_7_out);
  nor nor_14 (nor_14_out, in_17, in_24);
  or or_3 (or_3_out, or_2_out, nor_11_out, nor_13_out);
  nor nor_15 (nor_15_out, not_9_out, nor_14_out, not_8_out);
  buf buffer_1 (DATA_BUS, or_4_out);
  or or_4 (or_4_out, or_3_out, nor_15_out);
  buf buffer_2 (DATA_BUS, or_4_out);

  assign DATA_BUS_2 = DATA_BUS;

  // Notes on the sheet:
  //   EXTERNAL SWITCHES
  //   EXTERNAL PIN HEADER
endmodule
