// Logisim project New_ALU_RR_FullGates.circ as structural Verilog: 1 circuit, main circuit main
module main (
  input  Data,
  input  _0100_ONE,
  input  _0011_SUB,
  input  _0010_ADD,
  input  _0001_LD,
  input  _0101_NAND,
  input  _0110_OR,
  input  _0111_XOR,
  output CAR,
  output RR
);

  wire Clock_out, nand_1_out, nand_2_out, nand_3_out, nand_4_out, nand_5_out, nand_6_out, nor_1_out,
       nor_2_out, nor_3_out, nor_4_out, nor_5_out, nor_6_out, nor_7_out, nor_8_out, nor_9_out, nor_10_out,
       nor_11_out, nor_12_out, nor_13_out, nor_14_out, nor_15_out, nor_16_out, nor_17_out, nor_18_out,
       nor_19_out, nor_20_out, nor_21_out, nor_22_out, nor_23_out, nor_24_out, nor_25_out, nor_26_out,
       nor_27_out, nor_29_out, nor_31_out, not_1_out, not_2_out, not_3_out, not_4_out, not_5_out, not_6_out,
       not_7_out, not_8_out, or_1_out, or_2_out, or_3_out, or_4_out, or_5_out, or_6_out, or_7_out, or_8_out,
       or_9_out, or_10_out;

  nor nor_1 (nor_1_out, Data, _0011_SUB);
  not not_1 (not_1_out, Data);
  nor nor_2 (nor_2_out, Data, nor_1_out);
  nor nor_3 (nor_3_out, nor_1_out, _0011_SUB);
  nand nand_1 (nand_1_out, Data, _0001_LD);
  nor nor_4 (nor_4_out, _0101_NAND, Data, RR);
  nor nor_5 (nor_5_out, _0101_NAND, Data, RR);
  nor nor_6 (nor_6_out, _0110_OR, not_1_out, nor_31_out);
  or or_1 (or_1_out, _0101_NAND, _0110_OR, _0111_XOR);
  or or_2 (or_2_out, nor_2_out, nor_3_out);
  not not_2 (not_2_out, nand_1_out);
  nor nor_7 (nor_7_out, nor_4_out, nor_5_out, nor_6_out);
  nor nor_8 (nor_8_out, RR, or_2_out);
  nor nor_9 (nor_9_out, not_4_out, nor_8_out);
  nand nand_2 (nand_2_out, nor_16_out, or_3_out);
  or or_3 (or_3_out, _0011_SUB, _0010_ADD);
  or or_4 (or_4_out, not_2_out, _0100_ONE);
  not not_3 (not_3_out, nand_3_out);
  nand nand_3 (nand_3_out, nor_7_out, or_1_out);
  or or_5 (or_5_out, _0101_NAND, _0110_OR, _0111_XOR);
  or or_6 (or_6_out, _0001_LD, _0011_SUB, _0010_ADD);
  nand nand_4 (nand_4_out, Clock_out, or_7_out);
  or or_7 (or_7_out, _0010_ADD, _0011_SUB, _0100_ONE);
  not not_4 (not_4_out, nand_5_out);
  nand nand_5 (nand_5_out, RR, or_2_out);
  nor nor_10 (nor_10_out, nor_9_out, CAR);
  nand nand_6 (nand_6_out, nor_9_out, CAR);
  not not_5 (not_5_out, nand_2_out);
  nor nor_11 (nor_11_out, or_8_out, nor_12_out);
  nor nor_12 (nor_12_out, or_8_out, RR);
  or or_8 (or_8_out, or_5_out, or_6_out);
  not not_6 (not_6_out, nand_4_out);
  or or_9 (or_9_out, not_4_out, not_7_out);
  not not_7 (not_7_out, nand_6_out);
  or or_10 (or_10_out, not_5_out, or_4_out, not_3_out, nor_11_out);
  not not_8 (not_8_out, Clock_out);
  nor nor_13 (nor_13_out, nor_21_out, nand_4_out);
  nor nor_14 (nor_14_out, nor_13_out, nand_4_out);
  nor nor_15 (nor_15_out, _0100_ONE, or_9_out);
  nor nor_16 (nor_16_out, not_7_out, nor_10_out);
  nor nor_17 (nor_17_out, or_10_out, not_8_out);
  nor nor_18 (nor_18_out, nor_17_out, not_8_out);
  nor nor_19 (nor_19_out, nor_13_out, nor_20_out);
  nor nor_20 (nor_20_out, nor_19_out, nor_14_out);
  nor nor_21 (nor_21_out, _0100_ONE, nor_15_out);
  nor nor_22 (nor_22_out, nor_17_out, nor_23_out);
  nor nor_23 (nor_23_out, nor_22_out, nor_18_out);
  nor nor_24 (nor_24_out, nor_19_out, not_6_out);
  nor nor_25 (nor_25_out, nor_24_out, not_6_out);
  nor nor_26 (nor_26_out, nor_22_out, Clock_out);
  nor nor_27 (nor_27_out, nor_26_out, Clock_out);
  Clock Clock (.out(Clock_out));
  nor nor_28 (CAR, nor_24_out, nor_29_out);
  nor nor_29 (nor_29_out, CAR, nor_25_out);
  nor nor_30 (RR, nor_26_out, nor_31_out);
  nor nor_31 (nor_31_out, RR, nor_27_out);
endmodule
