// Logisim project UE14500_Compact_v2.circ as structural Verilog: 1 circuit, main circuit main
module main (
  input  I3,
  input  I2,
  input  I1,
  input  I0,
  input  RST,
  input  Data,
  output out_7,
  output out_8,
  output out_9,
  output out_10,
  output out_11,
  output out_12,
  output Flag_F,
  output Flag_O
);

  wire adder_1_cout, adder_1_out, and_1_out, and_2_out, and_3_out, and_4_out, and_5_out, and_6_out,
       and_7_out, and_8_out, and_9_out, and_11_out, and_12_out, and_13_out, Carry_q, CLK_out,
       demultiplexer_1_out1, demultiplexer_1_out2, demultiplexer_1_out3, demultiplexer_1_out4,
       demultiplexer_1_out5, demultiplexer_1_out6, demultiplexer_1_out7, demultiplexer_1_out8,
       demultiplexer_1_out9, demultiplexer_1_out10, demultiplexer_1_out11, demultiplexer_1_out14,
       demultiplexer_1_out15, I3_qn, IEN_q, nand_1_out, nor_1_out, nor_2_out, nor_3_out, nor_4_out,
       nor_5_out, nor_6_out, nor_7_out, nor_8_out, not_1_out, not_2_out, not_3_out, not_4_out, not_5_out,
       OEN_q, or_1_out, or_2_out, or_3_out, or_4_out, or_5_out, or_6_out, or_7_out, or_8_out, or_9_out,
       or_10_out, or_11_out, or_12_out, or_13_out, or_14_out, or_15_out, or_16_out, or_18_out, RR_qn, SKZ_q,
       SKZ_qn, xor_1_out;
  wire [3:0] I0_q;

  D_Flip_Flop u_I0 (.clk(CLK_out), .D(or_1_out), .Q(I0_q[0]), .reset(RST));  // open: Qn, preset, en
  or or_1 (or_1_out, I0, SKZ_q);
  D_Flip_Flop u_I1 (.clk(CLK_out), .D(or_2_out), .Q(I0_q[1]), .reset(RST));  // open: Qn, preset, en
  or or_2 (or_2_out, I1, SKZ_q);
  D_Flip_Flop u_I2 (.clk(CLK_out), .D(or_3_out), .Q(I0_q[2]), .reset(RST));  // open: Qn, preset, en
  or or_3 (or_3_out, I2, SKZ_q);
  D_Flip_Flop u_I3 (.clk(CLK_out), .D(or_4_out), .Q(I0_q[3]), .Qn(I3_qn), .reset(RST));  // open: preset, en
  or or_4 (or_4_out, I3, SKZ_q);
  Clock CLK (.out(CLK_out));
  Demultiplexer #(.select(4), .enable("false")) demultiplexer_1 (
    .out0(Flag_O), .out1(demultiplexer_1_out1), .out2(demultiplexer_1_out2), .out3(demultiplexer_1_out3),
    .out4(demultiplexer_1_out4), .out5(demultiplexer_1_out5), .out6(demultiplexer_1_out6),
    .out7(demultiplexer_1_out7), .out8(demultiplexer_1_out8), .out9(demultiplexer_1_out9),
    .out10(demultiplexer_1_out10), .out11(demultiplexer_1_out11), .out12(out_11), .out13(out_12),
    .out14(demultiplexer_1_out14), .out15(demultiplexer_1_out15), .in(1'b1), .sel(I0_q));
  or or_5 (or_5_out, demultiplexer_1_out14, out_12);
  not not_1 (not_1_out, CLK_out);
  D_Flip_Flop SKZ (.clk(not_1_out), .D(and_1_out), .Q(SKZ_q), .Qn(SKZ_qn));  // open: preset, en, reset
  and and_1 (and_1_out, or_5_out, SKZ_qn, or_6_out);
  or or_6 (or_6_out, out_12, RR_qn);
  not not_2 (not_2_out, CLK_out);
  and and_2 (and_2_out, and_4_out, demultiplexer_1_out1);
  not not_3 (not_3_out, and_4_out);
  D_Flip_Flop IEN (.clk(and_3_out), .D(out_7), .Q(IEN_q), .reset(RST));  // open: Qn, preset, en
  and and_3 (and_3_out, not_2_out, demultiplexer_1_out10);
  xor xor_1 (xor_1_out, and_4_out, demultiplexer_1_out3);
  nor nor_1 (nor_1_out, demultiplexer_1_out5, and_4_out, out_10);
  nor nor_2 (nor_2_out, demultiplexer_1_out5, and_4_out, out_10);
  nor nor_3 (nor_3_out, demultiplexer_1_out6, not_3_out, RR_qn);
  or or_7 (or_7_out, demultiplexer_1_out5, demultiplexer_1_out6, demultiplexer_1_out7);
  and and_4 (and_4_out, out_7, IEN_q);
  or or_8 (or_8_out, demultiplexer_1_out2, demultiplexer_1_out4, demultiplexer_1_out3);
  Adder #(.width(1)) adder_1 (.a(out_10), .b(xor_1_out), .out(adder_1_out), .cin(Carry_q), .cout(adder_1_cout));
  or or_9 (or_9_out, demultiplexer_1_out3, demultiplexer_1_out2);
  or or_10 (or_10_out, and_2_out, demultiplexer_1_out4);
  nor nor_4 (nor_4_out, nor_1_out, nor_2_out, nor_3_out);
  and and_5 (and_5_out, and_9_out, or_8_out);
  nor nor_5 (nor_5_out, demultiplexer_1_out4, adder_1_cout);
  and and_6 (and_6_out, adder_1_out, or_9_out);
  nor nor_6 (nor_6_out, nor_8_out, or_14_out);
  and and_7 (and_7_out, nor_4_out, or_7_out);
  or or_11 (or_11_out, demultiplexer_1_out5, demultiplexer_1_out6, demultiplexer_1_out7);
  or or_12 (or_12_out, demultiplexer_1_out1, demultiplexer_1_out2, demultiplexer_1_out3);
  and and_8 (and_8_out, demultiplexer_1_out15, SKZ_q);
  and and_9 (and_9_out, I3_qn, CLK_out);
  D_Flip_Flop #(.trigger("falling")) Carry (
    .clk(and_5_out), .D(nor_7_out), .Q(Carry_q), .reset(RST));  // open: Qn, preset, en
  nor nor_7 (nor_7_out, demultiplexer_1_out4, nor_5_out);
  D_Flip_Flop #(.trigger("falling")) RR (
    .clk(and_9_out), .D(or_13_out), .Q(out_10), .Qn(RR_qn), .reset(RST));  // open: preset, en
  or or_13 (or_13_out, and_6_out, or_10_out, and_7_out, nor_6_out);
  nor nor_8 (nor_8_out, out_10, or_14_out);
  or or_14 (or_14_out, or_11_out, or_12_out);
  not not_4 (not_4_out, nand_1_out);
  or or_15 (or_15_out, not_4_out, and_8_out);
  not not_5 (not_5_out, CLK_out);
  nand nand_1 (nand_1_out, or_15_out, demultiplexer_1_out15);
  and and_10 (Flag_F, nand_1_out, demultiplexer_1_out15);
  and and_11 (and_11_out, not_5_out, demultiplexer_1_out11);
  or or_16 (or_16_out, demultiplexer_1_out8, demultiplexer_1_out9);
  and and_12 (and_12_out, demultiplexer_1_out8, out_10);
  and and_13 (and_13_out, demultiplexer_1_out9, RR_qn);
  D_Flip_Flop OEN (.clk(and_11_out), .D(out_7), .Q(OEN_q), .reset(RST));  // open: Qn, preset, en
  or or_17 (out_7, or_18_out, Data);
  or or_18 (or_18_out, and_12_out, and_13_out);
  and and_14 (out_9, CLK_out, OEN_q, or_16_out);

  assign out_8 = out_7;
endmodule
