// Logisim project UERAM_1Cell.circ as structural Verilog: 1 circuit, main circuit main
module main (
  input  DATA,
  input  WRT,
  input  X_SEL,
  input  Y_SEL,
  output DATA_2
);

  wire nor_1_out, nor_2_out, nor_3_out, nor_4_out, not_1_out, or_1_out;

  not not_1 (not_1_out, WRT);
  nor nor_1 (nor_1_out, DATA, or_1_out);
  nor nor_2 (nor_2_out, nor_1_out, or_1_out);
  or or_1 (or_1_out, not_1_out, X_SEL, Y_SEL);
  nor nor_3 (nor_3_out, nor_1_out, nor_4_out);
  nor nor_4 (nor_4_out, nor_3_out, nor_2_out);
  nor nor_5 (DATA_2, WRT, nor_4_out, X_SEL, Y_SEL);
endmodule
