// Logisim project UERAM_V2.circ as structural Verilog: 1 circuit, main circuit main
module main (
  input  Write,
  input  Data,
  input  in_3,
  input  in_4,
  input  in_5,
  input  in_6,
  input  in_7,
  input  in_8,
  input  RR,
  input  E0,
  input  E1,
  input  E2,
  input  E3,
  input  E4,
  input  E5,
  input  E6,
  input  E7,
  output out_18
);

  wire buffer_1_out, buffer_2_out, buffer_3_out, buffer_4_out, buffer_5_out, buffer_6_out, buffer_7_out,
       buffer_8_out, buffer_9_out, buffer_13_out, buffer_17_out, HIGH_out, nor_1_out, nor_2_out, nor_3_out,
       nor_4_out, nor_5_out, nor_6_out, nor_7_out, nor_8_out, nor_9_out, nor_10_out, nor_11_out, nor_12_out,
       nor_13_out, nor_14_out, nor_15_out, nor_16_out, nor_17_out, nor_18_out, nor_19_out, nor_20_out,
       nor_21_out, nor_22_out, nor_23_out, nor_24_out, nor_25_out, nor_26_out, nor_27_out, nor_28_out,
       nor_29_out, nor_30_out, nor_31_out, nor_32_out, nor_33_out, nor_34_out, nor_35_out, nor_36_out,
       nor_37_out, nor_38_out, nor_39_out, nor_40_out, nor_41_out, nor_42_out, nor_43_out, nor_44_out,
       nor_45_out, nor_46_out, nor_47_out, nor_48_out, nor_49_out, nor_50_out, nor_51_out, nor_52_out,
       nor_53_out, nor_54_out, nor_55_out, nor_56_out, nor_57_out, nor_58_out, nor_59_out, nor_60_out,
       nor_61_out, nor_62_out, nor_63_out, nor_64_out, nor_65_out, nor_66_out, nor_67_out, nor_68_out,
       nor_69_out, nor_70_out, nor_71_out, nor_72_out, nor_73_out, nor_74_out, nor_75_out, nor_76_out,
       nor_77_out, nor_78_out, nor_79_out, nor_80_out, nor_81_out, nor_82_out, nor_83_out, nor_84_out,
       nor_85_out, nor_86_out, nor_87_out, nor_88_out, nor_89_out, nor_90_out, nor_91_out, nor_92_out,
       nor_93_out, nor_94_out, nor_95_out, nor_96_out, nor_97_out, nor_98_out, nor_99_out, nor_100_out,
       nor_101_out, nor_102_out, nor_103_out, nor_104_out, nor_105_out, nor_106_out, nor_107_out,
       nor_108_out, nor_109_out, nor_110_out, nor_111_out, nor_112_out, nor_113_out, nor_114_out,
       nor_115_out, nor_116_out, nor_117_out, nor_118_out, nor_119_out, nor_120_out, nor_121_out,
       nor_122_out, nor_123_out, nor_124_out, nor_125_out, nor_126_out, nor_127_out, nor_128_out,
       nor_129_out, nor_130_out, nor_131_out, nor_132_out, nor_133_out, nor_134_out, nor_135_out,
       nor_136_out, nor_137_out, nor_138_out, nor_139_out, nor_140_out, nor_141_out, nor_142_out,
       nor_143_out, nor_144_out, nor_145_out, nor_146_out, nor_147_out, nor_148_out, nor_149_out,
       nor_150_out, nor_151_out, nor_152_out, nor_153_out, nor_154_out, nor_155_out, nor_156_out,
       nor_157_out, nor_158_out, nor_159_out, nor_160_out, nor_161_out, nor_162_out, nor_163_out,
       nor_164_out, nor_165_out, nor_166_out, nor_167_out, nor_168_out, nor_169_out, nor_170_out,
       nor_171_out, nor_172_out, nor_173_out, nor_174_out, nor_175_out, nor_176_out, nor_177_out,
       nor_178_out, nor_179_out, nor_180_out, nor_181_out, nor_182_out, nor_183_out, nor_184_out,
       nor_185_out, nor_186_out, nor_187_out, nor_188_out, nor_189_out, nor_190_out, nor_191_out,
       nor_192_out, nor_193_out, nor_194_out, nor_195_out, nor_196_out, nor_197_out, nor_198_out,
       nor_199_out, nor_200_out, nor_201_out, nor_202_out, nor_203_out, nor_204_out, nor_205_out,
       nor_206_out, nor_207_out, nor_208_out, nor_209_out, nor_210_out, nor_211_out, nor_212_out,
       nor_213_out, nor_214_out, nor_215_out, nor_216_out, nor_217_out, nor_218_out, nor_219_out,
       nor_220_out, nor_221_out, nor_222_out, nor_223_out, nor_224_out, nor_225_out, nor_226_out,
       nor_227_out, nor_228_out, nor_229_out, nor_230_out, nor_231_out, nor_232_out, nor_233_out,
       nor_234_out, nor_235_out, nor_236_out, nor_237_out, nor_238_out, nor_239_out, nor_240_out,
       nor_241_out, nor_242_out, nor_243_out, nor_244_out, nor_245_out, nor_246_out, nor_247_out,
       nor_248_out, nor_249_out, nor_250_out, nor_251_out, not_1_out, not_2_out, not_3_out, not_4_out,
       not_5_out, not_6_out, not_7_out, not_8_out, not_9_out, not_10_out, not_11_out, not_12_out, not_13_out,
       not_14_out, not_15_out, not_16_out, or_1_out, or_2_out, or_3_out, or_4_out, or_5_out, or_6_out,
       or_7_out, or_8_out, or_9_out, or_10_out, or_11_out, or_12_out, or_13_out, or_14_out, or_15_out,
       or_16_out, or_17_out, or_18_out, or_19_out, or_20_out, or_21_out, or_22_out, or_23_out, or_24_out,
       or_25_out, or_26_out, or_27_out, or_28_out, or_29_out, or_30_out, or_31_out, or_32_out, or_33_out,
       or_34_out, or_35_out, or_36_out, or_37_out, or_38_out, or_39_out, or_40_out, or_41_out, or_42_out,
       or_43_out, or_44_out, or_45_out, or_46_out, or_47_out, or_48_out, or_49_out, or_50_out, or_51_out,
       or_52_out, or_53_out, or_54_out, or_55_out, or_56_out, or_57_out, or_58_out, or_59_out, or_60_out,
       or_61_out, or_62_out, or_63_out, or_64_out, or_65_out, or_67_out, or_68_out, or_69_out, or_70_out,
       or_71_out, or_72_out, or_73_out, or_74_out, or_75_out, or_76_out, or_77_out, or_78_out, or_79_out,
       or_80_out, or_81_out, or_82_out, or_83_out, or_84_out, or_85_out, or_86_out;

  not not_1 (not_1_out, in_6);
  not not_2 (not_2_out, in_7);
  not not_3 (not_3_out, in_4);
  not not_4 (not_4_out, in_3);
  not not_5 (not_5_out, in_8);
  or or_1 (or_1_out, in_8, in_7, in_6);
  or or_2 (or_2_out, not_5_out, in_7, in_6);
  or or_3 (or_3_out, in_8, not_2_out, in_6);
  or or_4 (or_4_out, not_5_out, not_2_out, in_6);
  or or_5 (or_5_out, in_8, in_7, not_1_out);
  or or_6 (or_6_out, not_5_out, in_7, not_1_out);
  or or_7 (or_7_out, in_8, not_2_out, not_1_out);
  or or_8 (or_8_out, not_5_out, not_2_out, not_1_out);
  not not_6 (not_6_out, in_5);
  or or_9 (or_9_out, in_5, in_4, in_3);
  or or_10 (or_10_out, not_6_out, in_4, in_3);
  or or_11 (or_11_out, in_5, not_3_out, in_3);
  or or_12 (or_12_out, not_6_out, not_3_out, in_3);
  or or_13 (or_13_out, in_5, in_4, not_4_out);
  or or_14 (or_14_out, not_6_out, in_4, not_4_out);
  or or_15 (or_15_out, in_5, not_3_out, not_4_out);
  or or_16 (or_16_out, not_6_out, not_3_out, not_4_out);
  buf buffer_1 (buffer_1_out, or_9_out);
  buf buffer_2 (buffer_2_out, or_10_out);
  buf buffer_3 (buffer_3_out, or_11_out);
  buf buffer_4 (buffer_4_out, or_12_out);
  buf buffer_5 (buffer_5_out, or_13_out);
  buf buffer_6 (buffer_6_out, or_14_out);
  buf buffer_7 (buffer_7_out, or_15_out);
  buf buffer_8 (buffer_8_out, or_16_out);
  or or_17 (or_17_out, buffer_13_out, buffer_1_out, or_1_out);
  or or_18 (or_18_out, buffer_13_out, buffer_2_out, or_1_out);
  or or_19 (or_19_out, buffer_13_out, buffer_1_out, or_2_out);
  or or_20 (or_20_out, buffer_13_out, buffer_2_out, or_2_out);
  or or_21 (or_21_out, buffer_13_out, buffer_1_out, or_3_out);
  or or_22 (or_22_out, buffer_13_out, buffer_2_out, or_3_out);
  or or_23 (or_23_out, buffer_13_out, buffer_1_out, or_4_out);
  or or_24 (or_24_out, buffer_13_out, buffer_2_out, or_4_out);
  or or_25 (or_25_out, buffer_13_out, buffer_2_out, or_5_out);
  or or_26 (or_26_out, buffer_13_out, buffer_1_out, or_5_out);
  or or_27 (or_27_out, buffer_13_out, buffer_2_out, or_6_out);
  or or_28 (or_28_out, buffer_13_out, buffer_2_out, or_6_out);
  or or_29 (or_29_out, out_18, Data);
  nor nor_1 (nor_1_out, buffer_9_out, or_17_out);
  nor nor_2 (nor_2_out, nor_1_out, or_17_out);
  nor nor_3 (nor_3_out, buffer_9_out, or_18_out);
  nor nor_4 (nor_4_out, nor_3_out, or_18_out);
  nor nor_5 (nor_5_out, buffer_9_out, or_19_out);
  nor nor_6 (nor_6_out, nor_5_out, or_19_out);
  nor nor_7 (nor_7_out, buffer_9_out, or_20_out);
  nor nor_8 (nor_8_out, nor_7_out, or_20_out);
  nor nor_9 (nor_9_out, buffer_9_out, or_21_out);
  nor nor_10 (nor_10_out, nor_9_out, or_21_out);
  nor nor_11 (nor_11_out, buffer_9_out, or_22_out);
  nor nor_12 (nor_12_out, nor_11_out, or_22_out);
  nor nor_13 (nor_13_out, buffer_9_out, or_23_out);
  nor nor_14 (nor_14_out, nor_13_out, or_23_out);
  nor nor_15 (nor_15_out, buffer_9_out, or_24_out);
  nor nor_16 (nor_16_out, nor_15_out, or_24_out);
  nor nor_17 (nor_17_out, buffer_9_out, or_25_out);
  nor nor_18 (nor_18_out, nor_17_out, or_25_out);
  nor nor_19 (nor_19_out, buffer_9_out, or_26_out);
  nor nor_20 (nor_20_out, nor_19_out, or_26_out);
  nor nor_21 (nor_21_out, buffer_9_out, or_27_out);
  nor nor_22 (nor_22_out, nor_21_out, or_27_out);
  nor nor_23 (nor_23_out, buffer_9_out, or_28_out);
  nor nor_24 (nor_24_out, nor_23_out, or_28_out);
  buf buffer_9 (buffer_9_out, or_29_out);
  buf buffer_10 (buffer_9_out, or_29_out);
  buf buffer_11 (buffer_9_out, or_29_out);
  buf buffer_12 (buffer_9_out, or_29_out);
  nor nor_25 (nor_25_out, nor_1_out, nor_26_out);
  nor nor_26 (nor_26_out, nor_25_out, nor_2_out);
  nor nor_27 (nor_27_out, nor_3_out, nor_28_out);
  nor nor_28 (nor_28_out, nor_27_out, nor_4_out);
  nor nor_29 (nor_29_out, nor_5_out, nor_30_out);
  nor nor_30 (nor_30_out, nor_29_out, nor_6_out);
  nor nor_31 (nor_31_out, nor_7_out, nor_32_out);
  nor nor_32 (nor_32_out, nor_31_out, nor_8_out);
  nor nor_33 (nor_33_out, nor_9_out, nor_34_out);
  nor nor_34 (nor_34_out, nor_33_out, nor_10_out);
  nor nor_35 (nor_35_out, nor_11_out, nor_36_out);
  nor nor_36 (nor_36_out, nor_35_out, nor_12_out);
  nor nor_37 (nor_37_out, nor_13_out, nor_38_out);
  nor nor_38 (nor_38_out, nor_37_out, nor_14_out);
  nor nor_39 (nor_39_out, nor_15_out, nor_40_out);
  nor nor_40 (nor_40_out, nor_39_out, nor_16_out);
  nor nor_41 (nor_41_out, nor_17_out, nor_42_out);
  nor nor_42 (nor_42_out, nor_41_out, nor_18_out);
  nor nor_43 (nor_43_out, nor_19_out, nor_44_out);
  nor nor_44 (nor_44_out, nor_43_out, nor_20_out);
  nor nor_45 (nor_45_out, nor_21_out, nor_46_out);
  nor nor_46 (nor_46_out, nor_45_out, nor_22_out);
  nor nor_47 (nor_47_out, nor_23_out, nor_48_out);
  nor nor_48 (nor_48_out, nor_47_out, nor_24_out);
  nor nor_49 (nor_49_out, buffer_17_out, nor_26_out, buffer_1_out, or_1_out);
  nor nor_50 (nor_50_out, buffer_17_out, nor_28_out, buffer_2_out, or_1_out);
  nor nor_51 (nor_51_out, buffer_17_out, nor_30_out, buffer_1_out, or_2_out);
  nor nor_52 (nor_52_out, buffer_17_out, nor_32_out, buffer_2_out, or_2_out);
  nor nor_53 (nor_53_out, buffer_17_out, nor_34_out, buffer_1_out, or_3_out);
  nor nor_54 (nor_54_out, buffer_17_out, nor_36_out, buffer_2_out, or_3_out);
  nor nor_55 (nor_55_out, buffer_17_out, nor_38_out, buffer_1_out, or_4_out);
  nor nor_56 (nor_56_out, buffer_17_out, nor_40_out, buffer_2_out, or_4_out);
  nor nor_57 (nor_57_out, buffer_17_out, nor_42_out, buffer_2_out, or_5_out);
  nor nor_58 (nor_58_out, buffer_17_out, nor_44_out, buffer_1_out, or_5_out);
  nor nor_59 (nor_59_out, buffer_17_out, nor_46_out, buffer_2_out, or_6_out);
  nor nor_60 (nor_60_out, buffer_17_out, nor_48_out, buffer_2_out, or_6_out);
  not not_7 (not_7_out, Write);
  buf buffer_13 (buffer_13_out, not_7_out);
  buf buffer_14 (buffer_13_out, not_7_out);
  buf buffer_15 (buffer_13_out, not_7_out);
  buf buffer_16 (buffer_13_out, not_7_out);
  or or_30 (or_30_out, buffer_13_out, buffer_3_out, or_1_out);
  or or_31 (or_31_out, buffer_13_out, buffer_4_out, or_1_out);
  or or_32 (or_32_out, buffer_13_out, buffer_3_out, or_2_out);
  or or_33 (or_33_out, buffer_13_out, buffer_4_out, or_2_out);
  or or_34 (or_34_out, buffer_13_out, buffer_3_out, or_3_out);
  or or_35 (or_35_out, buffer_13_out, buffer_4_out, or_3_out);
  or or_36 (or_36_out, buffer_13_out, buffer_3_out, or_4_out);
  or or_37 (or_37_out, buffer_13_out, buffer_4_out, or_4_out);
  or or_38 (or_38_out, buffer_13_out, buffer_4_out, or_5_out);
  or or_39 (or_39_out, buffer_13_out, buffer_3_out, or_5_out);
  or or_40 (or_40_out, buffer_13_out, buffer_4_out, or_6_out);
  or or_41 (or_41_out, buffer_13_out, buffer_4_out, or_6_out);
  nor nor_61 (nor_61_out, buffer_9_out, or_30_out);
  nor nor_62 (nor_62_out, nor_61_out, or_30_out);
  nor nor_63 (nor_63_out, buffer_9_out, or_31_out);
  nor nor_64 (nor_64_out, nor_63_out, or_31_out);
  nor nor_65 (nor_65_out, buffer_9_out, or_32_out);
  nor nor_66 (nor_66_out, nor_65_out, or_32_out);
  nor nor_67 (nor_67_out, buffer_9_out, or_33_out);
  nor nor_68 (nor_68_out, nor_67_out, or_33_out);
  nor nor_69 (nor_69_out, buffer_9_out, or_34_out);
  nor nor_70 (nor_70_out, nor_69_out, or_34_out);
  nor nor_71 (nor_71_out, buffer_9_out, or_35_out);
  nor nor_72 (nor_72_out, nor_71_out, or_35_out);
  nor nor_73 (nor_73_out, buffer_9_out, or_36_out);
  nor nor_74 (nor_74_out, nor_73_out, or_36_out);
  nor nor_75 (nor_75_out, buffer_9_out, or_37_out);
  nor nor_76 (nor_76_out, nor_75_out, or_37_out);
  nor nor_77 (nor_77_out, buffer_9_out, or_38_out);
  nor nor_78 (nor_78_out, nor_77_out, or_38_out);
  nor nor_79 (nor_79_out, buffer_9_out, or_39_out);
  nor nor_80 (nor_80_out, nor_79_out, or_39_out);
  nor nor_81 (nor_81_out, buffer_9_out, or_40_out);
  nor nor_82 (nor_82_out, nor_81_out, or_40_out);
  nor nor_83 (nor_83_out, buffer_9_out, or_41_out);
  nor nor_84 (nor_84_out, nor_83_out, or_41_out);
  buf buffer_17 (buffer_17_out, Write);
  buf buffer_18 (buffer_17_out, Write);
  buf buffer_19 (buffer_17_out, Write);
  buf buffer_20 (buffer_17_out, Write);
  nor nor_85 (nor_85_out, nor_61_out, nor_86_out);
  nor nor_86 (nor_86_out, nor_85_out, nor_62_out);
  nor nor_87 (nor_87_out, nor_63_out, nor_88_out);
  nor nor_88 (nor_88_out, nor_87_out, nor_64_out);
  nor nor_89 (nor_89_out, nor_65_out, nor_90_out);
  nor nor_90 (nor_90_out, nor_89_out, nor_66_out);
  nor nor_91 (nor_91_out, nor_67_out, nor_92_out);
  nor nor_92 (nor_92_out, nor_91_out, nor_68_out);
  nor nor_93 (nor_93_out, nor_69_out, nor_94_out);
  nor nor_94 (nor_94_out, nor_93_out, nor_70_out);
  nor nor_95 (nor_95_out, nor_71_out, nor_96_out);
  nor nor_96 (nor_96_out, nor_95_out, nor_72_out);
  nor nor_97 (nor_97_out, nor_73_out, nor_98_out);
  nor nor_98 (nor_98_out, nor_97_out, nor_74_out);
  nor nor_99 (nor_99_out, nor_75_out, nor_100_out);
  nor nor_100 (nor_100_out, nor_99_out, nor_76_out);
  nor nor_101 (nor_101_out, nor_77_out, nor_102_out);
  nor nor_102 (nor_102_out, nor_101_out, nor_78_out);
  nor nor_103 (nor_103_out, nor_79_out, nor_104_out);
  nor nor_104 (nor_104_out, nor_103_out, nor_80_out);
  nor nor_105 (nor_105_out, nor_81_out, nor_106_out);
  nor nor_106 (nor_106_out, nor_105_out, nor_82_out);
  nor nor_107 (nor_107_out, nor_83_out, nor_108_out);
  nor nor_108 (nor_108_out, nor_107_out, nor_84_out);
  nor nor_109 (nor_109_out, buffer_17_out, nor_86_out, buffer_3_out, or_1_out);
  nor nor_110 (nor_110_out, buffer_17_out, nor_88_out, buffer_4_out, or_1_out);
  nor nor_111 (nor_111_out, buffer_17_out, nor_90_out, buffer_3_out, or_2_out);
  nor nor_112 (nor_112_out, buffer_17_out, nor_92_out, buffer_4_out, or_2_out);
  nor nor_113 (nor_113_out, buffer_17_out, nor_94_out, buffer_3_out, or_3_out);
  nor nor_114 (nor_114_out, buffer_17_out, nor_96_out, buffer_4_out, or_3_out);
  nor nor_115 (nor_115_out, buffer_17_out, nor_98_out, buffer_3_out, or_4_out);
  nor nor_116 (nor_116_out, buffer_17_out, nor_100_out, buffer_4_out, or_4_out);
  nor nor_117 (nor_117_out, buffer_17_out, nor_102_out, buffer_4_out, or_5_out);
  nor nor_118 (nor_118_out, buffer_17_out, nor_104_out, buffer_3_out, or_5_out);
  nor nor_119 (nor_119_out, buffer_17_out, nor_106_out, buffer_4_out, or_6_out);
  nor nor_120 (nor_120_out, buffer_17_out, nor_108_out, buffer_4_out, or_6_out);
  or or_42 (or_42_out, buffer_13_out, buffer_5_out, or_1_out);
  or or_43 (or_43_out, buffer_13_out, buffer_6_out, or_1_out);
  or or_44 (or_44_out, buffer_13_out, buffer_5_out, or_2_out);
  or or_45 (or_45_out, buffer_13_out, buffer_6_out, or_2_out);
  or or_46 (or_46_out, buffer_13_out, buffer_5_out, or_3_out);
  or or_47 (or_47_out, buffer_13_out, buffer_6_out, or_3_out);
  or or_48 (or_48_out, buffer_13_out, buffer_5_out, or_4_out);
  or or_49 (or_49_out, buffer_13_out, buffer_6_out, or_4_out);
  or or_50 (or_50_out, buffer_13_out, buffer_6_out, or_5_out);
  or or_51 (or_51_out, buffer_13_out, buffer_5_out, or_5_out);
  or or_52 (or_52_out, buffer_13_out, buffer_6_out, or_6_out);
  or or_53 (or_53_out, buffer_13_out, buffer_6_out, or_6_out);
  nor nor_121 (nor_121_out, buffer_9_out, or_42_out);
  nor nor_122 (nor_122_out, nor_121_out, or_42_out);
  nor nor_123 (nor_123_out, buffer_9_out, or_43_out);
  nor nor_124 (nor_124_out, nor_123_out, or_43_out);
  nor nor_125 (nor_125_out, buffer_9_out, or_44_out);
  nor nor_126 (nor_126_out, nor_125_out, or_44_out);
  nor nor_127 (nor_127_out, buffer_9_out, or_45_out);
  nor nor_128 (nor_128_out, nor_127_out, or_45_out);
  nor nor_129 (nor_129_out, buffer_9_out, or_46_out);
  nor nor_130 (nor_130_out, nor_129_out, or_46_out);
  nor nor_131 (nor_131_out, buffer_9_out, or_47_out);
  nor nor_132 (nor_132_out, nor_131_out, or_47_out);
  nor nor_133 (nor_133_out, buffer_9_out, or_48_out);
  nor nor_134 (nor_134_out, nor_133_out, or_48_out);
  nor nor_135 (nor_135_out, buffer_9_out, or_49_out);
  nor nor_136 (nor_136_out, nor_135_out, or_49_out);
  nor nor_137 (nor_137_out, buffer_9_out, or_50_out);
  nor nor_138 (nor_138_out, nor_137_out, or_50_out);
  nor nor_139 (nor_139_out, buffer_9_out, or_51_out);
  nor nor_140 (nor_140_out, nor_139_out, or_51_out);
  nor nor_141 (nor_141_out, buffer_9_out, or_52_out);
  nor nor_142 (nor_142_out, nor_141_out, or_52_out);
  nor nor_143 (nor_143_out, buffer_9_out, or_53_out);
  nor nor_144 (nor_144_out, nor_143_out, or_53_out);
  nor nor_145 (nor_145_out, nor_121_out, nor_146_out);
  nor nor_146 (nor_146_out, nor_145_out, nor_122_out);
  nor nor_147 (nor_147_out, nor_123_out, nor_148_out);
  nor nor_148 (nor_148_out, nor_147_out, nor_124_out);
  nor nor_149 (nor_149_out, nor_125_out, nor_150_out);
  nor nor_150 (nor_150_out, nor_149_out, nor_126_out);
  nor nor_151 (nor_151_out, nor_127_out, nor_152_out);
  nor nor_152 (nor_152_out, nor_151_out, nor_128_out);
  nor nor_153 (nor_153_out, nor_129_out, nor_154_out);
  nor nor_154 (nor_154_out, nor_153_out, nor_130_out);
  nor nor_155 (nor_155_out, nor_131_out, nor_156_out);
  nor nor_156 (nor_156_out, nor_155_out, nor_132_out);
  nor nor_157 (nor_157_out, nor_133_out, nor_158_out);
  nor nor_158 (nor_158_out, nor_157_out, nor_134_out);
  nor nor_159 (nor_159_out, nor_135_out, nor_160_out);
  nor nor_160 (nor_160_out, nor_159_out, nor_136_out);
  nor nor_161 (nor_161_out, nor_137_out, nor_162_out);
  nor nor_162 (nor_162_out, nor_161_out, nor_138_out);
  nor nor_163 (nor_163_out, nor_139_out, nor_164_out);
  nor nor_164 (nor_164_out, nor_163_out, nor_140_out);
  nor nor_165 (nor_165_out, nor_141_out, nor_166_out);
  nor nor_166 (nor_166_out, nor_165_out, nor_142_out);
  nor nor_167 (nor_167_out, nor_143_out, nor_168_out);
  nor nor_168 (nor_168_out, nor_167_out, nor_144_out);
  nor nor_169 (nor_169_out, buffer_17_out, nor_146_out, buffer_5_out, or_1_out);
  nor nor_170 (nor_170_out, buffer_17_out, nor_148_out, buffer_6_out, or_1_out);
  nor nor_171 (nor_171_out, buffer_17_out, nor_150_out, buffer_5_out, or_2_out);
  nor nor_172 (nor_172_out, buffer_17_out, nor_152_out, buffer_6_out, or_2_out);
  nor nor_173 (nor_173_out, buffer_17_out, nor_154_out, buffer_5_out, or_3_out);
  nor nor_174 (nor_174_out, buffer_17_out, nor_156_out, buffer_6_out, or_3_out);
  nor nor_175 (nor_175_out, buffer_17_out, nor_158_out, buffer_5_out, or_4_out);
  nor nor_176 (nor_176_out, buffer_17_out, nor_160_out, buffer_6_out, or_4_out);
  nor nor_177 (nor_177_out, buffer_17_out, nor_162_out, buffer_6_out, or_5_out);
  nor nor_178 (nor_178_out, buffer_17_out, nor_164_out, buffer_5_out, or_5_out);
  nor nor_179 (nor_179_out, buffer_17_out, nor_166_out, buffer_6_out, or_6_out);
  nor nor_180 (nor_180_out, buffer_17_out, nor_168_out, buffer_6_out, or_6_out);
  or or_54 (or_54_out, buffer_13_out, buffer_7_out, or_1_out);
  or or_55 (or_55_out, buffer_13_out, buffer_8_out, or_1_out);
  or or_56 (or_56_out, buffer_13_out, buffer_7_out, or_2_out);
  or or_57 (or_57_out, buffer_13_out, buffer_8_out, or_2_out);
  or or_58 (or_58_out, buffer_13_out, buffer_7_out, or_3_out);
  or or_59 (or_59_out, buffer_13_out, buffer_8_out, or_3_out);
  or or_60 (or_60_out, buffer_13_out, buffer_7_out, or_4_out);
  or or_61 (or_61_out, buffer_13_out, buffer_8_out, or_4_out);
  or or_62 (or_62_out, buffer_13_out, buffer_8_out, or_5_out);
  or or_63 (or_63_out, buffer_13_out, buffer_7_out, or_5_out);
  or or_64 (or_64_out, buffer_13_out, buffer_8_out, or_6_out);
  or or_65 (or_65_out, buffer_13_out, buffer_8_out, or_6_out);
  nor nor_181 (nor_181_out, buffer_9_out, or_54_out);
  nor nor_182 (nor_182_out, nor_181_out, or_54_out);
  nor nor_183 (nor_183_out, buffer_9_out, or_55_out);
  nor nor_184 (nor_184_out, nor_183_out, or_55_out);
  nor nor_185 (nor_185_out, buffer_9_out, or_56_out);
  nor nor_186 (nor_186_out, nor_185_out, or_56_out);
  nor nor_187 (nor_187_out, buffer_9_out, or_57_out);
  nor nor_188 (nor_188_out, nor_187_out, or_57_out);
  nor nor_189 (nor_189_out, buffer_9_out, or_58_out);
  nor nor_190 (nor_190_out, nor_189_out, or_58_out);
  nor nor_191 (nor_191_out, buffer_9_out, or_59_out);
  nor nor_192 (nor_192_out, nor_191_out, or_59_out);
  nor nor_193 (nor_193_out, buffer_9_out, or_60_out);
  nor nor_194 (nor_194_out, nor_193_out, or_60_out);
  nor nor_195 (nor_195_out, buffer_9_out, or_61_out);
  nor nor_196 (nor_196_out, nor_195_out, or_61_out);
  nor nor_197 (nor_197_out, buffer_9_out, or_62_out);
  nor nor_198 (nor_198_out, nor_197_out, or_62_out);
  nor nor_199 (nor_199_out, buffer_9_out, or_63_out);
  nor nor_200 (nor_200_out, nor_199_out, or_63_out);
  nor nor_201 (nor_201_out, buffer_9_out, or_64_out);
  nor nor_202 (nor_202_out, nor_201_out, or_64_out);
  nor nor_203 (nor_203_out, buffer_9_out, or_65_out);
  nor nor_204 (nor_204_out, nor_203_out, or_65_out);
  nor nor_205 (nor_205_out, nor_181_out, nor_206_out);
  nor nor_206 (nor_206_out, nor_205_out, nor_182_out);
  nor nor_207 (nor_207_out, nor_183_out, nor_208_out);
  nor nor_208 (nor_208_out, nor_207_out, nor_184_out);
  nor nor_209 (nor_209_out, nor_185_out, nor_210_out);
  nor nor_210 (nor_210_out, nor_209_out, nor_186_out);
  nor nor_211 (nor_211_out, nor_187_out, nor_212_out);
  nor nor_212 (nor_212_out, nor_211_out, nor_188_out);
  nor nor_213 (nor_213_out, nor_189_out, nor_214_out);
  nor nor_214 (nor_214_out, nor_213_out, nor_190_out);
  nor nor_215 (nor_215_out, nor_191_out, nor_216_out);
  nor nor_216 (nor_216_out, nor_215_out, nor_192_out);
  nor nor_217 (nor_217_out, nor_193_out, nor_218_out);
  nor nor_218 (nor_218_out, nor_217_out, nor_194_out);
  nor nor_219 (nor_219_out, nor_195_out, nor_220_out);
  nor nor_220 (nor_220_out, nor_219_out, nor_196_out);
  nor nor_221 (nor_221_out, nor_197_out, nor_222_out);
  nor nor_222 (nor_222_out, nor_221_out, nor_198_out);
  nor nor_223 (nor_223_out, nor_199_out, nor_224_out);
  nor nor_224 (nor_224_out, nor_223_out, nor_200_out);
  nor nor_225 (nor_225_out, nor_201_out, nor_226_out);
  nor nor_226 (nor_226_out, nor_225_out, nor_202_out);
  nor nor_227 (nor_227_out, nor_203_out, nor_228_out);
  nor nor_228 (nor_228_out, nor_227_out, nor_204_out);
  nor nor_229 (nor_229_out, buffer_17_out, nor_206_out, buffer_7_out, or_1_out);
  nor nor_230 (nor_230_out, buffer_17_out, nor_208_out, buffer_8_out, or_1_out);
  nor nor_231 (nor_231_out, buffer_17_out, nor_210_out, buffer_7_out, or_2_out);
  nor nor_232 (nor_232_out, buffer_17_out, nor_212_out, buffer_8_out, or_2_out);
  nor nor_233 (nor_233_out, buffer_17_out, nor_214_out, buffer_7_out, or_3_out);
  nor nor_234 (nor_234_out, buffer_17_out, nor_216_out, buffer_8_out, or_3_out);
  nor nor_235 (nor_235_out, buffer_17_out, nor_218_out, buffer_7_out, or_4_out);
  nor nor_236 (nor_236_out, buffer_17_out, nor_220_out, buffer_8_out, or_4_out);
  nor nor_237 (nor_237_out, buffer_17_out, nor_222_out, buffer_8_out, or_5_out);
  nor nor_238 (nor_238_out, buffer_17_out, nor_224_out, buffer_7_out, or_5_out);
  nor nor_239 (nor_239_out, buffer_17_out, nor_226_out, buffer_8_out, or_6_out);
  nor nor_240 (nor_240_out, buffer_17_out, nor_228_out, buffer_8_out, or_6_out);
  or or_66 (out_18, or_79_out, or_81_out, or_72_out, or_80_out);
  or or_67 (or_67_out, nor_229_out, nor_169_out, nor_109_out, nor_49_out);
  or or_68 (or_68_out, nor_230_out, nor_170_out, nor_110_out, nor_50_out);
  or or_69 (or_69_out, nor_231_out, nor_171_out, nor_111_out, nor_51_out);
  or or_70 (or_70_out, nor_232_out, nor_172_out, nor_112_out, nor_52_out);
  or or_71 (or_71_out, nor_233_out, nor_173_out, nor_113_out, nor_53_out);
  or or_72 (or_72_out, nor_234_out, nor_174_out, nor_114_out, nor_54_out);
  or or_73 (or_73_out, nor_235_out, nor_175_out, nor_115_out, nor_55_out);
  or or_74 (or_74_out, nor_236_out, nor_176_out, nor_116_out, nor_56_out);
  or or_75 (or_75_out, nor_237_out, nor_177_out, nor_117_out, nor_57_out);
  or or_76 (or_76_out, nor_238_out, nor_178_out, nor_118_out, nor_58_out);
  or or_77 (or_77_out, nor_239_out, nor_179_out, nor_119_out, nor_59_out);
  or or_78 (or_78_out, nor_240_out, nor_180_out, nor_120_out, nor_60_out);
  or or_79 (or_79_out, or_86_out, or_85_out, or_84_out, or_83_out, or_82_out);
  or or_80 (or_80_out, or_71_out, or_70_out, or_69_out, or_68_out, or_67_out);
  not not_8 (not_8_out, RR);
  not not_9 (not_9_out, E0);
  not not_10 (not_10_out, E1);
  not not_11 (not_11_out, E2);
  not not_12 (not_12_out, E3);
  not not_13 (not_13_out, E4);
  not not_14 (not_14_out, E5);
  not not_15 (not_15_out, E6);
  not not_16 (not_16_out, E7);
  nor HIGH (HIGH_out, buffer_3_out, or_8_out);
  or or_81 (or_81_out, HIGH_out, nor_241_out, or_73_out);
  nor nor_241 (nor_241_out, buffer_4_out, or_8_out);
  nor nor_242 (nor_242_out, RR, or_8_out, buffer_1_out);
  nor nor_243 (nor_243_out, not_8_out, or_8_out, buffer_2_out);
  or or_82 (or_82_out, nor_242_out, nor_243_out, or_74_out);
  nor nor_244 (nor_244_out, not_9_out, or_7_out, buffer_1_out);
  or or_83 (or_83_out, nor_244_out, nor_245_out, or_75_out);
  nor nor_245 (nor_245_out, not_10_out, or_7_out, buffer_2_out);
  nor nor_246 (nor_246_out, not_11_out, or_7_out, buffer_3_out);
  nor nor_247 (nor_247_out, not_12_out, or_7_out, buffer_4_out);
  or or_84 (or_84_out, nor_246_out, nor_247_out, or_76_out);
  nor nor_248 (nor_248_out, not_13_out, or_7_out, buffer_5_out);
  nor nor_249 (nor_249_out, not_14_out, or_7_out, buffer_6_out);
  or or_85 (or_85_out, nor_248_out, nor_249_out, or_77_out);
  nor nor_250 (nor_250_out, not_15_out, or_7_out, buffer_7_out);
  nor nor_251 (nor_251_out, not_16_out, or_7_out, buffer_8_out);
  or or_86 (or_86_out, nor_250_out, nor_251_out, or_78_out);
endmodule
