// Logisim project UE14500_CMOS_Modules.circ as structural Verilog: 12 circuits, main circuit System
module CPU (
  input  DATA_IN,
  input  RST_BAR,
  input  SYS_CLK,
  input  INSTR_CLK,
  input  I0,
  input  I1,
  input  I2,
  input  I3,
  output WRITE,
  output DATA_OUT,
  output RR,
  output IOC,
  output FLG_O,
  output FLG_F,
  output RTN
);

  wire alu_1_carry, alu_1_rr_bar, and_1_out, and_2_out, and_3_out, InputEnable_q, instrdecoder_1_alu_en,
       instrdecoder_1_arith_en, instrdecoder_1_bitop0, instrdecoder_1_bitop1, instrdecoder_1_clear_carry,
       instrdecoder_1_io_output, instrdecoder_1_io_reg_ctl, instrdecoder_1_ld, instrdecoder_1_logic_en,
       instrdecoder_1_nopf, instrdecoder_1_skz, instrdecoder_1_sto_comp, instrdecoder_1_store,
       instrdecoder_1_sub, instrreg_1_q0, instrreg_1_q0_bar, instrreg_1_q1, instrreg_1_q1_bar, instrreg_1_q2,
       instrreg_1_q2_bar, instrreg_1_q3, instrreg_1_q3_bar, nand_1_out, nand_2_out, nand_3_out, nor_1_out,
       nor_2_out, nor_3_out, not_1_out, OutputEnable_q, Skip_q;

  InstrReg instrreg_1 (
    .CLK(INSTR_CLK), .RST_BAR(RST_BAR), .SKIP_EN(Skip_q), .I0(I0), .I1(I1), .I2(I2), .I3(I3),
    .Q0(instrreg_1_q0), .Q0_BAR(instrreg_1_q0_bar), .Q1(instrreg_1_q1), .Q1_BAR(instrreg_1_q1_bar),
    .Q2(instrreg_1_q2), .Q2_BAR(instrreg_1_q2_bar), .Q3(instrreg_1_q3), .Q3_BAR(instrreg_1_q3_bar));
  and and_1 (and_1_out, SYS_CLK, instrdecoder_1_io_reg_ctl, not_1_out);
  not not_1 (not_1_out, instrdecoder_1_io_output);
  D_FLIP_FLOP InputEnable (.CLK(and_1_out), .RST_BAR(RST_BAR), .DATA(DATA_IN), .Q(InputEnable_q));  // open: Q_BAR
  and and_2 (and_2_out, InputEnable_q, DATA_IN);
  InstrDecoder instrdecoder_1 (
    .Q0(instrreg_1_q0), .Q0_BAR(instrreg_1_q0_bar), .Q1(instrreg_1_q1), .Q1_BAR(instrreg_1_q1_bar),
    .Q2(instrreg_1_q2), .Q2_BAR(instrreg_1_q2_bar), .Q3(instrreg_1_q3), .Q3_BAR(instrreg_1_q3_bar),
    .IO_REG_CTL(instrdecoder_1_io_reg_ctl), .IO_OUTPUT(instrdecoder_1_io_output),
    .ALU_EN(instrdecoder_1_alu_en), .CLEAR_CARRY(instrdecoder_1_clear_carry), .SUB(instrdecoder_1_sub),
    .ARITH_EN(instrdecoder_1_arith_en), .LD(instrdecoder_1_ld), .BITOP0(instrdecoder_1_bitop0),
    .BITOP1(instrdecoder_1_bitop1), .LOGIC_EN(instrdecoder_1_logic_en), .STORE(instrdecoder_1_store),
    .STO_COMP(instrdecoder_1_sto_comp), .IO_EN(IOC), .NOPO(FLG_O), .NOPF(instrdecoder_1_nopf), .RTN(RTN),
    .SKZ(instrdecoder_1_skz));
  and and_3 (and_3_out, SYS_CLK, instrdecoder_1_io_reg_ctl, instrdecoder_1_io_output);
  nor nor_1 (nor_1_out, alu_1_rr_bar, RTN);
  nor nor_2 (nor_2_out, RTN, instrdecoder_1_skz);
  nor nor_3 (nor_3_out, nor_1_out, nor_2_out, Skip_q);
  D_FLIP_FLOP OutputEnable (.CLK(and_3_out), .RST_BAR(RST_BAR), .DATA(DATA_IN), .Q(OutputEnable_q));  // open: Q_BAR
  // Probe on alu_1_carry
  ALU alu_1 (
    .CLK(SYS_CLK), .RST_BAR(RST_BAR), .DATA(and_2_out), .ALU_EN(instrdecoder_1_alu_en),
    .CLEAR_CARRY(instrdecoder_1_clear_carry), .SUB(instrdecoder_1_sub), .ARITH_EN(instrdecoder_1_arith_en),
    .LD(instrdecoder_1_ld), .BITOP0(instrdecoder_1_bitop0), .BITOP1(instrdecoder_1_bitop1),
    .LOGIC_EN(instrdecoder_1_logic_en), .CARRY(alu_1_carry), .RR(RR), .RR_BAR(alu_1_rr_bar));
  // Probe on alu_1_rr_bar
  nand nand_1 (nand_1_out, Skip_q, instrdecoder_1_nopf);
  nand nand_2 (nand_2_out, nand_3_out, nand_1_out);
  nand nand_3 (nand_3_out, nand_2_out, instrdecoder_1_nopf);
  D_FLIP_FLOP Skip (.CLK(SYS_CLK), .RST_BAR(RST_BAR), .DATA(nor_3_out), .Q(Skip_q));  // open: Q_BAR
  and and_4 (WRITE, OutputEnable_q, INSTR_CLK, instrdecoder_1_store);
  xor xor_1 (DATA_OUT, instrdecoder_1_sto_comp, RR);
  and and_5 (FLG_F, nand_3_out, instrdecoder_1_nopf);
endmodule

module InstrReg (
  input  CLK,
  input  RST_BAR,
  input  SKIP_EN,
  input  I0,
  input  I1,
  input  I2,
  input  I3,
  output Q0,
  output Q0_BAR,
  output Q1,
  output Q1_BAR,
  output Q2,
  output Q2_BAR,
  output Q3,
  output Q3_BAR
);

  wire or_1_out, or_2_out, or_3_out, or_4_out;

  or or_1 (or_1_out, SKIP_EN, I0);
  or or_2 (or_2_out, SKIP_EN, I1);
  or or_3 (or_3_out, SKIP_EN, I2);
  or or_4 (or_4_out, SKIP_EN, I3);
  D_FLIP_FLOP d_flip_flop_1 (.CLK(CLK), .RST_BAR(RST_BAR), .DATA(or_1_out), .Q(Q0), .Q_BAR(Q0_BAR));
  D_FLIP_FLOP d_flip_flop_2 (.CLK(CLK), .RST_BAR(RST_BAR), .DATA(or_2_out), .Q(Q1), .Q_BAR(Q1_BAR));
  D_FLIP_FLOP d_flip_flop_3 (.CLK(CLK), .RST_BAR(RST_BAR), .DATA(or_3_out), .Q(Q2), .Q_BAR(Q2_BAR));
  D_FLIP_FLOP d_flip_flop_4 (.CLK(CLK), .RST_BAR(RST_BAR), .DATA(or_4_out), .Q(Q3), .Q_BAR(Q3_BAR));
endmodule

module InstrDecoder (
  input  Q0,
  input  Q0_BAR,
  input  Q1,
  input  Q1_BAR,
  input  Q2,
  input  Q2_BAR,
  input  Q3,
  input  Q3_BAR,
  output IO_REG_CTL,
  output IO_OUTPUT,
  output ALU_EN,
  output CLEAR_CARRY,
  output SUB,
  output ARITH_EN,
  output LD,
  output BITOP0,
  output BITOP1,
  output LOGIC_EN,
  output STORE,
  output STO_COMP,
  output IO_EN,
  output NOPO,
  output NOPF,
  output RTN,
  output SKZ
);

  wire nor_2_out;

  nor nor_1 (IO_REG_CTL, Q3_BAR, Q2, Q1_BAR);
  nor nor_2 (nor_2_out, Q2, Q1, Q0);
  nor nor_3 (CLEAR_CARRY, Q2_BAR, Q1, Q0);
  nor nor_4 (ARITH_EN, Q1_BAR, Q2);
  nor nor_5 (LD, Q2, Q1, Q0_BAR);
  nor nor_6 (STORE, Q3_BAR, Q2, Q1);
  nor nor_7 (IO_EN, Q0, Q1, Q2_BAR, Q3_BAR);
  nor nor_8 (NOPO, Q0, Q1, Q2, Q3);
  nor nor_9 (NOPF, Q0_BAR, Q1_BAR, Q2_BAR, Q3_BAR);
  nor nor_10 (RTN, Q0_BAR, Q1, Q2_BAR, Q3_BAR);
  nor nor_11 (SKZ, Q0, Q1_BAR, Q2_BAR, Q3_BAR);
  nor nor_12 (ALU_EN, nor_2_out, Q3);

  assign BITOP0 = Q0;
  assign BITOP1 = Q1;
  assign IO_OUTPUT = Q0;
  assign LOGIC_EN = Q2;
  assign STO_COMP = Q0;
  assign SUB = Q0;
endmodule

module ALU (
  input  CLK,
  input  RST_BAR,
  input  DATA,
  input  ALU_EN,
  input  CLEAR_CARRY,
  input  SUB,
  input  ARITH_EN,
  input  LD,
  input  BITOP0,
  input  BITOP1,
  input  LOGIC_EN,
  output CARRY,
  output RR,
  output RR_BAR
);

  wire and_1_out, and_2_out, and_3_out, full_adder_1_carry, full_adder_1_sum, logic_unit4_1_sum_bar,
       nand_1_out, nand_2_out, nand_3_out, not_1_out, or_1_out, xor_1_out;

  or or_1 (or_1_out, CLEAR_CARRY, ARITH_EN);
  and and_1 (and_1_out, CLK, ALU_EN);
  xor xor_1 (xor_1_out, DATA, SUB);
  nand nand_1 (nand_1_out, DATA, LD);
  FULL_ADDER full_adder_1 (.A(RR), .B(CARRY), .C(xor_1_out), .SUM(full_adder_1_sum), .CARRY(full_adder_1_carry));
  LOGIC_UNIT4 logic_unit4_1 (
    .DATA(DATA), .RR(RR), .RR_BAR(RR_BAR), .BITOP0(BITOP0), .BITOP1(BITOP1), .LOGIC_EN(LOGIC_EN),
    .SUM_BAR(logic_unit4_1_sum_bar));
  nand nand_2 (nand_2_out, full_adder_1_sum, ARITH_EN);
  and and_2 (and_2_out, full_adder_1_carry, not_1_out);
  not not_1 (not_1_out, CLEAR_CARRY);
  nand nand_3 (nand_3_out, nand_2_out, nand_1_out, logic_unit4_1_sum_bar);
  and and_3 (and_3_out, or_1_out, and_1_out);
  MS_D_FLIP_FLOP CarryReg (.CLK(and_3_out), .RST_BAR(RST_BAR), .DATA(and_2_out), .Q(CARRY));  // open: Q_BAR
  MS_D_FLIP_FLOP ResultReg (.CLK(and_1_out), .RST_BAR(RST_BAR), .DATA(nand_3_out), .Q(RR), .Q_BAR(RR_BAR));

  // Notes on the sheet:
  //   A
  //   C
  //   B
  //   A
endmodule

module D_FLIP_FLOP (
  input  CLK,
  input  RST_BAR,
  input  DATA,
  output Q,
  output Q_BAR
);

  wire nand_1_out, nand_2_out, nand_3_out, nand_4_out;

  nand nand_1 (nand_1_out, nand_4_out, nand_2_out);
  nand nand_2 (nand_2_out, nand_1_out, CLK, RST_BAR);
  nand nand_3 (nand_3_out, nand_2_out, CLK, nand_4_out);
  nand nand_4 (nand_4_out, nand_3_out, DATA, RST_BAR);
  nand nand_5 (Q, nand_2_out, Q_BAR);
  nand nand_6 (Q_BAR, Q, nand_3_out, RST_BAR);
endmodule

module FULL_ADDER (
  input  A,
  input  B,
  input  C,
  output SUM,
  output CARRY
);

  wire nand_1_out, nand_2_out, nand_3_out, nand_4_out, nand_5_out, nand_6_out, nand_7_out;

  nand nand_1 (nand_1_out, A, B);
  nand nand_2 (nand_2_out, A, nand_1_out);
  nand nand_3 (nand_3_out, nand_1_out, B);
  nand nand_4 (nand_4_out, nand_2_out, nand_3_out);
  nand nand_5 (nand_5_out, nand_4_out, C);
  nand nand_6 (nand_6_out, nand_4_out, nand_5_out);
  nand nand_7 (nand_7_out, nand_5_out, C);
  nand nand_8 (SUM, nand_6_out, nand_7_out);
  nand nand_9 (CARRY, nand_5_out, nand_1_out);
endmodule

module LOGIC_UNIT (
  input  DATA,
  input  RR,
  input  BITNAND,
  input  BITOR,
  input  BITXOR,
  output SUM
);

  wire nor_1_out, nor_2_out, nor_3_out, nor_4_out, not_1_out, not_2_out, or_1_out;

  not not_1 (not_1_out, DATA);
  not not_2 (not_2_out, RR);
  nor nor_1 (nor_1_out, BITNAND, DATA, RR);
  nor nor_2 (nor_2_out, BITNAND, DATA, RR);
  nor nor_3 (nor_3_out, BITOR, not_1_out, not_2_out);
  or or_1 (or_1_out, BITNAND, BITOR, BITXOR);
  nor nor_4 (nor_4_out, nor_1_out, nor_2_out, nor_3_out);
  and and_1 (SUM, nor_4_out, or_1_out);
endmodule

module MS_D_FLIP_FLOP (
  input  CLK,
  input  RST_BAR,
  input  DATA,
  output Q,
  output Q_BAR
);

  wire nand_1_out, nand_2_out, nand_3_out, nand_4_out, nand_5_out, nand_6_out, not_1_out;

  nand nand_1 (nand_1_out, DATA, CLK);
  nand nand_2 (nand_2_out, nand_1_out, CLK);
  nand nand_3 (nand_3_out, nand_1_out, nand_4_out);
  nand nand_4 (nand_4_out, nand_3_out, nand_2_out, RST_BAR);
  not not_1 (not_1_out, CLK);
  nand nand_5 (nand_5_out, nand_3_out, not_1_out);
  nand nand_6 (nand_6_out, nand_5_out, not_1_out);
  nand nand_7 (Q, nand_5_out, Q_BAR);
  nand nand_8 (Q_BAR, Q, nand_6_out, RST_BAR);
endmodule

module LOGIC_UNIT2 (
  input  DATA,
  input  RR,
  input  BITNAND,
  input  BITOR,
  input  BITXOR,
  output SUM
);

  wire not_1_out, not_2_out, or_1_out, or_2_out, or_3_out;

  not not_1 (not_1_out, RR);
  not not_2 (not_2_out, DATA);
  or or_1 (or_1_out, DATA, RR, BITNAND);
  or or_2 (or_2_out, BITNAND, BITOR, BITXOR);
  or or_3 (or_3_out, not_2_out, not_1_out, BITOR);
  and and_1 (SUM, or_1_out, or_2_out, or_3_out);
endmodule

module LOGIC_UNIT3 (
  input  DATA,
  input  RR,
  input  RR_BAR,
  input  BITOP0_BAR,
  input  BITOP1_BAR,
  input  LOGIC_EN,
  output SUM_BAR
);

  wire not_1_out, or_1_out, or_2_out;

  not not_1 (not_1_out, DATA);
  or or_1 (or_1_out, BITOP0_BAR, not_1_out, RR_BAR);
  or or_2 (or_2_out, BITOP1_BAR, DATA, RR);
  nand nand_1 (SUM_BAR, or_1_out, or_2_out, LOGIC_EN);
endmodule

module LOGIC_UNIT4 (
  input  DATA,
  input  RR,
  input  RR_BAR,
  input  BITOP0,
  input  BITOP1,
  input  LOGIC_EN,
  output SUM_BAR
);

  wire nand_1_out, nand_2_out, not_1_out;

  not not_1 (not_1_out, DATA);
  nand nand_1 (nand_1_out, DATA, RR, BITOP0);
  nand nand_2 (nand_2_out, not_1_out, RR_BAR, BITOP1);
  nand nand_3 (SUM_BAR, nand_1_out, nand_2_out, LOGIC_EN);
endmodule

module System (
  input  RST
);

  wire and_1_out, and_2_out, and_3_out, and_4_out, and_5_out, cpu_1_data_out, cpu_1_rr, cpu_1_write,
       demultiplexer_1_out1, demultiplexer_1_out2, demultiplexer_1_out3, INSTR_CLK_out, not_1_out, or_1_out,
       or_2_out, ram_1_dout, SYS_CLK_out;
  wire [1:0] rom_1_data;
  wire [7:0] counter_1_q;
  wire [15:2] rom_1_data_2;

  Counter #(.trigger("falling")) counter_1 (
    .clr(RST), .load(1'b0), .up(1'b1), .count(1'b1), .clk(SYS_CLK_out), .Q(counter_1_q));  // open: D, carry
  Clock #(.highDuration(2), .lowDuration(2)) SYS_CLK (.out(SYS_CLK_out));
  ROM #(.dataWidth(16)) rom_1 (.addr(counter_1_q), .data({rom_1_data_2, rom_1_data}));
  Demultiplexer #(.select(2)) demultiplexer_1 (
    .out1(demultiplexer_1_out1), .out2(demultiplexer_1_out2), .out3(demultiplexer_1_out3), .in(1'b1),
    .sel(rom_1_data));  // open: out0
  and and_1 (and_1_out, ram_1_dout, ~rom_1_data_2[7]);  // AND_Gate
  or or_1 (or_1_out, and_1_out, and_2_out);
  and and_2 (and_2_out, rom_1_data_2[7], or_2_out);
  or or_2 (or_2_out, demultiplexer_1_out1, and_4_out, and_5_out);
  Clock #(.highDuration(2), .lowDuration(2), .phaseOffset(1)) INSTR_CLK (.out(INSTR_CLK_out));
  and and_3 (and_3_out, ~rom_1_data_2[7], cpu_1_write);  // AND_Gate
  and and_4 (and_4_out, demultiplexer_1_out2, cpu_1_rr);
  RAM #(.addrWidth(7), .dataWidth(1)) ram_1 (
    .addr({rom_1_data_2[6:2], rom_1_data}), .we(and_3_out), .oe(1'b1), .clk(SYS_CLK_out),
    .din(cpu_1_data_out), .dout(ram_1_dout));
  not not_1 (not_1_out, RST);
  and and_5 (and_5_out, demultiplexer_1_out3, ~cpu_1_rr);  // AND_Gate
  CPU cpu_1 (
    .DATA_IN(or_1_out), .RST_BAR(not_1_out), .SYS_CLK(SYS_CLK_out), .INSTR_CLK(INSTR_CLK_out),
    .I0(rom_1_data_2[8]), .I1(rom_1_data_2[9]), .I2(rom_1_data_2[10]), .I3(rom_1_data_2[11]),
    .WRITE(cpu_1_write), .DATA_OUT(cpu_1_data_out), .RR(cpu_1_rr));  // open: IOC, FLG_O, FLG_F, RTN

  // Notes on the sheet:
  //   contents of rom_1 (hex, n*v repeats v):
  //   a80 b80 400 181 180 280 900 181 281 801 580 b82 180 803
  //   0x80: 1
  //   0x81: 0
  //   0x82: RR
  //   0x83: !RR
  //   0x00 - 0x7F: RAM
endmodule
