// Logisim project MSDFF.circ as structural Verilog: 1 circuit, main circuit main
module main (
  input  CLK,
  input  DATA,
  input  DATA_2,
  input  CLK_2,
  output out_5,
  output out_6
);

  wire and_1_out, and_2_out, and_3_out, and_4_out, and_5_out, and_6_out, and_7_out, and_8_out, not_1_out,
       not_2_out, not_3_out, not_4_out, not_5_out, not_6_out, not_7_out, not_9_out, not_11_out, or_1_out,
       or_2_out, or_3_out, or_4_out, or_5_out, or_6_out, or_7_out, or_8_out;

  not not_1 (not_1_out, CLK);
  not not_2 (not_2_out, DATA);
  not not_3 (not_3_out, DATA_2);
  and and_1 (and_1_out, DATA, not_1_out);
  or or_1 (or_1_out, and_1_out, not_5_out);
  or or_2 (or_2_out, not_4_out, and_2_out);
  and and_2 (and_2_out, not_1_out, not_2_out);
  or or_3 (or_3_out, CLK_2, DATA_2);
  and and_3 (and_3_out, or_3_out, not_7_out);
  and and_4 (and_4_out, not_6_out, or_4_out);
  or or_4 (or_4_out, not_3_out, CLK_2);
  not not_4 (not_4_out, or_1_out);
  not not_5 (not_5_out, or_2_out);
  not not_6 (not_6_out, and_3_out);
  not not_7 (not_7_out, and_4_out);
  and and_5 (and_5_out, not_4_out, CLK);
  not not_8 (out_5, or_5_out);
  or or_5 (or_5_out, and_5_out, not_9_out);
  or or_6 (or_6_out, out_5, and_6_out);
  not not_9 (not_9_out, or_6_out);
  and and_6 (and_6_out, CLK, not_5_out);
  and and_7 (and_7_out, CLK_2, not_6_out);
  or or_7 (or_7_out, and_7_out, not_11_out);
  not not_10 (out_6, or_7_out);
  not not_11 (not_11_out, or_8_out);
  or or_8 (or_8_out, out_6, and_8_out);
  and and_8 (and_8_out, not_7_out, CLK_2);
endmodule
