// Logisim project UEX_Octal_Baudot.circ as structural Verilog: 1 circuit, main circuit main
module main (
  input  in_1,
  input  in_2,
  input  in_3,
  output out_4,
  output out_5,
  output out_6,
  output out_7,
  output out_8
);

  wire and_1_out, and_2_out, and_3_out, and_4_out, and_5_out, and_6_out, and_7_out, and_8_out, not_1_out,
       not_2_out, not_3_out;

  not not_1 (not_1_out, in_1);
  not not_2 (not_2_out, in_2);
  not not_3 (not_3_out, in_3);
  nor nor_1 (out_4, and_1_out, and_5_out, and_6_out);
  and and_1 (and_1_out, not_3_out, not_2_out, not_1_out);
  and and_2 (and_2_out, in_3, not_2_out, not_1_out);
  and and_3 (and_3_out, not_3_out, in_2, not_1_out);
  and and_4 (and_4_out, in_3, in_2, not_1_out);
  and and_5 (and_5_out, not_3_out, not_2_out, in_1);
  and and_6 (and_6_out, in_3, not_2_out, in_1);
  and and_7 (and_7_out, not_3_out, in_2, in_1);
  and and_8 (and_8_out, in_3, in_2, in_1);
  nor nor_2 (out_5, and_4_out, and_6_out, and_7_out);
  nor nor_3 (out_6, and_4_out, and_3_out, and_5_out, and_6_out);
  nor nor_4 (out_7, and_4_out, and_3_out, and_2_out, and_1_out, and_6_out, and_7_out, and_8_out);
  nor nor_5 (out_8, and_4_out, and_5_out, and_8_out);
endmodule
