// Logisim project Move.circ as structural Verilog: 1 circuit, main circuit main
module main (
  input  MM1,
  input  Step_2,
  input  Step_3,
  input  Step_4,
  input  MM2,
  input  OIR0,
  input  OIR1,
  input  OIR2,
  input  SRC0,
  input  SRC1,
  input  SRC2,
  input  DST0,
  input  DST1,
  input  DST2,
  input  DST3,
  input  DST4,
  output HCOT,
  output ACOT,
  output BFOT,
  output HCIN,
  output ACIN,
  output BFIN,
  output MAIN,
  output PCIN
);

  wire and_1_out, and_2_out, nand_1_out, nor_1_out, or_1_out;

  nor nor_1 (nor_1_out, MM1, MM2);
  and and_1 (and_1_out, OIR0, OIR1, OIR2);
  nand nand_1 (nand_1_out, and_1_out, nor_1_out, Step_3);
  or or_1 (or_1_out, Step_3, Step_2);
  and and_2 (and_2_out, or_1_out, nor_1_out, and_1_out);
  and and_3 (HCOT, and_2_out, SRC0);
  and and_4 (ACOT, and_2_out, SRC1);
  and and_5 (BFOT, and_2_out, SRC2);
  and and_6 (HCIN, nand_1_out, DST0);
  and and_7 (ACIN, nand_1_out, DST1);
  and and_8 (BFIN, nand_1_out, DST2);
  and and_9 (MAIN, nand_1_out, DST3);
  and and_10 (PCIN, nand_1_out, DST4);
endmodule
