// Logisim project MUX_CPU2TTY.circ as structural Verilog: 1 circuit, main circuit main
module main (
  input  in_1,
  input  _4_BIT_VALUE_IN,
  input  in_3,
  input  in_4,
  output out_5,
  output out_6,
  output out_7,
  output out_8,
  output out_9
);

  wire nor_1_out, nor_2_out, nor_3_out, nor_4_out, nor_5_out, nor_6_out, nor_7_out, nor_8_out, nor_9_out,
       nor_10_out, nor_11_out, nor_12_out, nor_13_out, nor_14_out, not_1_out, not_2_out, not_3_out, not_4_out;

  not not_1 (not_1_out, _4_BIT_VALUE_IN);
  not not_2 (not_2_out, in_1);
  not not_3 (not_3_out, in_3);
  not not_4 (not_4_out, in_4);
  nor nor_1 (nor_1_out, in_4, in_3, _4_BIT_VALUE_IN, in_1);
  nor nor_2 (nor_2_out, not_4_out, in_3, _4_BIT_VALUE_IN, in_1);
  nor nor_3 (nor_3_out, in_4, not_3_out, _4_BIT_VALUE_IN, in_1);
  nor nor_4 (nor_4_out, not_4_out, not_3_out, _4_BIT_VALUE_IN, in_1);
  nor nor_5 (nor_5_out, in_4, in_3, not_1_out, in_1);
  nor nor_6 (nor_6_out, not_4_out, in_3, not_1_out, in_1);
  nor nor_7 (nor_7_out, in_4, not_3_out, not_1_out, in_1);
  nor nor_8 (nor_8_out, not_4_out, not_3_out, not_1_out, in_1);
  nor nor_9 (nor_9_out, in_4, in_3, _4_BIT_VALUE_IN, not_2_out);
  nor nor_10 (nor_10_out, not_4_out, in_3, _4_BIT_VALUE_IN, not_2_out);
  nor nor_11 (nor_11_out, in_4, not_3_out, _4_BIT_VALUE_IN, not_2_out);
  nor nor_12 (nor_12_out, not_4_out, not_3_out, _4_BIT_VALUE_IN, not_2_out);
  nor nor_13 (nor_13_out, in_4, in_3, not_1_out, not_2_out);
  nor nor_14 (nor_14_out, not_4_out, in_3, not_1_out, not_2_out);
  or or_1 (out_5, nor_13_out, nor_9_out, nor_7_out, nor_6_out, nor_3_out, nor_2_out, nor_1_out);
  or or_2 (out_6, nor_13_out, nor_11_out, nor_9_out, nor_5_out);
  or or_3 (out_7, nor_14_out, nor_13_out, nor_10_out, nor_8_out, nor_7_out, nor_2_out, nor_1_out);
  or or_4 (out_8, nor_12_out, nor_9_out, nor_8_out, nor_5_out, nor_3_out, nor_2_out, nor_1_out);
  or or_5 (out_9, nor_14_out, nor_9_out, nor_8_out, nor_7_out, nor_4_out, nor_3_out, nor_2_out);

  // Notes on the sheet:
  //   7
  //   0
  //   1
  //   2
  //   3
  //   4
  //   5
  //   6
  //   FIGS
  //   SPACE
  //   CR
  //   LF
  //   PERIOD
  //   BELL
endmodule
