// Logisim project UE3_CPU_v2.circ as structural Verilog: 1 circuit, main circuit main
module main (
  input  A2,
  input  A1,
  input  A0,
  input  I1,
  input  I0,
  input  RST,
  input  DI0,
  input  DI1,
  input  DI2,
  input  EX2,
  input  EX1,
  input  EX0,
  input  ADD_ADC,
  output DO0,
  output DO1,
  output DO2,
  output OU0,
  output WRT,
  output OU1,
  output OU2,
  output out_21,
  output out_22,
  output out_23,
  output FLG1F,
  output out_25,
  output CARRY
);

  wire and_1_out, and_2_out, and_3_out, and_4_out, and_5_out, and_6_out, and_7_out, and_8_out, and_9_out,
       and_10_out, and_11_out, and_12_out, and_13_out, and_14_out, and_15_out, and_16_out, and_17_out,
       and_18_out, and_19_out, and_20_out, and_21_out, and_22_out, and_23_out, and_24_out, and_25_out,
       and_26_out, and_27_out, and_28_out, and_29_out, and_30_out, and_31_out, and_32_out, and_33_out,
       and_34_out, and_35_out, and_36_out, and_37_out, and_38_out, and_39_out, and_40_out, buffer_1_out,
       buffer_2_out, buffer_3_out, buffer_4_out, buffer_5_out, buffer_6_out, CLK_out, nand_1_out, nand_2_out,
       nand_3_out, nand_4_out, nand_5_out, nand_6_out, nand_7_out, nand_8_out, nand_9_out, nand_10_out,
       nand_11_out, nor_2_out, nor_4_out, nor_6_out, nor_8_out, nor_9_out, nor_10_out, nor_11_out,
       nor_12_out, nor_13_out, nor_14_out, nor_15_out, nor_16_out, nor_17_out, nor_18_out, nor_19_out,
       nor_20_out, nor_21_out, nor_22_out, nor_23_out, nor_24_out, nor_25_out, nor_26_out, nor_27_out,
       nor_28_out, nor_29_out, nor_30_out, nor_31_out, nor_32_out, nor_33_out, nor_34_out, nor_35_out,
       nor_36_out, nor_37_out, nor_39_out, nor_41_out, nor_43_out, nor_45_out, nor_46_out, nor_47_out,
       nor_48_out, not_1_out, not_2_out, not_3_out, not_4_out, not_5_out, not_6_out, not_7_out, not_8_out,
       not_9_out, not_10_out, not_11_out, not_12_out, not_13_out, not_14_out, not_15_out, not_16_out,
       not_17_out, not_18_out, not_19_out, not_20_out, not_21_out, not_22_out, not_23_out, not_24_out,
       not_25_out, not_26_out, not_27_out, or_1_out, or_2_out, or_3_out, or_4_out, or_5_out, or_6_out,
       or_7_out, or_8_out, or_9_out, or_10_out, or_11_out, or_12_out, or_13_out, or_14_out, or_15_out,
       or_16_out, or_17_out, or_18_out;

  or or_1 (or_1_out, RST, and_1_out);
  nor nor_1 (OU0, or_1_out, nor_2_out);
  nor nor_2 (nor_2_out, OU0, and_2_out);
  or or_2 (or_2_out, RST, and_3_out);
  nor nor_3 (OU1, or_2_out, nor_4_out);
  nor nor_4 (nor_4_out, OU1, and_4_out);
  or or_3 (or_3_out, RST, and_5_out);
  nor nor_5 (OU2, or_3_out, nor_6_out);
  nor nor_6 (nor_6_out, OU2, and_6_out);
  and and_1 (and_1_out, OU0, not_1_out, nor_8_out);
  and and_2 (and_2_out, nor_8_out, DO0, nor_2_out);
  and and_3 (and_3_out, OU1, not_2_out, nor_8_out);
  and and_4 (and_4_out, nor_8_out, DO1, nor_4_out);
  and and_5 (and_5_out, OU2, not_3_out, nor_8_out);
  and and_6 (and_6_out, nor_8_out, DO2, nor_6_out);
  not not_1 (not_1_out, DO0);
  not not_2 (not_2_out, DO1);
  not not_3 (not_3_out, DO2);
  nor nor_7 (FLG1F, not_7_out, not_11_out, not_10_out, not_12_out, not_13_out);
  not not_4 (not_4_out, EX2);
  nor nor_8 (nor_8_out, not_8_out, or_4_out, or_5_out);
  not not_5 (not_5_out, EX0);
  not not_6 (not_6_out, EX1);
  nor nor_9 (nor_9_out, not_4_out, or_6_out);
  nor nor_10 (nor_10_out, not_6_out, or_6_out);
  buf buffer_1 (buffer_1_out, nor_10_out);
  buf buffer_2 (buffer_2_out, nor_9_out);
  not not_7 (not_7_out, A2);
  not not_8 (not_8_out, WRT);
  or or_4 (or_4_out, not_13_out, not_12_out);
  or or_5 (or_5_out, A0, not_11_out, not_7_out);
  not not_9 (not_9_out, or_4_out);
  or or_6 (or_6_out, not_9_out, or_5_out);
  nor nor_11 (nor_11_out, not_5_out, or_6_out);
  buf buffer_3 (buffer_3_out, nor_11_out);
  not not_10 (not_10_out, A0);
  not not_11 (not_11_out, A1);
  not not_12 (not_12_out, I1);
  not not_13 (not_13_out, I0);
  and and_7 (and_7_out, not_13_out, I1, not_10_out, not_11_out, not_7_out);
  and and_8 (and_8_out, I0, I1);
  and and_9 (and_9_out, A0, A1, A2);
  and and_10 (and_10_out, not_13_out, not_12_out, not_10_out, A1, A2);
  nor nor_12 (nor_12_out, I0, I1);
  nand nand_1 (nand_1_out, I0, not_12_out);
  not not_14 (not_14_out, and_8_out);
  nor nor_13 (nor_13_out, and_8_out, and_9_out);
  nor nor_14 (nor_14_out, out_21, DO0);
  nor nor_15 (nor_15_out, out_22, DO1);
  nor nor_16 (nor_16_out, out_23, DO2);
  and and_11 (and_11_out, nor_12_out, not_15_out);
  not not_15 (not_15_out, nor_14_out);
  and and_12 (and_12_out, nor_12_out, not_16_out);
  not not_16 (not_16_out, nor_15_out);
  and and_13 (and_13_out, nor_12_out, not_17_out);
  not not_17 (not_17_out, nor_16_out);
  nand nand_2 (nand_2_out, nor_35_out, out_21, DO0);
  or or_7 (or_7_out, nor_35_out, out_21, DO0);
  and and_14 (and_14_out, DO0, out_21);
  nor nor_17 (nor_17_out, and_14_out, and_15_out, and_16_out);
  and and_15 (and_15_out, out_21, nor_35_out);
  and and_16 (and_16_out, DO0, nor_35_out);
  nand nand_3 (nand_3_out, not_18_out, out_22, DO1);
  or or_8 (or_8_out, not_18_out, out_22, DO1);
  and and_17 (and_17_out, DO1, out_22);
  nor nor_18 (nor_18_out, and_17_out, and_18_out, and_19_out);
  and and_18 (and_18_out, out_22, not_18_out);
  and and_19 (and_19_out, DO1, not_18_out);
  nand nand_4 (nand_4_out, not_19_out, out_23, DO2);
  or or_9 (or_9_out, not_19_out, out_23, DO2);
  and and_20 (and_20_out, DO2, out_23);
  nor nor_19 (nor_19_out, and_20_out, and_21_out, and_22_out);
  and and_21 (and_21_out, out_23, not_19_out);
  and and_22 (and_22_out, DO2, not_19_out);
  nand nand_5 (nand_5_out, or_7_out, nor_17_out);
  not not_18 (not_18_out, nor_17_out);
  nand nand_6 (nand_6_out, or_8_out, nor_18_out);
  not not_19 (not_19_out, nor_18_out);
  nand nand_7 (nand_7_out, or_9_out, nor_19_out);
  not not_20 (not_20_out, nor_19_out);
  nor nor_20 (nor_20_out, nand_1_out, nand_8_out);
  nand nand_8 (nand_8_out, nand_2_out, nand_5_out);
  nor nor_21 (nor_21_out, nand_1_out, nand_9_out);
  nand nand_9 (nand_9_out, nand_3_out, nand_6_out);
  nor nor_22 (nor_22_out, nand_1_out, nand_10_out);
  nand nand_10 (nand_10_out, nand_4_out, nand_7_out);
  nor nor_23 (nor_23_out, and_11_out, and_10_out, nor_20_out);
  nor nor_24 (nor_24_out, and_12_out, and_10_out, nor_21_out);
  nor nor_25 (nor_25_out, and_13_out, and_10_out, nor_22_out);
  Clock CLK (.out(CLK_out));
  not not_21 (not_21_out, CLK_out);
  nor nor_26 (nor_26_out, not_21_out, and_8_out);
  not not_22 (not_22_out, nor_23_out);
  not not_23 (not_23_out, nor_24_out);
  not not_24 (not_24_out, nor_25_out);
  not not_25 (not_25_out, not_20_out);
  and and_23 (and_23_out, nor_27_out, nor_23_out, nor_26_out);
  and and_24 (and_24_out, nor_26_out, not_22_out, nor_28_out);
  or or_10 (or_10_out, RST, and_24_out);
  and and_25 (and_25_out, nor_29_out, nor_24_out, nor_26_out);
  and and_26 (and_26_out, nor_26_out, not_23_out, nor_30_out);
  or or_11 (or_11_out, RST, and_26_out);
  and and_27 (and_27_out, nor_31_out, nor_25_out, nor_26_out);
  and and_28 (and_28_out, nor_26_out, not_24_out, nor_32_out);
  or or_12 (or_12_out, RST, and_28_out);
  and and_29 (and_29_out, nor_33_out, not_20_out, nor_26_out);
  and and_30 (and_30_out, nor_26_out, not_25_out, nor_34_out);
  or or_13 (or_13_out, RST, and_30_out);
  nand nand_11 (nand_11_out, and_7_out, CLK_out);
  not not_26 (not_26_out, nand_11_out);
  not not_27 (not_27_out, CARRY);
  nor nor_27 (nor_27_out, and_23_out, nor_28_out);
  nor nor_28 (nor_28_out, nor_27_out, or_10_out);
  nor nor_29 (nor_29_out, and_25_out, nor_30_out);
  nor nor_30 (nor_30_out, nor_29_out, or_11_out);
  nor nor_31 (nor_31_out, and_27_out, nor_32_out);
  nor nor_32 (nor_32_out, nor_31_out, or_12_out);
  nor nor_33 (nor_33_out, and_29_out, nor_34_out);
  nor nor_34 (nor_34_out, nor_33_out, or_13_out);
  nor nor_35 (nor_35_out, ADD_ADC, CARRY);
  or or_14 (or_14_out, RST, and_31_out);
  and and_31 (and_31_out, nor_36_out, not_27_out, not_26_out);
  and and_32 (and_32_out, not_26_out, CARRY, nor_37_out);
  or or_15 (or_15_out, RST, and_33_out);
  and and_33 (and_33_out, out_21, nor_27_out, not_21_out);
  and and_34 (and_34_out, not_21_out, nor_28_out, nor_39_out);
  or or_16 (or_16_out, RST, and_35_out);
  and and_35 (and_35_out, out_22, nor_29_out, not_21_out);
  and and_36 (and_36_out, not_21_out, nor_30_out, nor_41_out);
  or or_17 (or_17_out, RST, and_37_out);
  and and_37 (and_37_out, out_23, nor_31_out, not_21_out);
  and and_38 (and_38_out, not_21_out, nor_32_out, nor_43_out);
  or or_18 (or_18_out, RST, and_39_out);
  and and_39 (and_39_out, CARRY, nor_33_out, not_21_out);
  and and_40 (and_40_out, not_21_out, nor_34_out, nor_45_out);
  nor nor_36 (nor_36_out, or_14_out, nor_37_out);
  nor nor_37 (nor_37_out, nor_36_out, and_32_out);
  nor nor_38 (out_21, or_15_out, nor_39_out);
  nor nor_39 (nor_39_out, out_21, and_34_out);
  nor nor_40 (out_22, or_16_out, nor_41_out);
  nor nor_41 (nor_41_out, out_22, and_36_out);
  nor nor_42 (out_23, or_17_out, nor_43_out);
  nor nor_43 (nor_43_out, out_23, and_38_out);
  nor nor_44 (CARRY, or_18_out, nor_45_out);
  nor nor_45 (nor_45_out, CARRY, and_40_out);
  nor nor_46 (nor_46_out, nor_13_out, nor_39_out);
  nor nor_47 (nor_47_out, nor_13_out, nor_41_out);
  nor nor_48 (nor_48_out, nor_13_out, nor_43_out);
  or or_19 (DO0, buffer_3_out, DI0, buffer_4_out);
  or or_20 (DO1, buffer_1_out, DI1, buffer_5_out);
  or or_21 (DO2, buffer_2_out, DI2, buffer_6_out);
  nor nor_49 (WRT, not_21_out, not_14_out, nor_37_out);
  buf buffer_4 (buffer_4_out, nor_46_out);
  buf buffer_5 (buffer_5_out, nor_47_out);
  buf buffer_6 (buffer_6_out, nor_48_out);

  assign out_25 = CARRY;

  // Notes on the sheet:
  //   OUTPUT REGISTER
  //   50 NOR GATES
  //   27 NOT GATES
  //   11 NAND GATES
  //   88 INVERTERS NEEDED
  //   EXTERNAL INPUT
  //   OEN
  //   STO
  //   111
  //   CLR
  //   NOR
  //   ADD
  //   00: NOR, 01: ADC
  //   10: OEN, 11: STO
  //   ARITHMETIC UNIT
  //   RESULTS REGISTER
  //   OEN REGISTER
endmodule
