// Logisim project 5bit_CompleteSystem.circ as structural Verilog: 1 circuit, main circuit main
module main (
  input  in_1,
  output out_2,
  output out_3,
  output out_4,
  output out_5,
  output out_6,
  output WRT,
  output FLG
);

  wire and_1_out, clock_1_out, d_ff_1_q, d_ff_2_q, d_ff_3_q, d_ff_4_q, nor_2_out, nor_3_out, nor_4_out,
       nor_5_out, nor_6_out, nor_7_out, nor_8_out, not_1_out, not_2_out, not_3_out, not_4_out, not_5_out,
       not_6_out, not_7_out, OEN_q;
  wire [4:0] and_3_out, nor_9_out, or_2_out, OR_3_q, ram_1_data, RR_q;
  wire [4:4] nor_1_out, or_1_out;
  wire [7:0] counter_1_q;

  Clock clock_1 (.out(clock_1_out));
  D_Flip_Flop d_ff_1 (.clk(clock_1_out), .D(d_ff_4_q), .Q(d_ff_1_q), .preset(in_1));  // open: Qn, en, reset
  D_Flip_Flop d_ff_2 (.clk(clock_1_out), .D(d_ff_3_q), .Q(d_ff_2_q), .reset(in_1));  // open: Qn, preset, en
  D_Flip_Flop d_ff_3 (.clk(clock_1_out), .D(d_ff_1_q), .Q(d_ff_3_q), .reset(in_1));  // open: Qn, preset, en
  not not_1 (not_1_out, out_2);
  not not_2 (not_2_out, out_5);
  not not_3 (not_3_out, out_6);
  D_Flip_Flop d_ff_4 (.clk(clock_1_out), .D(d_ff_2_q), .Q(d_ff_4_q), .reset(in_1));  // open: Qn, preset, en
  not not_4 (not_4_out, out_4);
  not not_5 (not_5_out, out_3);
  nor nor_1 (nor_1_out[4], out_6, out_5);
  nor nor_2 (nor_2_out, out_6, not_2_out);
  or or_1 (or_1_out[4], nor_1_out[4], nor_2_out, nor_3_out);
  nor nor_3 (nor_3_out, not_3_out, not_2_out);
  nor nor_4 (nor_4_out, not_3_out, not_2_out);
  and and_1 (and_1_out, nor_4_out, nor_7_out);
  and and_2 (FLG, nor_4_out, nor_6_out);
  nor nor_5 (nor_5_out, not_2_out, out_6);
  nor nor_6 (nor_6_out, not_4_out, not_5_out, not_1_out);
  nor nor_7 (nor_7_out, out_4, not_5_out, not_1_out);
  nor nor_8 (nor_8_out, nor_6_out, nor_7_out);
  assign and_3_out = {5{nor_1_out[4]}} & ram_1_data;  // AND_Gate and_3, 5 bits wide
  Counter counter_1 (.Q(counter_1_q), .clk(d_ff_1_q), .clr(in_1));  // open: load, D, count, carry
  assign or_2_out = and_3_out | nor_9_out;  // OR_Gate or_2, 5 bits wide
  assign nor_9_out = ~(ram_1_data | {5{or_1_out[4]}} | RR_q);  // NOR_Gate nor_9, 5 bits wide
  _7_Segment_Display u_7_segment_display_1 (
    .f(not_6_out), .a(not_6_out), .b(1'b1), .e(not_6_out), .d(not_6_out), .c(1'b1));  // open: g, dp
  not not_6 (not_6_out, RR_q[4]);
  Register #(.width(5)) RR (.D(or_2_out), .Q(RR_q), .clk(d_ff_2_q));  // open: en, clr
  _7_Segment_Display u_7_segment_display_2 (
    .f(not_7_out), .a(not_7_out), .b(1'b1), .e(not_7_out), .d(not_7_out), .c(1'b1));  // open: g, dp
  not not_7 (not_7_out, OR_3_q[4]);
  Register #(.width(5)) OR_3 (.D(ram_1_data), .Q(OR_3_q), .clk(and_1_out));  // open: en, clr
  and and_4 (WRT, and_1_out, OEN_q);
  D_Flip_Flop OEN (.clk(nor_5_out), .D(ram_1_data[0]), .Q(OEN_q));  // open: Qn, preset, en, reset
  RAM #(.addrWidth(3), .dataWidth(5), .bus("separate")) ram_1 (
    .addr({out_2, out_3, out_4}), .din(ram_1_data), .data(ram_1_data), .str(d_ff_4_q), .sel(nor_8_out),
    .ld(d_ff_3_q));  // open: clk, clr
  ROM #(.dataWidth(5)) rom_1 (.addr(counter_1_q), .data({out_5, out_6, out_2, out_3, out_4}));  // open: sel
  Hex_Digit_Display hex_digit_display_1 (.value(RR_q[3:0]));  // open: dp
  Hex_Digit_Display hex_digit_display_2 (.value(OR_3_q[3:0]));  // open: dp

  // Notes on the sheet:
  //   00: LD
  //   10: OEN
  //   OPERATION
  //   01: NOR
  //   11: STO
endmodule
