// Logisim project CoreMemory_v4.circ as structural Verilog: 1 circuit, main circuit main
module main (
  input  A4,
  input  A3,
  input  A2,
  input  A1,
  input  A0,
  input  WRITEBACK,
  input  WRT,
  input  DATA,
  input  START,
  output nRD,
  output nWT
);

  wire and_1_out, and_2_out, and_3_out, clock_1_out, controlled_buffer_1_out, controlled_buffer_2_out,
       controlled_buffer_3_out, controlled_buffer_4_out, controlled_buffer_5_out, controlled_buffer_6_out,
       controlled_buffer_7_out, controlled_buffer_8_out, controlled_buffer_9_out, controlled_buffer_10_out,
       controlled_buffer_11_out, controlled_buffer_12_out, controlled_buffer_13_out,
       controlled_buffer_14_out, controlled_buffer_15_out, controlled_buffer_16_out, d_ff_1_q, d_ff_2_q,
       d_ff_2_qn, d_ff_3_q, d_ff_3_qn, nor_1_out, nor_2_out, nor_3_out, nor_4_out, nor_5_out, nor_6_out,
       nor_7_out, nor_8_out, nor_9_out, nor_10_out, nor_11_out, nor_12_out, nor_13_out, nor_14_out,
       nor_15_out, nor_16_out, not_1_out, not_2_out, not_3_out, not_4_out, not_5_out, or_1_out, or_2_out,
       or_3_out, or_4_out, or_5_out, or_6_out, or_7_out, or_8_out, or_9_out;

  not not_1 (not_1_out, A2);
  not not_2 (not_2_out, A3);
  Clock clock_1 (.out(clock_1_out));
  not not_3 (not_3_out, A0);
  not not_4 (not_4_out, A1);
  and and_1 (and_1_out, START, d_ff_3_qn, d_ff_2_qn, nRD);
  or or_1 (or_1_out, A2, A3);
  or or_2 (or_2_out, not_1_out, A3);
  or or_3 (or_3_out, A2, not_2_out);
  or or_4 (or_4_out, not_1_out, not_2_out);
  or or_5 (or_5_out, A0, A1);
  or or_6 (or_6_out, not_3_out, A1);
  or or_7 (or_7_out, A0, not_4_out);
  or or_8 (or_8_out, not_3_out, not_4_out);
  D_Flip_Flop d_ff_1 (.clk(clock_1_out), .D(and_1_out), .Q(d_ff_1_q), .Qn(nRD));  // open: preset, en, reset
  nor nor_1 (nor_1_out, nWT, A4, or_1_out);
  nor nor_2 (nor_2_out, or_1_out, A4, nRD);
  nor nor_3 (nor_3_out, nWT, A4, or_2_out);
  nor nor_4 (nor_4_out, or_2_out, A4, nRD);
  nor nor_5 (nor_5_out, nWT, A4, or_3_out);
  nor nor_6 (nor_6_out, or_3_out, A4, nRD);
  nor nor_7 (nor_7_out, nWT, A4, or_4_out);
  nor nor_8 (nor_8_out, or_4_out, A4, nRD);
  nor nor_9 (nor_9_out, nWT, A4, or_5_out);
  nor nor_10 (nor_10_out, or_5_out, A4, nRD);
  nor nor_11 (nor_11_out, nWT, A4, or_6_out);
  nor nor_12 (nor_12_out, or_6_out, A4, nRD);
  nor nor_13 (nor_13_out, nWT, A4, or_7_out);
  nor nor_14 (nor_14_out, or_7_out, A4, nRD);
  nor nor_15 (nor_15_out, nWT, A4, or_8_out);
  nor nor_16 (nor_16_out, or_8_out, A4, nRD);
  nand nand_1 (nWT, d_ff_3_q, or_9_out);
  D_Flip_Flop d_ff_2 (.clk(clock_1_out), .D(d_ff_1_q), .Q(d_ff_2_q), .Qn(d_ff_2_qn));  // open: preset, en, reset
  D_Flip_Flop d_ff_3 (.clk(clock_1_out), .D(d_ff_2_q), .Q(d_ff_3_q), .Qn(d_ff_3_qn));  // open: preset, en, reset
  assign controlled_buffer_1_out = nor_2_out ? 1'b1 : 1'bz;  // Controlled_Buffer controlled_buffer_1
  assign controlled_buffer_2_out = nor_4_out ? 1'b1 : 1'bz;  // Controlled_Buffer controlled_buffer_2
  assign controlled_buffer_3_out = nor_6_out ? 1'b1 : 1'bz;  // Controlled_Buffer controlled_buffer_3
  assign controlled_buffer_4_out = nor_8_out ? 1'b1 : 1'bz;  // Controlled_Buffer controlled_buffer_4
  or or_9 (or_9_out, and_2_out, and_3_out);
  assign controlled_buffer_5_out = nor_9_out ? 1'b1 : 1'bz;  // Controlled_Buffer controlled_buffer_5
  assign controlled_buffer_6_out = nor_10_out ? 1'b1 : 1'bz;  // Controlled_Buffer controlled_buffer_6
  and and_2 (and_2_out, WRITEBACK, not_5_out);
  not not_5 (not_5_out, WRT);
  and and_3 (and_3_out, WRT, DATA);
  assign controlled_buffer_7_out = nor_11_out ? 1'b1 : 1'bz;  // Controlled_Buffer controlled_buffer_7
  assign controlled_buffer_8_out = nor_12_out ? 1'b1 : 1'bz;  // Controlled_Buffer controlled_buffer_8
  assign controlled_buffer_9_out = nor_15_out ? 1'b1 : 1'bz;  // Controlled_Buffer controlled_buffer_9
  assign controlled_buffer_10_out = nor_13_out ? 1'b1 : 1'bz;  // Controlled_Buffer controlled_buffer_10
  assign controlled_buffer_11_out = nor_16_out ? 1'b1 : 1'bz;  // Controlled_Buffer controlled_buffer_11
  assign controlled_buffer_12_out = nor_14_out ? 1'b1 : 1'bz;  // Controlled_Buffer controlled_buffer_12
  assign controlled_buffer_13_out = nor_1_out ? 1'b1 : 1'bz;  // Controlled_Buffer controlled_buffer_13
  assign controlled_buffer_14_out = nor_3_out ? 1'b1 : 1'bz;  // Controlled_Buffer controlled_buffer_14
  assign controlled_buffer_15_out = nor_5_out ? 1'b1 : 1'bz;  // Controlled_Buffer controlled_buffer_15
  assign controlled_buffer_16_out = nor_7_out ? 1'b1 : 1'bz;  // Controlled_Buffer controlled_buffer_16
  // also tied to GND on the sheet: {controlled_buffer_1_out, controlled_buffer_2_out, controlled_buffer_3_out, controlled_buffer_4_out, controlled_buffer_5_out, controlled_buffer_6_out, controlled_buffer_7_out, controlled_buffer_8_out, controlled_buffer_10_out, controlled_buffer_12_out, controlled_buffer_9_out, controlled_buffer_11_out, controlled_buffer_13_out, controlled_buffer_14_out, controlled_buffer_15_out, controlled_buffer_16_out}
endmodule
