// Logisim project UE4_MEM.circ as structural Verilog: 1 circuit, main circuit main
module main (
  input  A2,
  input  A1,
  input  A0,
  input  nRD,
  input  nWT,
  input  S0,
  input  S1,
  input  S2,
  input  S3,
  output nRD_2,
  output nWT_2
);

  wire controlled_buffer_1_out, controlled_buffer_2_out, controlled_buffer_3_out, controlled_buffer_4_out,
       controlled_buffer_5_out, controlled_buffer_6_out, controlled_buffer_7_out, controlled_buffer_8_out,
       controlled_buffer_9_out, controlled_buffer_10_out, controlled_buffer_11_out, controlled_buffer_12_out,
       controlled_buffer_13_out, controlled_buffer_14_out, nand_1_out, nor_1_out, nor_2_out, nor_3_out,
       nor_4_out, nor_5_out, nor_6_out, nor_7_out, nor_8_out, nor_9_out, nor_10_out, nor_11_out, nor_12_out,
       not_1_out, not_2_out, not_3_out, or_1_out, or_2_out, or_3_out, or_4_out, or_5_out, or_6_out;

  not not_1 (not_1_out, A2);
  not not_2 (not_2_out, A1);
  not not_3 (not_3_out, A0);
  or or_1 (or_1_out, A0, A1, A2);
  or or_2 (or_2_out, not_3_out, A1, A2);
  or or_3 (or_3_out, A0, not_2_out, A2);
  or or_4 (or_4_out, not_3_out, not_2_out, A2);
  or or_5 (or_5_out, A0, A1, not_1_out);
  or or_6 (or_6_out, not_3_out, A1, not_1_out);
  nor nor_1 (nor_1_out, nWT, or_1_out);
  nor nor_2 (nor_2_out, or_1_out, nRD);
  nor nor_3 (nor_3_out, nWT, or_2_out);
  nor nor_4 (nor_4_out, or_2_out, nRD);
  nor nor_5 (nor_5_out, nWT, or_3_out);
  nor nor_6 (nor_6_out, or_3_out, nRD);
  nor nor_7 (nor_7_out, nWT, or_4_out);
  nor nor_8 (nor_8_out, or_4_out, nRD);
  nor nor_9 (nor_9_out, nWT, or_5_out);
  nor nor_10 (nor_10_out, or_5_out, nRD);
  nor nor_11 (nor_11_out, nWT, or_6_out);
  nor nor_12 (nor_12_out, or_6_out, nRD);
  nand nand_1 (nand_1_out, nWT, nRD);
  assign controlled_buffer_1_out = nor_2_out ? 1'b1 : 1'bz;  // Controlled_Buffer controlled_buffer_1
  assign controlled_buffer_2_out = nor_4_out ? 1'b1 : 1'bz;  // Controlled_Buffer controlled_buffer_2
  assign controlled_buffer_3_out = nor_6_out ? 1'b1 : 1'bz;  // Controlled_Buffer controlled_buffer_3
  assign controlled_buffer_4_out = nor_8_out ? 1'b1 : 1'bz;  // Controlled_Buffer controlled_buffer_4
  assign controlled_buffer_5_out = nor_10_out ? 1'b1 : 1'bz;  // Controlled_Buffer controlled_buffer_5
  assign controlled_buffer_6_out = nor_12_out ? 1'b1 : 1'bz;  // Controlled_Buffer controlled_buffer_6
  assign controlled_buffer_7_out = nand_1_out ? 1'b1 : 1'bz;  // Controlled_Buffer controlled_buffer_7
  assign controlled_buffer_8_out = nand_1_out ? 1'b1 : 1'bz;  // Controlled_Buffer controlled_buffer_8
  assign controlled_buffer_9_out = nor_1_out ? 1'b1 : 1'bz;  // Controlled_Buffer controlled_buffer_9
  assign controlled_buffer_10_out = nor_3_out ? 1'b1 : 1'bz;  // Controlled_Buffer controlled_buffer_10
  assign controlled_buffer_11_out = nor_5_out ? 1'b1 : 1'bz;  // Controlled_Buffer controlled_buffer_11
  assign controlled_buffer_12_out = nor_7_out ? 1'b1 : 1'bz;  // Controlled_Buffer controlled_buffer_12
  assign controlled_buffer_13_out = nor_9_out ? 1'b1 : 1'bz;  // Controlled_Buffer controlled_buffer_13
  assign controlled_buffer_14_out = nor_11_out ? 1'b1 : 1'bz;  // Controlled_Buffer controlled_buffer_14

  assign nRD_2 = nRD;
  assign nWT_2 = nWT;
  // also tied to GND on the sheet: {controlled_buffer_1_out, controlled_buffer_2_out, controlled_buffer_3_out, controlled_buffer_4_out, controlled_buffer_5_out, controlled_buffer_6_out, controlled_buffer_7_out, controlled_buffer_8_out, controlled_buffer_9_out, controlled_buffer_10_out, controlled_buffer_11_out, controlled_buffer_12_out, controlled_buffer_13_out, controlled_buffer_14_out}
endmodule
