// Logisim project UE4_Total.circ as structural Verilog: 1 circuit, main circuit main
module main (
  input  XXX_11,
  input  _110_11,
  input  XXX_10,
  input  RST,
  input  _110_00,
  input  EXT_INPUT,
  input  in_7,
  input  ADD_ADC,
  input  in_9,
  input  in_10,
  input  _110_01_10,
  output WRT,
  output CARRY
);

  wire adder_1_cout, clock_1_out, nor_2_out, OEN_q, or_1_out, or_2_out;
  wire [2:0] undriven;
  wire [3:0] adder_1_out, multiplexer_1_out, nor_1_out, OUTREG_q, ram_1_data, RR_q;
  wire [4:0] counter_1_q;

  Clock clock_1 (.out(clock_1_out));
  Counter #(.width(5), .max('h1f)) counter_1 (
    .Q(counter_1_q), .clk(clock_1_out), .clr(RST));  // open: load, D, count, carry
  RAM #(.addrWidth(3), .dataWidth(4)) ram_1 (.addr(undriven), .data(ram_1_data));  // open: sel, clk, ld, clr
  ROM #(.addrWidth(5), .dataWidth(5)) rom_1 (.addr(counter_1_q));  // open: data, sel
  Register #(.width(4)) OUTREG (.D(ram_1_data), .en(_110_11), .Q(OUTREG_q), .clk(WRT), .clr(RST));
  Hex_Digit_Display hex_digit_display_1 (.value(OUTREG_q));  // open: dp
  Decoder #(.select(2)) decoder_1 ();  // open: out0, out1, out2, out3, sel, en
  or or_1 (or_1_out, RST, _110_00);
  assign ram_1_data = _110_01_10 ? {in_10, in_9, in_7, EXT_INPUT} : 4'bz;  // Controlled_Buffer controlled_buffer_1
  assign nor_1_out = ~(ram_1_data | RR_q);  // NOR_Gate nor_1, 4 bits wide
  Adder #(.width(4)) adder_1 (.a(ram_1_data), .b(RR_q), .out(adder_1_out), .cin(nor_2_out), .cout(adder_1_cout));
  // OR_Gate or_2 has open pins: out=or_2_out
  nor nor_2 (nor_2_out, CARRY, ADD_ADC);
  D_Flip_Flop OEN (.clk(XXX_10), .D(ram_1_data[0]), .Q(OEN_q), .reset(RST));  // open: Qn, preset, en
  Multiplexer #(.width(4)) multiplexer_1 (
    .in0(nor_1_out), .in1(adder_1_out), .out(multiplexer_1_out));  // open: sel, en
  Register #(.width(4), .trigger("falling")) RR (
    .D(multiplexer_1_out), .Q(RR_q), .clk(or_2_out), .clr(or_1_out));  // open: en
  and and_1 (WRT, XXX_11, clock_1_out, OEN_q);
  D_Flip_Flop u_CARRY (.clk(or_2_out), .D(adder_1_cout), .Q(CARRY), .reset(or_1_out));  // open: Qn, preset, en

  // Notes on the sheet:
  //   contents of rom_1 (hex, n*v repeats v):
  //   0 18 1c 1e 18 19 3 18 1 0 1b
  //   00: NOR, 01: ADC
  //   10: OEN, 11: STO
endmodule
