// Logisim project BinaryCounter.circ as structural Verilog: 1 circuit, main circuit main
module main (
  input  Reset,
  output out_2,
  output out_3,
  output out_4,
  output out_5
);

  wire clock_1_out, nor_1_out, nor_2_out, nor_3_out, nor_4_out, nor_5_out, nor_6_out, nor_7_out, nor_8_out,
       nor_9_out, nor_10_out, nor_11_out, nor_12_out, nor_13_out, nor_14_out, nor_15_out, nor_16_out,
       nor_17_out, nor_18_out, nor_19_out, nor_20_out, nor_21_out, nor_22_out, nor_23_out, nor_24_out,
       nor_26_out, nor_28_out, nor_30_out, nor_32_out, not_1_out, or_1_out, or_2_out, or_3_out, or_4_out;

  Clock clock_1 (.out(clock_1_out));
  not not_1 (not_1_out, clock_1_out);
  or or_1 (or_1_out, nor_1_out, Reset);
  nor nor_1 (nor_1_out, nor_26_out, not_1_out);
  nor nor_2 (nor_2_out, nor_1_out, not_1_out);
  or or_2 (or_2_out, nor_3_out, Reset);
  nor nor_3 (nor_3_out, nor_28_out, nor_26_out);
  nor nor_4 (nor_4_out, nor_3_out, nor_26_out);
  or or_3 (or_3_out, nor_5_out, Reset);
  nor nor_5 (nor_5_out, nor_30_out, nor_28_out);
  nor nor_6 (nor_6_out, nor_5_out, nor_28_out);
  or or_4 (or_4_out, nor_7_out, Reset);
  nor nor_7 (nor_7_out, nor_32_out, nor_30_out);
  nor nor_8 (nor_8_out, nor_7_out, nor_30_out);
  nor nor_9 (nor_9_out, or_1_out, nor_10_out);
  nor nor_10 (nor_10_out, nor_9_out, nor_2_out);
  nor nor_11 (nor_11_out, or_2_out, nor_12_out);
  nor nor_12 (nor_12_out, nor_11_out, nor_4_out);
  nor nor_13 (nor_13_out, or_3_out, nor_14_out);
  nor nor_14 (nor_14_out, nor_13_out, nor_6_out);
  nor nor_15 (nor_15_out, or_4_out, nor_16_out);
  nor nor_16 (nor_16_out, nor_15_out, nor_8_out);
  nor nor_17 (nor_17_out, nor_9_out, clock_1_out);
  nor nor_18 (nor_18_out, nor_17_out, clock_1_out);
  nor nor_19 (nor_19_out, nor_11_out, out_2);
  nor nor_20 (nor_20_out, nor_19_out, out_2);
  nor nor_21 (nor_21_out, nor_13_out, out_3);
  nor nor_22 (nor_22_out, nor_21_out, out_3);
  nor nor_23 (nor_23_out, nor_15_out, out_4);
  nor nor_24 (nor_24_out, nor_23_out, out_4);
  nor nor_25 (out_2, nor_17_out, nor_26_out);
  nor nor_26 (nor_26_out, out_2, nor_18_out);
  nor nor_27 (out_3, nor_19_out, nor_28_out);
  nor nor_28 (nor_28_out, out_3, nor_20_out);
  nor nor_29 (out_4, nor_21_out, nor_30_out);
  nor nor_30 (nor_30_out, out_4, nor_22_out);
  nor nor_31 (out_5, nor_23_out, nor_32_out);
  nor nor_32 (nor_32_out, out_5, nor_24_out);
endmodule
